// Logisim project 8-Bit Computer.circ as structural Verilog: 12 circuits, main circuit Haupt
module _1bit_ALU (
  input  Cin,
  input  [2:0] Op,
  input  A,
  input  B,
  input  Less,
  output Out,
  output Cout,
  output Set
);

  wire and_1_out, decoder_1_out6, nor_1_out, or_1_out, undriven, xor_1_out, xor_2_out;

  and and_1 (and_1_out, A, B);
  or or_1 (or_1_out, A, B);
  xor xor_1 (xor_1_out, A, B);
  nor nor_1 (nor_1_out, A, B);
  Adder #(.width(1)) adder_1 (.a(A), .b(xor_2_out), .out(Set), .cin(Cin), .cout(Cout));
  xor xor_2 (xor_2_out, decoder_1_out6, B);
  Decoder #(.select(3)) decoder_1 (
    .out6(decoder_1_out6), .sel(Op));  // open: out0, out1, out2, out3, out4, out5, out7, en
  Multiplexer #(.select(3)) multiplexer_1 (
    .in0(and_1_out), .in1(or_1_out), .in2(xor_1_out), .in3(nor_1_out), .in4(Set), .in5(Less), .in6(Set),
    .in7(undriven), .out(Out), .sel(Op));  // open: en
endmodule

module _8_Bit_ALU (
  input  [2:0] OPs,
  input  [7:0] A,
  input  SUM_OUT,
  input  [7:0] B,
  output out_5,
  output out_6,
  output direct_out,
  output out_8,
  output out_9,
  output out_10,
  output out_11,
  output out_12,
  output [7:0] Out,
  output out_14,
  output Cout
);

  wire decoder_1_out6, n1bit_alu_1_cout, n1bit_alu_2_cout, n1bit_alu_3_cout, n1bit_alu_4_cout,
       n1bit_alu_5_cout, n1bit_alu_6_cout, n1bit_alu_7_cout, n1bit_alu_8_set;

  Decoder #(.select(3)) decoder_1 (
    .out6(decoder_1_out6), .sel(OPs));  // open: out0, out1, out2, out3, out4, out5, out7, en
  _1bit_ALU u_1bit_alu_1 (
    .A(A[0]), .B(B[0]), .Less(n1bit_alu_8_set), .Out(out_12), .Cin(decoder_1_out6), .Op(OPs),
    .Cout(n1bit_alu_1_cout));  // open: Set
  _1bit_ALU u_1bit_alu_2 (
    .A(A[1]), .B(B[1]), .Less(1'b0), .Out(out_11), .Cin(n1bit_alu_1_cout), .Op(OPs), .Cout(n1bit_alu_2_cout));  // open: Set
  _1bit_ALU u_1bit_alu_3 (
    .A(A[2]), .B(B[2]), .Less(1'b0), .Out(out_10), .Cin(n1bit_alu_2_cout), .Op(OPs), .Cout(n1bit_alu_3_cout));  // open: Set
  _1bit_ALU u_1bit_alu_4 (
    .A(A[3]), .B(B[3]), .Less(1'b0), .Out(out_9), .Cin(n1bit_alu_3_cout), .Op(OPs), .Cout(n1bit_alu_4_cout));  // open: Set
  _1bit_ALU u_1bit_alu_5 (
    .A(A[4]), .B(B[4]), .Less(1'b0), .Out(out_8), .Cin(n1bit_alu_4_cout), .Op(OPs), .Cout(n1bit_alu_5_cout));  // open: Set
  _1bit_ALU u_1bit_alu_6 (
    .A(A[5]), .B(B[5]), .Less(1'b0), .Out(direct_out), .Cin(n1bit_alu_5_cout), .Op(OPs),
    .Cout(n1bit_alu_6_cout));  // open: Set
  _1bit_ALU u_1bit_alu_7 (
    .A(A[6]), .B(B[6]), .Less(1'b0), .Out(out_6), .Cin(n1bit_alu_6_cout), .Op(OPs), .Cout(n1bit_alu_7_cout));  // open: Set
  _1bit_ALU u_1bit_alu_8 (
    .A(A[7]), .B(B[7]), .Less(1'b0), .Out(out_5), .Cin(n1bit_alu_7_cout), .Op(OPs), .Cout(Cout),
    .Set(n1bit_alu_8_set));
  nor nor_1 (out_14, out_12, out_11, out_10, out_9, out_8, direct_out, out_6, out_5);
  assign Out = SUM_OUT ? {out_5, out_6, direct_out, out_8, out_9, out_10, out_11, out_12} : 8'bz;  // Controlled_Buffer controlled_buffer_1
endmodule

module Haupt (
  input  [7:0] in_1,
  input  in_2,
  input  in_3,
  input  in_4,
  input  in_5,
  input  [15:0] in_6,
  input  in_7,
  input  in_8,
  input  in_9
);

  wire a_register_1_direct_out, a_register_1_out_7, a_register_1_out_8, a_register_1_out_10,
       a_register_1_out_12, a_register_1_out_13, a_register_1_out_14, a_register_1_out_15, AI, and_1_out,
       and_2_out, Ao, b_register_1_direct_out, b_register_1_out_7, b_register_1_out_8, b_register_1_out_10,
       b_register_1_out_12, b_register_1_out_13, b_register_1_out_14, b_register_1_out_15, BI, Bo,
       Carry_Out_Flag, CLK, clock_1_out, cu_control_logic_unit_1_out_36, cu_control_logic_unit_1_out_37,
       cu_control_logic_unit_1_out_38, cu_control_logic_unit_1_out_39, cu_control_logic_unit_1_out_41,
       cu_control_logic_unit_1_out_42, cu_control_logic_unit_1_out_43, cu_control_logic_unit_1_out_44, CURi,
       dw, dxI, dyI, FU, hlt, IBo, ICo, II, ir_instruction_register_1_direct_out,
       ir_instruction_register_1_out_8, ir_instruction_register_1_out_9, ir_instruction_register_1_out_10,
       ir_instruction_register_1_out_11, ir_instruction_register_1_out_12, ir_instruction_register_1_out_13,
       ir_instruction_register_1_out_14, ir_instruction_register_1_out_16, ir_instruction_register_1_out_17,
       ir_instruction_register_1_out_18, ir_instruction_register_1_out_19, ir_instruction_register_1_out_20,
       ir_instruction_register_1_out_21, ir_instruction_register_1_out_22, ir_instruction_register_1_out_23,
       mar_memory_address_register_1_direct_output, mar_memory_address_register_1_mode,
       mar_memory_address_register_1_out_11, mar_memory_address_register_1_out_14,
       mar_memory_address_register_1_out_15, mar_memory_address_register_1_out_16,
       mar_memory_address_register_1_out_18, mar_memory_address_register_1_out_19,
       mar_memory_address_register_1_out_20, mar_memory_address_register_1_out_21, MBo, MRo, Mw,
       n8_bit_alu_1_direct_out, n8_bit_alu_1_out_5, n8_bit_alu_1_out_6, n8_bit_alu_1_out_8,
       n8_bit_alu_1_out_9, n8_bit_alu_1_out_10, n8_bit_alu_1_out_11, n8_bit_alu_1_out_12, not_1_out,
       not_2_out, OP1, OP2, OP3, or_1_out, or_2_out, or_4_out, pc_program_counter_1_direct_out,
       pc_program_counter_1_out_8, pc_program_counter_1_out_9, pc_program_counter_1_out_10,
       pc_program_counter_1_out_12, pc_program_counter_1_out_13, pc_program_counter_1_out_14,
       pc_program_counter_1_out_15, PCe, PCl, PCo, ram_direct_out, ram_out_9, ram_out_10, ram_out_11,
       ram_out_12, ram_out_13, ram_out_14, ram_out_15, ram_out_16, ram_out_18, ram_out_19, ram_out_20,
       ram_out_21, ram_out_22, ram_out_23, ram_out_24, Ro, Rw, So, Sr, Xi, Xo, Zero_Flag;
  wire [2:0] flag_register_1_data_out;
  wire [2:2] undriven;
  wire [5:0] ir_instruction_register_1_out_7;
  wire [7:0] a_register_1_data_out_alu, b_register_1_out_6, mar_memory_address_register_1_ram_output;
  wire [7:6] pull_resistor_1_node;
  wire [15:0] ram_out_25;
  wire [15:15] pull_resistor_8_node;

  or or_1 (or_1_out, IBo, ICo);
  Pull_Resistor pull_resistor_1 (.node(pull_resistor_1_node[6]));
  Pull_Resistor pull_resistor_2 (.node(pull_resistor_1_node[7]));
  or or_2 (or_2_out, in_8, MRo);
  RAM ram (
    .WE(Rw), .clk(CLK), .OE(Ro), .Mode(in_2), .in_6(in_6),
    .in_7({{8{pull_resistor_8_node[15]}}, ram_out_25[7:0]}),
    .address(mar_memory_address_register_1_ram_output), .out_25(ram_out_25), .out_9(ram_out_9),
    .out_10(ram_out_10), .out_11(ram_out_11), .out_12(ram_out_12), .out_13(ram_out_13), .out_14(ram_out_14),
    .out_15(ram_out_15), .out_16(ram_out_16), .direct_out(ram_direct_out), .out_18(ram_out_18),
    .out_19(ram_out_19), .out_20(ram_out_20), .out_21(ram_out_21), .out_22(ram_out_22), .out_23(ram_out_23),
    .out_24(ram_out_24), .Manual_Write(in_7));
  IR__Instruction_Register ir_instruction_register_1 (
    .out_6(ram_out_25[7:0]), .out_7({pull_resistor_1_node, ir_instruction_register_1_out_7}),
    .in_1(ram_out_25), .clk(CLK), .II(II), .reset(in_3), .IO(or_1_out),
    .out_8(ir_instruction_register_1_out_8), .out_9(ir_instruction_register_1_out_9),
    .out_10(ir_instruction_register_1_out_10), .out_11(ir_instruction_register_1_out_11),
    .out_12(ir_instruction_register_1_out_12), .out_13(ir_instruction_register_1_out_13),
    .out_14(ir_instruction_register_1_out_14), .direct_out(ir_instruction_register_1_direct_out),
    .out_16(ir_instruction_register_1_out_16), .out_17(ir_instruction_register_1_out_17),
    .out_18(ir_instruction_register_1_out_18), .out_19(ir_instruction_register_1_out_19),
    .out_20(ir_instruction_register_1_out_20), .out_21(ir_instruction_register_1_out_21),
    .out_22(ir_instruction_register_1_out_22), .out_23(ir_instruction_register_1_out_23));
  CU__Control_Logic_Unit cu_control_logic_unit_1 (
    .step_reset(or_4_out), .OP_code(ir_instruction_register_1_out_7), .Flags(flag_register_1_data_out),
    .out_8(hlt), .out_9(Sr), .out_10(Ro), .out_11(Rw), .out_12(MBo), .out_13(MRo), .out_14(Mw), .out_15(IBo),
    .out_16(ICo), .out_17(II), .out_18(Ao), .out_19(AI), .out_20(Bo), .out_21(BI), .out_22(OP1),
    .out_23(OP2), .out_24(OP3), .out_25(So), .out_26(PCo), .out_27(PCe), .out_28(PCl), .out_29(FU),
    .out_30(Xi), .out_31(Xo), .out_32(dxI), .out_33(dyI), .out_34(dw), .out_35(CURi),
    .out_36(cu_control_logic_unit_1_out_36), .out_37(cu_control_logic_unit_1_out_37),
    .out_38(cu_control_logic_unit_1_out_38), .out_39(cu_control_logic_unit_1_out_39), .clk(CLK),
    .out_44(cu_control_logic_unit_1_out_44), .out_43(cu_control_logic_unit_1_out_43),
    .out_41(cu_control_logic_unit_1_out_41), .out_42(cu_control_logic_unit_1_out_42), .in_2(in_2),
    .RegID(ram_out_25[3:0]), .reset(in_3));  // open: out_40
  Clock clock_1 (.out(clock_1_out));
  not not_1 (not_1_out, in_4);
  and and_1 (and_1_out, not_1_out, not_2_out, clock_1_out);
  or or_3 (CLK, and_1_out, and_2_out);
  MAR__Memory_Address_Register mar_memory_address_register_1 (
    .RAM_Out(or_2_out), .Bus_Out(MBo), .Mode(mar_memory_address_register_1_mode),
    .out_11(mar_memory_address_register_1_out_11), .Mode_select(in_2), .Manual_Address(in_1),
    .Address(ram_out_25[7:0]), .clk(CLK), .MAR_In(Mw), .reset(in_3),
    .RAM_Output(mar_memory_address_register_1_ram_output), .Bus_Output(ram_out_25[7:0]),
    .out_14(mar_memory_address_register_1_out_14), .out_15(mar_memory_address_register_1_out_15),
    .out_16(mar_memory_address_register_1_out_16),
    .Direct_Output(mar_memory_address_register_1_direct_output),
    .out_18(mar_memory_address_register_1_out_18), .out_19(mar_memory_address_register_1_out_19),
    .out_20(mar_memory_address_register_1_out_20), .out_21(mar_memory_address_register_1_out_21), .in_4(in_9));
  LED led_1 (.in(ram_out_11));
  LED led_2 (.in(ram_out_10));
  LED led_3 (.in(ram_out_9));
  LED led_4 (.in(ram_out_12));
  LED led_5 (.in(ir_instruction_register_1_out_8));
  LED led_6 (.in(ir_instruction_register_1_out_11));
  LED led_7 (.in(ir_instruction_register_1_out_9));
  LED led_8 (.in(ir_instruction_register_1_out_10));
  LED led_9 (.in(cu_control_logic_unit_1_out_41));
  LED led_10 (.in(cu_control_logic_unit_1_out_42));
  LED led_11 (.in(cu_control_logic_unit_1_out_43));
  not not_2 (not_2_out, hlt);
  and and_2 (and_2_out, in_4, not_2_out, in_5);
  LED led_12 (.in(CLK));
  LED led_13 (.in(mar_memory_address_register_1_mode));
  LED led_14 (.in(mar_memory_address_register_1_out_11));
  LED led_15 (.in(mar_memory_address_register_1_out_15));
  LED led_16 (.in(mar_memory_address_register_1_out_14));
  LED led_17 (.in(mar_memory_address_register_1_out_16));
  LED led_18 (.in(ram_out_13));
  LED led_19 (.in(ram_out_16));
  LED led_20 (.in(ram_out_14));
  LED led_21 (.in(ram_out_15));
  LED led_22 (.in(ir_instruction_register_1_direct_out));
  LED led_23 (.in(ir_instruction_register_1_out_14));
  LED led_24 (.in(ir_instruction_register_1_out_13));
  LED led_25 (.in(ir_instruction_register_1_out_12));
  LED led_26 (.in(cu_control_logic_unit_1_out_44));
  LED led_27 (.in(mar_memory_address_register_1_out_19));
  LED led_28 (.in(mar_memory_address_register_1_direct_output));
  LED led_29 (.in(mar_memory_address_register_1_out_18));
  LED led_30 (.in(mar_memory_address_register_1_out_20));
  LED led_31 (.in(ram_out_20));
  LED led_32 (.in(ram_out_19));
  LED led_33 (.in(ram_direct_out));
  LED led_34 (.in(ram_out_18));
  LED led_35 (.in(ir_instruction_register_1_out_19));
  LED led_36 (.in(ir_instruction_register_1_out_18));
  LED led_37 (.in(ir_instruction_register_1_out_16));
  LED led_38 (.in(ir_instruction_register_1_out_17));
  LED led_39 (.in(mar_memory_address_register_1_out_21));
  LED led_40 (.in(ram_out_23));
  LED led_41 (.in(ram_out_24));
  LED led_42 (.in(ram_out_22));
  LED led_43 (.in(ram_out_21));
  LED led_44 (.in(ir_instruction_register_1_out_23));
  LED led_45 (.in(ir_instruction_register_1_out_21));
  LED led_46 (.in(ir_instruction_register_1_out_20));
  LED led_47 (.in(ir_instruction_register_1_out_22));
  or or_4 (or_4_out, in_3, Sr);
  Pull_Resistor pull_resistor_3 (.node(ram_out_25[4]));
  Pull_Resistor pull_resistor_4 (.node(ram_out_25[5]));
  Pull_Resistor pull_resistor_5 (.node(ram_out_25[6]));
  Pull_Resistor pull_resistor_6 (.node(ram_out_25[7]));
  Pull_Resistor pull_resistor_7 (.node(ram_out_25[7]));
  LED led_48 (.in(ram_out_25[7]));
  Pull_Resistor pull_resistor_8 (.node(pull_resistor_8_node[15]));
  Pull_Resistor pull_resistor_9 (.node(ram_out_25[8]));
  Pull_Resistor pull_resistor_10 (.node(ram_out_25[9]));
  Pull_Resistor pull_resistor_11 (.node(ram_out_25[10]));
  Pull_Resistor pull_resistor_12 (.node(ram_out_25[11]));
  Pull_Resistor pull_resistor_13 (.node(ram_out_25[12]));
  Pull_Resistor pull_resistor_14 (.node(ram_out_25[13]));
  Pull_Resistor pull_resistor_15 (.node(ram_out_25[14]));
  Pull_Resistor pull_resistor_16 (.node(ram_out_25[15]));
  LED led_49 (.in(undriven[2]));
  LED led_50 (.in(Carry_Out_Flag));
  LED led_51 (.in(Zero_Flag));
  LED led_52 (.in(flag_register_1_data_out[0]));
  LED led_53 (.in(flag_register_1_data_out[2]));
  LED led_54 (.in(flag_register_1_data_out[1]));
  Pull_Resistor pull_resistor_17 (.node(ram_out_25[3]));
  Pull_Resistor pull_resistor_18 (.node(ram_out_25[5]));
  Pull_Resistor pull_resistor_19 (.node(ram_out_25[6]));
  Pull_Resistor pull_resistor_20 (.node(ram_out_25[4]));
  LED led_55 (.in(ram_out_25[5]));
  LED led_56 (.in(ram_out_25[6]));
  LED led_57 (.in(ram_out_25[4]));
  LED led_58 (.in(ram_out_25[3]));
  Flag_Register flag_register_1 (
    .WE(FU), .clk(CLK), .reset(in_3), .Data_out(flag_register_1_data_out),
    .Data_in({undriven[2], Carry_Out_Flag, Zero_Flag}));
  Pull_Resistor pull_resistor_21 (.node(ram_out_25[2]));
  Pull_Resistor pull_resistor_22 (.node(ram_out_25[1]));
  Pull_Resistor pull_resistor_23 (.node(ram_out_25[0]));
  LED led_59 (.in(ram_out_25[0]));
  LED led_60 (.in(ram_out_25[2]));
  LED led_61 (.in(ram_out_25[1]));
  _8_Bit_ALU u_8_bit_alu_1 (
    .OPs({OP1, OP2, OP3}), .A(a_register_1_data_out_alu), .B(b_register_1_out_6), .Out(ram_out_25[7:0]),
    .out_14(Zero_Flag), .Cout(Carry_Out_Flag), .SUM_OUT(So), .out_5(n8_bit_alu_1_out_5),
    .out_6(n8_bit_alu_1_out_6), .direct_out(n8_bit_alu_1_direct_out), .out_8(n8_bit_alu_1_out_8),
    .out_9(n8_bit_alu_1_out_9), .out_10(n8_bit_alu_1_out_10), .out_11(n8_bit_alu_1_out_11),
    .out_12(n8_bit_alu_1_out_12));
  PC__Program_Counter pc_program_counter_1 (
    .LOAD(PCl), .in_4(ram_out_25[7:0]), .Reset(in_3), .CE(PCe), .out_8(pc_program_counter_1_out_8),
    .out_9(pc_program_counter_1_out_9), .out_10(pc_program_counter_1_out_10),
    .direct_out(pc_program_counter_1_direct_out), .out_12(pc_program_counter_1_out_12),
    .out_13(pc_program_counter_1_out_13), .out_14(pc_program_counter_1_out_14),
    .out_15(pc_program_counter_1_out_15), .CO(PCo), .clk(CLK), .out_7(ram_out_25[7:0]));  // open: Carry_Out
  LED led_62 (.in(pc_program_counter_1_out_8));
  LED led_63 (.in(pc_program_counter_1_out_9));
  A_Register a_register_1 (
    .Data_Out_ALU(a_register_1_data_out_alu), .Data_Out(ram_out_25[7:0]), .Data_In(ram_out_25[7:0]), .WE(AI),
    .Clk(CLK), .Reset(in_3), .OE(Ao), .out_7(a_register_1_out_7), .out_8(a_register_1_out_8),
    .out_10(a_register_1_out_10), .direct_out(a_register_1_direct_out), .out_12(a_register_1_out_12),
    .out_13(a_register_1_out_13), .out_14(a_register_1_out_14), .out_15(a_register_1_out_15));
  LED led_64 (.in(a_register_1_out_8));
  LED led_65 (.in(a_register_1_out_10));
  LED led_66 (.in(a_register_1_out_7));
  LED led_67 (.in(n8_bit_alu_1_direct_out));
  LED led_68 (.in(n8_bit_alu_1_out_6));
  LED led_69 (.in(n8_bit_alu_1_out_5));
  LED led_70 (.in(n8_bit_alu_1_out_8));
  B_Register b_register_1 (
    .out_6(b_register_1_out_6), .out_7(b_register_1_out_7), .out_8(b_register_1_out_8),
    .Data_Out(ram_out_25[7:0]), .out_10(b_register_1_out_10), .direct_out(b_register_1_direct_out),
    .out_12(b_register_1_out_12), .out_13(b_register_1_out_13), .out_14(b_register_1_out_14),
    .out_15(b_register_1_out_15), .Data_In(ram_out_25[7:0]), .WE(BI), .Clk(CLK), .Reset(in_3),
    .Data_Out_ALU(Bo));
  LED led_71 (.in(b_register_1_out_8));
  LED led_72 (.in(b_register_1_out_10));
  LED led_73 (.in(b_register_1_out_7));
  LED led_74 (.in(pc_program_counter_1_out_10));
  LED led_75 (.in(pc_program_counter_1_direct_out));
  LED led_76 (.in(pc_program_counter_1_out_12));
  LED led_77 (.in(pc_program_counter_1_out_13));
  LED led_78 (.in(a_register_1_out_13));
  LED led_79 (.in(a_register_1_out_14));
  LED led_80 (.in(a_register_1_direct_out));
  LED led_81 (.in(a_register_1_out_12));
  LED led_82 (.in(n8_bit_alu_1_out_11));
  LED led_83 (.in(n8_bit_alu_1_out_12));
  LED led_84 (.in(n8_bit_alu_1_out_10));
  LED led_85 (.in(n8_bit_alu_1_out_9));
  LED led_86 (.in(b_register_1_out_13));
  LED led_87 (.in(b_register_1_out_12));
  LED led_88 (.in(b_register_1_out_14));
  LED led_89 (.in(b_register_1_direct_out));
  LED led_90 (.in(pc_program_counter_1_out_15));
  LED led_91 (.in(pc_program_counter_1_out_14));
  LED led_92 (.in(a_register_1_out_15));
  LED led_93 (.in(b_register_1_out_15));

  // Other names for the same wires on the sheet: manuel = in_2; RESET = in_3

  // Notes on the sheet:
  //   Microcode ADDc falsch
  //   ICo = IBo
  //   ICo löschen
  //   Microcode updaten
  //   |
  //   100+50
  //   LDA 64
  //   ADD 31
  //   150
  //   =
  //   10010110
  //   CF
  //   ZF
  //   OP Code
  //   000 = AND
  //   001 = OR
  //   010 = XOR
  //   011 = NOR
  //   100 = ADD
  //   101 = EQU
  //   110 = SUB
endmodule

module _8_Bit_Register (
  input  [7:0] Data_In,
  input  WE,
  input  Clk,
  input  OE,
  input  in_5,
  output [7:0] Data_Out
);

  wire and_1_out, and_2_out, and_3_out, and_4_out, and_5_out, and_6_out, and_7_out, and_8_out, and_9_out,
       and_10_out, and_11_out, and_12_out, and_13_out, and_14_out, and_15_out, and_16_out, d_ff_1_q,
       d_ff_1_qn, d_ff_2_q, d_ff_2_qn, d_ff_3_q, d_ff_3_qn, d_ff_4_q, d_ff_4_qn, d_ff_5_q, d_ff_5_qn,
       d_ff_6_q, d_ff_6_qn, d_ff_7_q, d_ff_7_qn, d_ff_8_q, d_ff_8_qn, not_1_out, or_1_out, or_2_out,
       or_3_out, or_4_out, or_5_out, or_6_out, or_7_out, or_8_out;

  not not_1 (not_1_out, WE);
  and and_1 (and_1_out, d_ff_1_q, not_1_out);
  and and_2 (and_2_out, Data_In[0], WE);
  and and_3 (and_3_out, d_ff_2_q, not_1_out);
  and and_4 (and_4_out, Data_In[1], WE);
  and and_5 (and_5_out, d_ff_3_q, not_1_out);
  and and_6 (and_6_out, Data_In[2], WE);
  and and_7 (and_7_out, d_ff_4_q, not_1_out);
  and and_8 (and_8_out, Data_In[3], WE);
  and and_9 (and_9_out, d_ff_5_q, not_1_out);
  and and_10 (and_10_out, Data_In[4], WE);
  and and_11 (and_11_out, d_ff_6_q, not_1_out);
  and and_12 (and_12_out, Data_In[5], WE);
  and and_13 (and_13_out, d_ff_7_q, not_1_out);
  and and_14 (and_14_out, Data_In[6], WE);
  and and_15 (and_15_out, d_ff_8_q, not_1_out);
  and and_16 (and_16_out, Data_In[7], WE);
  or or_1 (or_1_out, and_1_out, and_2_out);
  or or_2 (or_2_out, and_3_out, and_4_out);
  or or_3 (or_3_out, and_5_out, and_6_out);
  or or_4 (or_4_out, and_7_out, and_8_out);
  or or_5 (or_5_out, and_9_out, and_10_out);
  or or_6 (or_6_out, and_11_out, and_12_out);
  or or_7 (or_7_out, and_13_out, and_14_out);
  or or_8 (or_8_out, and_15_out, and_16_out);
  D_Flip_Flop d_ff_1 (.clk(Clk), .D(or_1_out), .Q(d_ff_1_q), .Qn(d_ff_1_qn), .reset(OE));  // open: preset, en
  assign Data_Out[0] = in_5 ? ~d_ff_1_qn : 1'bz;  // Controlled_Inverter controlled_inverter_1
  D_Flip_Flop d_ff_2 (.clk(Clk), .D(or_2_out), .Q(d_ff_2_q), .Qn(d_ff_2_qn), .reset(OE));  // open: preset, en
  assign Data_Out[1] = in_5 ? ~d_ff_2_qn : 1'bz;  // Controlled_Inverter controlled_inverter_2
  D_Flip_Flop d_ff_3 (.clk(Clk), .D(or_3_out), .Q(d_ff_3_q), .Qn(d_ff_3_qn), .reset(OE));  // open: preset, en
  assign Data_Out[2] = in_5 ? ~d_ff_3_qn : 1'bz;  // Controlled_Inverter controlled_inverter_3
  D_Flip_Flop d_ff_4 (.clk(Clk), .D(or_4_out), .Q(d_ff_4_q), .Qn(d_ff_4_qn), .reset(OE));  // open: preset, en
  assign Data_Out[3] = in_5 ? ~d_ff_4_qn : 1'bz;  // Controlled_Inverter controlled_inverter_4
  D_Flip_Flop d_ff_5 (.clk(Clk), .D(or_5_out), .Q(d_ff_5_q), .Qn(d_ff_5_qn), .reset(OE));  // open: preset, en
  assign Data_Out[4] = in_5 ? ~d_ff_5_qn : 1'bz;  // Controlled_Inverter controlled_inverter_5
  D_Flip_Flop d_ff_6 (.clk(Clk), .D(or_6_out), .Q(d_ff_6_q), .Qn(d_ff_6_qn), .reset(OE));  // open: preset, en
  assign Data_Out[5] = in_5 ? ~d_ff_6_qn : 1'bz;  // Controlled_Inverter controlled_inverter_6
  D_Flip_Flop d_ff_7 (.clk(Clk), .D(or_7_out), .Q(d_ff_7_q), .Qn(d_ff_7_qn), .reset(OE));  // open: preset, en
  assign Data_Out[6] = in_5 ? ~d_ff_7_qn : 1'bz;  // Controlled_Inverter controlled_inverter_7
  D_Flip_Flop d_ff_8 (.clk(Clk), .D(or_8_out), .Q(d_ff_8_q), .Qn(d_ff_8_qn), .reset(OE));  // open: preset, en
  assign Data_Out[7] = in_5 ? ~d_ff_8_qn : 1'bz;  // Controlled_Inverter controlled_inverter_8

  // Other names for the same wires on the sheet: Clr = OE
endmodule

module CU__Control_Logic_Unit (
  input  clk,
  input  in_2,
  input  step_reset,
  input  [5:0] OP_code,
  input  [2:0] Flags,
  input  [3:0] RegID,
  input  reset,
  output out_8,
  output out_9,
  output out_10,
  output out_11,
  output out_12,
  output out_13,
  output out_14,
  output out_15,
  output out_16,
  output out_17,
  output out_18,
  output out_19,
  output out_20,
  output out_21,
  output out_22,
  output out_23,
  output out_24,
  output out_25,
  output out_26,
  output out_27,
  output out_28,
  output out_29,
  output out_30,
  output out_31,
  output out_32,
  output out_33,
  output out_34,
  output out_35,
  output out_36,
  output out_37,
  output out_38,
  output out_39,
  output [31:0] out_40,
  output out_41,
  output out_42,
  output out_43,
  output out_44
);

  wire and_1_out, and_2_out, and_3_out, and_4_out, and_5_out, and_6_out, and_8_out, and_9_out, and_10_out,
       and_11_out, and_12_out, and_13_out, and_14_out, and_15_out, and_16_out, and_17_out, and_18_out,
       and_19_out, and_20_out, and_21_out, d_ff_1_q, d_ff_2_q, d_ff_2_qn, d_ff_3_q, d_ff_3_qn, d_ff_4_q,
       d_ff_4_qn, d_ff_5_q, d_ff_5_qn, not_1_out, not_2_out, not_3_out, not_4_out, not_5_out, not_6_out,
       not_7_out, not_8_out, not_9_out, or_1_out, or_2_out, or_3_out, or_4_out, or_5_out, or_6_out;
  wire [3:0] and_7_out, not_10_out, not_15_out;
  wire [5:0] not_11_out;
  wire [7:0] controlled_buffer_1_out, rom_2_data;

  and and_1 (and_1_out, OP_code[4], OP_code[2], OP_code[1], not_9_out, not_8_out, not_6_out);
  and and_2 (and_2_out, OP_code[4], OP_code[2], OP_code[0], not_9_out, not_8_out, not_5_out);
  and and_3 (and_3_out, OP_code[4], OP_code[2], not_9_out, not_8_out, not_5_out, not_6_out);
  or or_1 (or_1_out, and_1_out, and_2_out, and_3_out, and_4_out);
  and and_4 (and_4_out, OP_code[4], OP_code[1], OP_code[0], not_9_out, not_8_out, not_7_out);
  D_Flip_Flop d_ff_1 (.clk(clk), .D(step_reset), .Q(d_ff_1_q), .reset(and_6_out));  // open: Qn, preset, en
  not not_1 (not_1_out, and_16_out);
  not not_2 (not_2_out, in_2);
  and and_5 (and_5_out, clk, not_2_out);
  not not_3 (not_3_out, and_5_out);
  and and_6 (and_6_out, ~clk, d_ff_1_q);  // AND_Gate
  not not_4 (not_4_out, OP_code[4]);
  not not_5 (not_5_out, OP_code[1]);
  not not_6 (not_6_out, OP_code[0]);
  not not_7 (not_7_out, OP_code[2]);
  not not_8 (not_8_out, OP_code[3]);
  not not_9 (not_9_out, OP_code[5]);
  assign and_7_out = {4{out_35}} & RegID;  // AND_Gate and_7, 4 bits wide
  and and_8 (and_8_out, d_ff_2_q, not_1_out);
  or or_2 (or_2_out, and_8_out, and_9_out);
  and and_9 (and_9_out, and_7_out[0], and_16_out);
  and and_10 (and_10_out, d_ff_3_q, not_1_out);
  or or_3 (or_3_out, and_10_out, and_11_out);
  and and_11 (and_11_out, and_7_out[1], and_16_out);
  and and_12 (and_12_out, d_ff_4_q, not_1_out);
  or or_4 (or_4_out, and_12_out, and_13_out);
  and and_13 (and_13_out, and_7_out[2], and_16_out);
  and and_14 (and_14_out, d_ff_5_q, not_1_out);
  or or_5 (or_5_out, and_14_out, and_15_out);
  and and_15 (and_15_out, and_7_out[3], and_16_out);
  Counter #(.width(4), .max('hf)) counter_1 (
    .load(1'b0), .count(1'b1), .Q({out_41, out_42, out_43, out_44}), .clk(not_3_out), .clr(and_6_out));  // open: D, carry
  and and_16 (and_16_out, out_35, and_5_out);
  D_Flip_Flop d_ff_2 (.clk(and_5_out), .D(or_2_out), .Q(d_ff_2_q), .Qn(d_ff_2_qn), .reset(reset));  // open: preset, en
  D_Flip_Flop d_ff_3 (.clk(and_5_out), .D(or_3_out), .Q(d_ff_3_q), .Qn(d_ff_3_qn), .reset(reset));  // open: preset, en
  D_Flip_Flop d_ff_4 (.clk(and_5_out), .D(or_4_out), .Q(d_ff_4_q), .Qn(d_ff_4_qn), .reset(reset));  // open: preset, en
  D_Flip_Flop d_ff_5 (.clk(and_5_out), .D(or_5_out), .Q(d_ff_5_q), .Qn(d_ff_5_qn), .reset(reset));  // open: preset, en
  assign not_10_out = ~{out_41, out_42, out_43, out_44};  // NOT_Gate not_10, 4 bits wide
  assign not_11_out = ~OP_code;  // NOT_Gate not_11, 6 bits wide
  ROM #(.addrWidth(13), .dataWidth(32)) rom_1 (
    .addr({OP_code, Flags, out_41, out_42, out_43, out_44}),
    .data({out_8, out_9, out_10, out_11, out_12, out_13, out_14, out_15, out_16, out_17, out_40[21:18], out_22, out_23, out_24, out_25, out_26, out_27, out_28, out_29, out_40[9:6], out_34, out_35, out_36, out_37, out_38, out_39}),
    .sel(1'b1));
  and and_17 (and_17_out, not_11_out[5], not_11_out[3], not_11_out[2], OP_code[4], OP_code[1], OP_code[0], not_10_out[3], not_10_out[2], out_43, out_44);
  not not_12 (not_15_out[3], d_ff_5_qn);
  not not_13 (not_15_out[2], d_ff_4_qn);
  not not_14 (not_15_out[1], d_ff_3_qn);
  not not_15 (not_15_out[0], d_ff_2_qn);
  and and_18 (and_18_out, not_11_out[5], not_11_out[3], not_11_out[1], not_11_out[0], OP_code[4], OP_code[2], not_10_out[3], not_10_out[1], out_42, out_44);
  and and_19 (and_19_out, not_11_out[5], not_11_out[3], not_11_out[1], OP_code[4], OP_code[2], OP_code[0], not_10_out[3], not_10_out[2], out_43, out_44);
  or or_6 (or_6_out, and_17_out, and_18_out, and_19_out, and_20_out, and_21_out);
  assign controlled_buffer_1_out = or_6_out ? rom_2_data : 8'bz;  // Controlled_Buffer controlled_buffer_1
  ROM #(.addrWidth(4)) rom_2 (.addr(not_15_out), .data(rom_2_data), .sel(or_1_out));
  and and_20 (and_20_out, not_11_out[5], not_11_out[3], not_11_out[1], OP_code[4], OP_code[2], OP_code[0], not_10_out[3], not_10_out[0], out_42, out_43);
  and and_21 (and_21_out, not_11_out[5], not_11_out[3], not_11_out[0], OP_code[4], OP_code[2], OP_code[1], not_10_out[3], not_10_out[2], out_43, out_44);
  or or_7 (out_18, out_40[21], controlled_buffer_1_out[7]);
  Pull_Resistor pull_resistor_1 (.node(controlled_buffer_1_out[6]));
  Pull_Resistor pull_resistor_2 (.node(controlled_buffer_1_out[7]));
  or or_8 (out_20, out_40[19], controlled_buffer_1_out[5]);
  or or_9 (out_21, out_40[18], controlled_buffer_1_out[4]);
  or or_10 (out_19, out_40[20], controlled_buffer_1_out[6]);
  Pull_Resistor pull_resistor_3 (.node(controlled_buffer_1_out[3]));
  Pull_Resistor pull_resistor_4 (.node(controlled_buffer_1_out[1]));
  Pull_Resistor pull_resistor_5 (.node(controlled_buffer_1_out[0]));
  Pull_Resistor pull_resistor_6 (.node(controlled_buffer_1_out[2]));
  Pull_Resistor pull_resistor_7 (.node(controlled_buffer_1_out[5]));
  Pull_Resistor pull_resistor_8 (.node(controlled_buffer_1_out[4]));
  or or_11 (out_32, out_40[7], controlled_buffer_1_out[1]);
  or or_12 (out_31, out_40[8], controlled_buffer_1_out[2]);
  or or_13 (out_30, out_40[9], controlled_buffer_1_out[3]);
  or or_14 (out_33, out_40[6], controlled_buffer_1_out[0]);

  assign {out_40[31:22], out_40[17:10], out_40[5:0]} = {out_8, out_9, out_10, out_11, out_12, out_13, out_14, out_15, out_16, out_17, out_22, out_23, out_24, out_25, out_26, out_27, out_28, out_29, out_34, out_35, out_36, out_37, out_38, out_39};

  // Notes on the sheet:
  //   Step
  //   contents of rom_1 (hex, n*v repeats v):
  //   2002000 24401000 40000400 13*0 2002000 24401000 40000400 13*0 2002000 24401000 40000400 13*0 2002000
  //   24401000 40000400 13*0 2002000 24401000 40000400 13*0 2002000 24401000 40000400 13*0 2002000
  //   24401000 40000400 13*0 2002000 24401000 40000400 13*0 2002000 24401000 2800000 24100000 40000000
  //   11*0 2002000 24401000 2800000 24100000 40000000 11*0 2002000 24401000 2800000 24100000 40000000 11*0
  //   2002000 24401000 2800000 24100000 40000000 11*0 2002000 24401000 2800000 24100000 40000000 11*0
  //   2002000 24401000 2800000 24100000 40000000 11*0 2002000 24401000 2800000 24100000 40000000 11*0
  //   2002000 24401000 2800000 24100000 40000000 11*0 2002000 24401000 2800000 24040000 40000000 11*0
  //   2002000 24401000 2800000 24040000 40000000 11*0 2002000 24401000 2800000 24040000 40000000 11*0
  //   2002000 24401000 2800000 24040000 40000000 11*0 2002000 24401000 2800000 24040000 40000000 11*0
  //   2002000 24401000 2800000 24040000 40000000 11*0 2002000 24401000 2800000 24040000 40000000 11*0
  //   2002000 24401000 2800000 24040000 40000000 11*0 2002000 24401000 2800000 24000200 40000000 11*0
  //   2002000 24401000 2800000 24000200 40000000 11*0 2002000 24401000 2800000 24000200 40000000 11*0
  //   2002000 24401000 2800000 24000200 40000000 11*0 2002000 24401000 2800000 24000200 40000000 11*0
  //   2002000 24401000 2800000 24000200 40000000 11*0 2002000 24401000 2800000 24000200 40000000 11*0
  //   2002000 24401000 2800000 24000200 40000000 11*0 2002000 24401000 3000000 24060000 124000 40000000
  //   10*0 2002000 24401000 3000000 24060000 124000 40000000 10*0 2002000 24401000 3000000 24060000 124000
  //   40000000 10*0 2002000 24401000 3000000 24060000 124000 40000000 10*0 2002000 24401000 3000000
  //   24060000 124000 40000000 10*0 2002000 24401000 3000000 24060000 124000 40000000 10*0 2002000
  //   24401000 3000000 24060000 124000 40000000 10*0 2002000 24401000 3000000 24060000 124000 40000000
  //   10*0 2002000 24401000 2406000 124000 40000000 11*0 2002000 24401000 24060000 124000 40000000 11*0
  //   2002000 24401000 24060000 124000 40000000 11*0 2002000 24401000 24060000 124000 40000000 11*0
  //   2002000 24401000 24060000 124000 40000000 11*0 2002000 24401000 24060000 124000 40000000 11*0
  //   2002000 24401000 24060000 124000 40000000 11*0 2002000 24401000 24060000 124000 40000000 11*0
  //   2002000 24401000 14*0 2002000 24401000 14*0 2002000 24401000 14*0 2002000 24401000 14*0 2002000
  //   24401000 14*0 2002000 24401000 14*0 2002000 24401000 14*0 2002000 24401000 14*0 2002000 24401000
  //   14*0 2002000 24401000 14*0 2002000 24401000 14*0 2002000 24401000 14*0 2002000 24401000 14*0 2002000
  //   24401000 14*0 2002000 24401000 14*0 2002000 24401000 14*0 2002000 24401000 14*0 2002000 24401000
  //   14*0 2002000 24401000 14*0 2002000 24401000 14*0 2002000 24401000 14*0 2002000 24401000 14*0 2002000
  //   24401000 14*0 2002000 24401000 14*0 2002000 24401000 14*0 2002000 24401000 14*0 2002000 24401000
  //   14*0 2002000 24401000 14*0 2002000 24401000 14*0 2002000 24401000 14*0 2002000 24401000 14*0 2002000
  //   24401000 14*0 2002000 24401000 14*0 2002000 24401000 14*0 2002000 24401000 14*0 2002000 24401000
  //   14*0 2002000 24401000 14*0 2002000 24401000 14*0 2002000 24401000 14*0 2002000 24401000 14*0 2002000
  //   24401000 80000000 13*0 2002000 24401000 80000000 13*0 2002000 24401000 80000000 13*0 2002000
  //   24401000 80000000 13*0 2002000 24401000 80000000 13*0 2002000 24401000 80000000 13*0 2002000
  //   24401000 80000000 13*0 2002000 24401000 80000000 13*0 2002000 24401000 14*0 2002000 24401000 14*0
  //   2002000 24401000 14*0 2002000 24401000 14*0 2002000 24401000 14*0 2002000 24401000 14*0 2002000
  //   24401000 14*0 2002000 24401000 14*0 2002000 24401000 14*0 2002000 24401000 14*0 2002000 24401000
  //   14*0 2002000 24401000 14*0 2002000 24401000 14*0 2002000 24401000 14*0 2002000 24401000 14*0 2002000
  //   24401000 14*0 2002000 24401000 14*0 2002000 24401000 14*0 2002000 24401000 14*0 2002000 24401000
  //   14*0 2002000 24401000 14*0 2002000 24401000 14*0 2002000 24401000 14*0 2002000 24401000 14*0 2002000
  //   24401000 14*0 2002000 24401000 14*0 2002000 24401000 14*0 2002000 24401000 14*0 2002000 24401000
  //   14*0 2002000 24401000 14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
  //   MOVIn
  //   MOVmo
  //   MOVR
  //   MOVR
  //   SETcr
endmodule

module MAR__Memory_Address_Register (
  input  RAM_Out,
  input  Bus_Out,
  input  Mode_select,
  input  in_4,
  input  [7:0] Manual_Address,
  input  [7:0] Address,
  input  clk,
  input  MAR_In,
  input  reset,
  output Mode,
  output out_11,
  output [7:0] RAM_Output,
  output [7:0] Bus_Output,
  output out_14,
  output out_15,
  output out_16,
  output Direct_Output,
  output out_18,
  output out_19,
  output out_20,
  output out_21
);

  wire and_2_out, and_3_out, and_4_out, and_5_out, and_6_out, and_7_out, and_8_out, and_9_out, and_10_out,
       and_11_out, and_12_out, and_13_out, and_14_out, and_15_out, and_16_out, and_17_out, or_9_out;
  wire [7:0] or_8_out;

  LED led_1 (.in(Mode_select));
  LED led_2 (.in(out_11));
  assign RAM_Output = {8{RAM_Out}} & {out_14, out_15, out_16, Direct_Output, out_18, out_19, out_20, out_21};  // AND_Gate and_1, 8 bits wide
  assign Bus_Output = Bus_Out ? {out_14, out_15, out_16, Direct_Output, out_18, out_19, out_20, out_21} : 8'bz;  // Controlled_Buffer controlled_buffer_1
  not not_1 (out_11, Mode_select);
  and and_2 (and_2_out, Mode_select, Manual_Address[6]);
  and and_3 (and_3_out, Mode_select, Manual_Address[7]);
  and and_4 (and_4_out, Mode_select, Manual_Address[5]);
  and and_5 (and_5_out, Mode_select, Manual_Address[3]);
  and and_6 (and_6_out, Mode_select, Manual_Address[4]);
  and and_7 (and_7_out, Mode_select, Manual_Address[2]);
  and and_8 (and_8_out, Mode_select, Manual_Address[1]);
  and and_9 (and_9_out, Mode_select, Manual_Address[0]);
  and and_10 (and_10_out, out_11, Address[7]);
  and and_11 (and_11_out, out_11, Address[6]);
  or or_1 (or_8_out[7], and_3_out, and_10_out);
  or or_2 (or_8_out[6], and_2_out, and_11_out);
  and and_12 (and_12_out, out_11, Address[4]);
  and and_13 (and_13_out, out_11, Address[5]);
  or or_3 (or_8_out[4], and_6_out, and_12_out);
  or or_4 (or_8_out[5], and_4_out, and_13_out);
  or or_5 (or_8_out[3], and_5_out, and_15_out);
  and and_14 (and_14_out, out_11, Address[2]);
  and and_15 (and_15_out, out_11, Address[3]);
  and and_16 (and_16_out, out_11, Address[1]);
  or or_6 (or_8_out[1], and_8_out, and_16_out);
  or or_7 (or_8_out[2], and_7_out, and_14_out);
  and and_17 (and_17_out, out_11, Address[0]);
  or or_8 (or_8_out[0], and_9_out, and_17_out);
  or or_9 (or_9_out, in_4, MAR_In);
  _8_Bit_Register u_8_bit_register_1 (
    .Data_Out({out_14, out_15, out_16, Direct_Output, out_18, out_19, out_20, out_21}), .Data_In(or_8_out),
    .WE(or_9_out), .Clk(clk), .in_5(1'b1), .OE(reset));

  assign Mode = Mode_select;

  // Notes on the sheet:
  //   Programming Mode
  //   running mode
endmodule

module RAM (
  input  WE,
  input  clk,
  input  OE,
  input  Mode,
  input  [7:0] address,
  input  [15:0] in_6,
  input  [15:0] in_7,
  input  Manual_Write,
  output out_9,
  output out_10,
  output out_11,
  output out_12,
  output out_13,
  output out_14,
  output out_15,
  output out_16,
  output direct_out,
  output out_18,
  output out_19,
  output out_20,
  output out_21,
  output out_22,
  output out_23,
  output out_24,
  output [15:0] out_25
);

  wire or_1_out;
  wire [15:0] and_1_out, and_2_out, not_1_out, or_2_out;

  or or_1 (or_1_out, Manual_Write, WE);
  assign not_1_out = ~{16{Mode}};  // NOT_Gate not_1, 16 bits wide
  assign and_1_out = {16{Mode}} & in_6;  // AND_Gate and_1, 16 bits wide
  assign and_2_out = not_1_out & in_7;  // AND_Gate and_2, 16 bits wide
  assign or_2_out = and_1_out | and_2_out;  // OR_Gate or_2, 16 bits wide
  assign out_25 = OE ? {out_9, out_10, out_11, out_12, out_13, out_14, out_15, out_16, direct_out, out_18, out_19, out_20, out_21, out_22, out_23, out_24} : 16'bz;  // Controlled_Buffer controlled_buffer_1
  RAM_part #(.dataWidth(16), .bus("separate")) ram_1 (
    .addr(address), .din(or_2_out),
    .data({out_9, out_10, out_11, out_12, out_13, out_14, out_15, out_16, direct_out, out_18, out_19, out_20, out_21, out_22, out_23, out_24}),
    .str(or_1_out), .sel(1'b1), .clk(clk), .ld(1'b1), .clr(1'b0));

  // Notes on the sheet:
  //   manual Data In
  //   Data In
  //   Data OUT
endmodule

module IR__Instruction_Register (
  input  [15:0] in_1,
  input  clk,
  input  II,
  input  reset,
  input  IO,
  output [7:0] out_6,
  output [7:0] out_7,
  output out_8,
  output out_9,
  output out_10,
  output out_11,
  output out_12,
  output out_13,
  output out_14,
  output direct_out,
  output out_16,
  output out_17,
  output out_18,
  output out_19,
  output out_20,
  output out_21,
  output out_22,
  output out_23
);

  assign out_6 = IO ? {out_16, out_17, out_18, out_19, out_20, out_21, out_22, out_23} : 8'bz;  // Controlled_Buffer controlled_buffer_1
  _8_Bit_Register u_8_bit_register_1 (
    .Data_Out({out_16, out_17, out_18, out_19, out_20, out_21, out_22, out_23}), .Data_In(in_1[7:0]),
    .WE(II), .Clk(clk), .in_5(1'b1), .OE(reset));
  _8_Bit_Register u_8_bit_register_2 (
    .Data_Out({out_7[7:1], direct_out}), .Data_In(in_1[15:8]), .WE(II), .Clk(clk), .in_5(1'b1), .OE(reset));

  assign out_7[0] = direct_out;
  assign out_8 = out_7[7];
  assign out_9 = out_7[6];
  assign out_10 = out_7[5];
  assign out_11 = out_7[4];
  assign out_12 = out_7[3];
  assign out_13 = out_7[2];
  assign out_14 = out_7[1];

  // Notes on the sheet:
  //   Data IN
  //   Value
  //   Instruction
  //   BUS OUT
  //   CU OUT
endmodule

module A_Register (
  input  OE,
  input  [7:0] Data_In,
  input  WE,
  input  Clk,
  input  Reset,
  output [7:0] Data_Out_ALU,
  output out_7,
  output out_8,
  output [7:0] Data_Out,
  output out_10,
  output direct_out,
  output out_12,
  output out_13,
  output out_14,
  output out_15
);

  wire and_1_out, and_2_out, and_3_out, and_4_out, and_5_out, and_6_out, and_7_out, and_8_out, and_9_out,
       and_10_out, and_11_out, and_12_out, and_13_out, and_14_out, and_15_out, and_16_out, d_ff_1_q,
       d_ff_2_q, d_ff_3_q, d_ff_4_q, d_ff_5_q, d_ff_6_q, d_ff_7_q, d_ff_8_q, not_1_out, or_1_out, or_2_out,
       or_3_out, or_4_out, or_5_out, or_6_out, or_7_out, or_8_out;
  wire [7:0] d_ff_1_qn;

  not not_1 (not_1_out, WE);
  and and_1 (and_1_out, d_ff_1_q, not_1_out);
  and and_2 (and_2_out, Data_In[0], WE);
  and and_3 (and_3_out, d_ff_2_q, not_1_out);
  and and_4 (and_4_out, Data_In[1], WE);
  and and_5 (and_5_out, d_ff_3_q, not_1_out);
  and and_6 (and_6_out, Data_In[2], WE);
  and and_7 (and_7_out, d_ff_4_q, not_1_out);
  and and_8 (and_8_out, Data_In[3], WE);
  and and_9 (and_9_out, d_ff_5_q, not_1_out);
  and and_10 (and_10_out, Data_In[4], WE);
  and and_11 (and_11_out, d_ff_6_q, not_1_out);
  and and_12 (and_12_out, Data_In[5], WE);
  and and_13 (and_13_out, d_ff_7_q, not_1_out);
  and and_14 (and_14_out, Data_In[6], WE);
  and and_15 (and_15_out, d_ff_8_q, not_1_out);
  and and_16 (and_16_out, Data_In[7], WE);
  or or_1 (or_1_out, and_1_out, and_2_out);
  or or_2 (or_2_out, and_3_out, and_4_out);
  or or_3 (or_3_out, and_5_out, and_6_out);
  or or_4 (or_4_out, and_7_out, and_8_out);
  or or_5 (or_5_out, and_9_out, and_10_out);
  or or_6 (or_6_out, and_11_out, and_12_out);
  or or_7 (or_7_out, and_13_out, and_14_out);
  or or_8 (or_8_out, and_15_out, and_16_out);
  D_Flip_Flop d_ff_1 (.clk(Clk), .D(or_1_out), .Q(d_ff_1_q), .Qn(d_ff_1_qn[0]), .reset(Reset));  // open: preset, en
  D_Flip_Flop d_ff_2 (.clk(Clk), .D(or_2_out), .Q(d_ff_2_q), .Qn(d_ff_1_qn[1]), .reset(Reset));  // open: preset, en
  D_Flip_Flop d_ff_3 (.clk(Clk), .D(or_3_out), .Q(d_ff_3_q), .Qn(d_ff_1_qn[2]), .reset(Reset));  // open: preset, en
  D_Flip_Flop d_ff_4 (.clk(Clk), .D(or_4_out), .Q(d_ff_4_q), .Qn(d_ff_1_qn[3]), .reset(Reset));  // open: preset, en
  D_Flip_Flop d_ff_5 (.clk(Clk), .D(or_5_out), .Q(d_ff_5_q), .Qn(d_ff_1_qn[4]), .reset(Reset));  // open: preset, en
  D_Flip_Flop d_ff_6 (.clk(Clk), .D(or_6_out), .Q(d_ff_6_q), .Qn(d_ff_1_qn[5]), .reset(Reset));  // open: preset, en
  D_Flip_Flop d_ff_7 (.clk(Clk), .D(or_7_out), .Q(d_ff_7_q), .Qn(d_ff_1_qn[6]), .reset(Reset));  // open: preset, en
  D_Flip_Flop d_ff_8 (.clk(Clk), .D(or_8_out), .Q(d_ff_8_q), .Qn(d_ff_1_qn[7]), .reset(Reset));  // open: preset, en
  not not_2 (out_7, d_ff_1_qn[7]);
  not not_3 (out_8, d_ff_1_qn[6]);
  not not_4 (out_10, d_ff_1_qn[5]);
  not not_5 (direct_out, d_ff_1_qn[4]);
  not not_6 (out_12, d_ff_1_qn[3]);
  not not_7 (out_13, d_ff_1_qn[2]);
  not not_8 (out_14, d_ff_1_qn[1]);
  not not_9 (out_15, d_ff_1_qn[0]);
  assign Data_Out_ALU = ~d_ff_1_qn;  // NOT_Gate not_10, 8 bits wide
  assign Data_Out = OE ? Data_Out_ALU : 8'bz;  // Controlled_Buffer controlled_buffer_1

  // Other names for the same wires on the sheet: Clr = Reset
endmodule

module B_Register (
  input  Data_Out_ALU,
  input  [7:0] Data_In,
  input  WE,
  input  Clk,
  input  Reset,
  output [7:0] out_6,
  output out_7,
  output out_8,
  output [7:0] Data_Out,
  output out_10,
  output direct_out,
  output out_12,
  output out_13,
  output out_14,
  output out_15
);

  wire and_1_out, and_2_out, and_3_out, and_4_out, and_5_out, and_6_out, and_7_out, and_8_out, and_9_out,
       and_10_out, and_11_out, and_12_out, and_13_out, and_14_out, and_15_out, and_16_out, d_ff_1_q,
       d_ff_2_q, d_ff_3_q, d_ff_4_q, d_ff_5_q, d_ff_6_q, d_ff_7_q, d_ff_8_q, not_1_out, or_1_out, or_2_out,
       or_3_out, or_4_out, or_5_out, or_6_out, or_7_out, or_8_out;
  wire [7:0] d_ff_1_qn;

  not not_1 (not_1_out, WE);
  and and_1 (and_1_out, d_ff_1_q, not_1_out);
  and and_2 (and_2_out, Data_In[0], WE);
  and and_3 (and_3_out, d_ff_2_q, not_1_out);
  and and_4 (and_4_out, Data_In[1], WE);
  and and_5 (and_5_out, d_ff_3_q, not_1_out);
  and and_6 (and_6_out, Data_In[2], WE);
  and and_7 (and_7_out, d_ff_4_q, not_1_out);
  and and_8 (and_8_out, Data_In[3], WE);
  and and_9 (and_9_out, d_ff_5_q, not_1_out);
  and and_10 (and_10_out, Data_In[4], WE);
  and and_11 (and_11_out, d_ff_6_q, not_1_out);
  and and_12 (and_12_out, Data_In[5], WE);
  and and_13 (and_13_out, d_ff_7_q, not_1_out);
  and and_14 (and_14_out, Data_In[6], WE);
  and and_15 (and_15_out, d_ff_8_q, not_1_out);
  and and_16 (and_16_out, Data_In[7], WE);
  or or_1 (or_1_out, and_1_out, and_2_out);
  or or_2 (or_2_out, and_3_out, and_4_out);
  or or_3 (or_3_out, and_5_out, and_6_out);
  or or_4 (or_4_out, and_7_out, and_8_out);
  or or_5 (or_5_out, and_9_out, and_10_out);
  or or_6 (or_6_out, and_11_out, and_12_out);
  or or_7 (or_7_out, and_13_out, and_14_out);
  or or_8 (or_8_out, and_15_out, and_16_out);
  D_Flip_Flop d_ff_1 (.clk(Clk), .D(or_1_out), .Q(d_ff_1_q), .Qn(d_ff_1_qn[0]), .reset(Reset));  // open: preset, en
  D_Flip_Flop d_ff_2 (.clk(Clk), .D(or_2_out), .Q(d_ff_2_q), .Qn(d_ff_1_qn[1]), .reset(Reset));  // open: preset, en
  D_Flip_Flop d_ff_3 (.clk(Clk), .D(or_3_out), .Q(d_ff_3_q), .Qn(d_ff_1_qn[2]), .reset(Reset));  // open: preset, en
  D_Flip_Flop d_ff_4 (.clk(Clk), .D(or_4_out), .Q(d_ff_4_q), .Qn(d_ff_1_qn[3]), .reset(Reset));  // open: preset, en
  D_Flip_Flop d_ff_5 (.clk(Clk), .D(or_5_out), .Q(d_ff_5_q), .Qn(d_ff_1_qn[4]), .reset(Reset));  // open: preset, en
  D_Flip_Flop d_ff_6 (.clk(Clk), .D(or_6_out), .Q(d_ff_6_q), .Qn(d_ff_1_qn[5]), .reset(Reset));  // open: preset, en
  D_Flip_Flop d_ff_7 (.clk(Clk), .D(or_7_out), .Q(d_ff_7_q), .Qn(d_ff_1_qn[6]), .reset(Reset));  // open: preset, en
  D_Flip_Flop d_ff_8 (.clk(Clk), .D(or_8_out), .Q(d_ff_8_q), .Qn(d_ff_1_qn[7]), .reset(Reset));  // open: preset, en
  not not_2 (out_7, d_ff_1_qn[7]);
  not not_3 (out_8, d_ff_1_qn[6]);
  not not_4 (out_10, d_ff_1_qn[5]);
  not not_5 (direct_out, d_ff_1_qn[4]);
  not not_6 (out_12, d_ff_1_qn[3]);
  not not_7 (out_13, d_ff_1_qn[2]);
  not not_8 (out_14, d_ff_1_qn[1]);
  not not_9 (out_15, d_ff_1_qn[0]);
  assign out_6 = ~d_ff_1_qn;  // NOT_Gate not_10, 8 bits wide
  assign Data_Out = Data_Out_ALU ? out_6 : 8'bz;  // Controlled_Buffer controlled_buffer_1

  // Other names for the same wires on the sheet: Clr = Reset
endmodule

module PC__Program_Counter (
  input  CO,
  input  clk,
  input  LOAD,
  input  [7:0] in_4,
  input  Reset,
  input  CE,
  output [7:0] out_7,
  output out_8,
  output out_9,
  output out_10,
  output direct_out,
  output out_12,
  output out_13,
  output out_14,
  output out_15,
  output Carry_Out
);

  wire and_1_out, and_2_out, and_3_out, and_4_out, and_5_out, and_6_out, and_7_out, and_8_out, and_9_out,
       and_10_out, and_11_out, and_12_out, and_13_out, and_14_out, and_15_out, and_16_out, and_17_out,
       and_18_out, and_19_out, and_20_out, and_21_out, and_22_out, and_23_out, and_24_out, and_25_out,
       and_26_out, and_27_out, and_28_out, and_29_out, and_30_out, and_31_out, and_32_out, and_33_out,
       and_34_out, and_35_out, and_36_out, and_37_out, and_38_out, and_39_out, and_40_out, not_1_out,
       not_2_out, not_3_out, not_4_out, not_5_out, not_6_out, not_7_out, not_8_out, not_9_out, not_10_out,
       not_11_out, not_12_out, not_13_out, not_14_out, not_15_out, not_16_out, not_17_out, not_18_out,
       not_19_out, not_20_out, or_1_out, or_2_out, or_3_out, or_4_out, or_5_out, or_6_out, or_7_out,
       or_8_out, or_9_out, or_10_out;

  not not_1 (not_1_out, LOAD);
  not not_2 (not_2_out, Reset);
  not not_3 (not_3_out, LOAD);
  not not_4 (not_4_out, Reset);
  and and_1 (and_1_out, and_40_out, CE);
  assign out_7 = CO ? {out_15, out_14, out_13, out_12, direct_out, out_10, out_9, out_8} : 8'bz;  // Controlled_Buffer controlled_buffer_1
  or or_1 (or_1_out, ~not_1_out, ~not_2_out);  // OR_Gate
  and and_2 (and_2_out, out_8, CE);
  and and_3 (and_3_out, out_9, out_8, CE);
  and and_4 (and_4_out, out_10, out_9, out_8, CE);
  or or_2 (or_2_out, ~not_3_out, ~not_4_out);  // OR_Gate
  and and_5 (and_5_out, out_12, and_1_out);
  and and_6 (and_6_out, out_13, out_12, and_1_out);
  and and_7 (and_7_out, out_14, out_13, out_12, and_1_out);
  and and_8 (and_8_out, or_1_out, not_6_out);
  and and_9 (and_9_out, in_4[0], not_2_out, or_1_out);
  and and_10 (and_10_out, or_1_out, not_8_out);
  and and_11 (and_11_out, in_4[1], not_2_out, or_1_out);
  and and_12 (and_12_out, or_1_out, not_10_out);
  and and_13 (and_13_out, in_4[2], not_2_out, or_1_out);
  and and_14 (and_14_out, or_1_out, not_12_out);
  and and_15 (and_15_out, in_4[3], not_2_out, or_1_out);
  and and_16 (and_16_out, or_2_out, not_14_out);
  and and_17 (and_17_out, in_4[4], not_4_out, or_2_out);
  and and_18 (and_18_out, or_2_out, not_16_out);
  and and_19 (and_19_out, in_4[5], not_4_out, or_2_out);
  and and_20 (and_20_out, or_2_out, not_18_out);
  and and_21 (and_21_out, in_4[6], not_4_out, or_2_out);
  and and_22 (and_22_out, or_2_out, not_20_out);
  and and_23 (and_23_out, in_4[7], not_4_out, or_2_out);
  not not_5 (not_5_out, and_8_out);
  or or_3 (or_3_out, CE, or_1_out);
  not not_6 (not_6_out, and_9_out);
  not not_7 (not_7_out, and_10_out);
  or or_4 (or_4_out, and_2_out, or_1_out);
  not not_8 (not_8_out, and_11_out);
  not not_9 (not_9_out, and_12_out);
  or or_5 (or_5_out, and_3_out, or_1_out);
  not not_10 (not_10_out, and_13_out);
  not not_11 (not_11_out, and_14_out);
  or or_6 (or_6_out, and_4_out, or_1_out);
  not not_12 (not_12_out, and_15_out);
  not not_13 (not_13_out, and_16_out);
  or or_7 (or_7_out, and_1_out, or_2_out);
  not not_14 (not_14_out, and_17_out);
  not not_15 (not_15_out, and_18_out);
  or or_8 (or_8_out, and_5_out, or_2_out);
  not not_16 (not_16_out, and_19_out);
  not not_17 (not_17_out, and_20_out);
  or or_9 (or_9_out, and_6_out, or_2_out);
  not not_18 (not_18_out, and_21_out);
  not not_19 (not_19_out, and_22_out);
  or or_10 (or_10_out, and_7_out, or_2_out);
  not not_20 (not_20_out, and_23_out);
  and and_24 (and_24_out, not_5_out, or_3_out);
  and and_25 (and_25_out, or_3_out, not_6_out);
  and and_26 (and_26_out, not_7_out, or_4_out);
  and and_27 (and_27_out, or_4_out, not_8_out);
  and and_28 (and_28_out, not_9_out, or_5_out);
  and and_29 (and_29_out, or_5_out, not_10_out);
  and and_30 (and_30_out, not_11_out, or_6_out);
  and and_31 (and_31_out, or_6_out, not_12_out);
  and and_32 (and_32_out, not_13_out, or_7_out);
  and and_33 (and_33_out, or_7_out, not_14_out);
  and and_34 (and_34_out, not_15_out, or_8_out);
  and and_35 (and_35_out, or_8_out, not_16_out);
  and and_36 (and_36_out, not_17_out, or_9_out);
  and and_37 (and_37_out, or_9_out, not_18_out);
  and and_38 (and_38_out, not_19_out, or_10_out);
  and and_39 (and_39_out, or_10_out, not_20_out);
  J_K_Flip_Flop j_k_ff_1 (.J(and_24_out), .clk(clk), .K(and_25_out), .Q(out_8), .reset(Reset));  // open: Qn, preset, en
  J_K_Flip_Flop j_k_ff_2 (.J(and_26_out), .clk(clk), .K(and_27_out), .Q(out_9), .reset(Reset));  // open: Qn, preset, en
  J_K_Flip_Flop j_k_ff_3 (
    .J(and_28_out), .clk(clk), .K(and_29_out), .Q(out_10), .reset(Reset));  // open: Qn, preset, en
  J_K_Flip_Flop j_k_ff_4 (
    .J(and_30_out), .clk(clk), .K(and_31_out), .Q(direct_out), .reset(Reset));  // open: Qn, preset, en
  and and_40 (and_40_out, direct_out, out_10, out_9, out_8, CE);
  J_K_Flip_Flop j_k_ff_5 (
    .J(and_32_out), .clk(clk), .K(and_33_out), .Q(out_12), .reset(Reset));  // open: Qn, preset, en
  J_K_Flip_Flop j_k_ff_6 (
    .J(and_34_out), .clk(clk), .K(and_35_out), .Q(out_13), .reset(Reset));  // open: Qn, preset, en
  J_K_Flip_Flop j_k_ff_7 (
    .J(and_36_out), .clk(clk), .K(and_37_out), .Q(out_14), .reset(Reset));  // open: Qn, preset, en
  J_K_Flip_Flop j_k_ff_8 (
    .J(and_38_out), .clk(clk), .K(and_39_out), .Q(out_15), .reset(Reset));  // open: Qn, preset, en
  and and_41 (Carry_Out, out_15, out_14, out_13, out_12, CE);

  // Notes on the sheet:
  //   BUS
endmodule

module Flag_Register (
  input  [2:0] Data_in,
  input  WE,
  input  clk,
  input  reset,
  output [2:0] Data_out
);

  wire and_1_out, and_2_out, and_3_out, and_4_out, and_5_out, and_6_out, d_ff_1_q, d_ff_2_q, d_ff_3_q,
       not_1_out, or_1_out, or_2_out, or_3_out;
  wire [2:0] d_ff_1_qn;

  not not_1 (not_1_out, WE);
  and and_1 (and_1_out, d_ff_1_q, not_1_out);
  and and_2 (and_2_out, Data_in[0], WE);
  and and_3 (and_3_out, d_ff_2_q, not_1_out);
  and and_4 (and_4_out, Data_in[1], WE);
  and and_5 (and_5_out, d_ff_3_q, not_1_out);
  and and_6 (and_6_out, Data_in[2], WE);
  D_Flip_Flop d_ff_1 (.clk(clk), .D(or_1_out), .Q(d_ff_1_q), .Qn(d_ff_1_qn[0]), .reset(reset));  // open: preset, en
  or or_1 (or_1_out, and_1_out, and_2_out);
  D_Flip_Flop d_ff_2 (.clk(clk), .D(or_2_out), .Q(d_ff_2_q), .Qn(d_ff_1_qn[1]), .reset(reset));  // open: preset, en
  or or_2 (or_2_out, and_3_out, and_4_out);
  D_Flip_Flop d_ff_3 (.clk(clk), .D(or_3_out), .Q(d_ff_3_q), .Qn(d_ff_1_qn[2]), .reset(reset));  // open: preset, en
  or or_3 (or_3_out, and_5_out, and_6_out);
  assign Data_out = ~d_ff_1_qn;  // NOT_Gate not_2, 3 bits wide
endmodule
