// Logisim project Dragon2_CPU.circ as structural Verilog: 4 circuits, main circuit Dragon_2_CPU
module Dragon_2_CPU (
  input  in_1
);

  wire Ao, Aw, Bo, Bw, clock_1_out, clock_2_out, clock_3_out, clock_4_out, clock_5_out, clock_6_out,
       clock_7_out, clock_8_out, clock_9_out, clock_10_out, clock_11_out, d_ff_1_q, d_ff_1_qn, d_ff_2_qn,
       decoder_1_out7, DRAMo, DRAMw, Fl, FLG_C, FLG_Z, IRw, not_1_out, not_2_out, not_3_out, or_1_out,
       or_2_out, PRAMo, PRAMw, rst, So, Stko, Stkw, undriven_2, undriven_3, Xo, Xw, Yo, Yw;
  wire [2:0] bit_extender_2_out, bit_extender_3_out, register_1_q, undriven_4;
  wire [2:2] undriven;
  wire [7:0] adder_1_out, and_1_out, bit_extender_1_out, controlled_buffer_1_out, counter_1_q, Data_RAM_dout,
       multiplexer_1_out, nor_1_out, or_3_out, Program_RAM_dout, pull_resistor_1_node, ram_1_dout,
       register_2_q, register_3_q, register_4_q, register_5_q, register_6_q, register_7_q, register_8_q,
       shifter_1_out, shifter_2_out, xor_1_out, xor_2_out;

  D_Flip_Flop d_ff_1 (.D(d_ff_1_qn), .clk(in_1), .Q(d_ff_1_q), .Qn(d_ff_1_qn), .reset(rst));  // open: preset
  Register #(.width(3)) register_1 (
    .D({undriven[2], FLG_Z, FLG_C}), .en(Fl), .clk(clock_1_out), .Q(register_1_q));  // open: clr
  Clock clock_1 (.out(clock_1_out));
  D_Flip_Flop d_ff_2 (.D(d_ff_2_qn), .clk(d_ff_1_q), .Qn(d_ff_2_qn), .reset(rst));  // open: Q, preset
  not not_1 (not_1_out, d_ff_1_q);
  Clock clock_2 (.out(clock_2_out));
  LedBar #(.matrixcols(3)) ledbar_1 (.led0(register_1_q[2]), .led1(register_1_q[1]), .led2(register_1_q[0]));
  not not_2 (not_2_out, d_ff_2_qn);
  Register register_2 (.D(controlled_buffer_1_out), .en(undriven_2), .clk(clock_2_out), .Q(register_2_q), .clr(rst));
  not not_3 (not_3_out, Stko);
  or or_1 (or_1_out, Stko, Stkw);
  Register register_3 (.D(controlled_buffer_1_out), .en(undriven_3), .clk(clock_2_out), .Q(register_3_q), .clr(rst));
  or or_2 (or_2_out, Stkw, not_3_out);
  Counter counter_1 (
    .clr(rst), .load(1'b0), .up(or_2_out), .count(or_1_out), .clk(clock_3_out), .Q(counter_1_q));  // open: D, carry
  Clock clock_3 (.out(clock_3_out));
  RAM #(.addrWidth(16)) Data_RAM (
    .addr({register_2_q, register_3_q}), .we(DRAMw), .oe(DRAMo), .clk(clock_4_out),
    .din(controlled_buffer_1_out), .dout(Data_RAM_dout));
  Clock clock_4 (.out(clock_4_out));
  RAM #(.addrWidth(16)) Program_RAM (
    .addr({register_2_q, register_3_q}), .we(PRAMw), .oe(PRAMo), .clk(clock_5_out),
    .din(controlled_buffer_1_out), .dout(Program_RAM_dout));
  Clock clock_5 (.out(clock_5_out));
  Decoder #(.select(3)) decoder_1 (
    .out7(decoder_1_out7), .sel(undriven_4));  // open: out0, out1, out2, out3, out4, out5, out6, en
  assign xor_1_out = register_5_q ^ bit_extender_1_out;  // XOR_Gate xor_1, 8 bits wide
  assign bit_extender_1_out = {{7{decoder_1_out7}}, decoder_1_out7};  // Bit_Extender bit_extender_1
  RAM ram_1 (
    .addr(counter_1_q), .we(Stkw), .oe(Stko), .clk(clock_6_out), .din(controlled_buffer_1_out),
    .dout(ram_1_dout));
  Clock clock_6 (.out(clock_6_out));
  assign and_1_out = register_4_q & register_4_q;  // AND_Gate and_1, 8 bits wide
  assign or_3_out = register_4_q | register_4_q;  // OR_Gate or_3, 8 bits wide
  assign xor_2_out = register_4_q ^ register_4_q;  // XOR_Gate xor_2, 8 bits wide
  assign nor_1_out = ~(register_4_q | register_4_q);  // NOR_Gate nor_1, 8 bits wide
  Shifter shifter_1 (.in(register_4_q), .\dist (bit_extender_2_out), .out(shifter_1_out));
  Bit_Extender #(.out_width(3)) bit_extender_2 (.in(register_4_q), .out(bit_extender_2_out));
  Shifter #(.shift("lr")) shifter_2 (.in(register_4_q), .\dist (bit_extender_3_out), .out(shifter_2_out));
  Bit_Extender #(.out_width(3)) bit_extender_3 (.in(register_4_q), .out(bit_extender_3_out));
  Adder adder_1 (.a(register_4_q), .b(xor_1_out), .out(adder_1_out), .cin(decoder_1_out7), .cout(FLG_C));
  Pull_Resistor pull_resistor_1 (.node(pull_resistor_1_node));
  assign controlled_buffer_1_out = DRAMo ? Data_RAM_dout : 8'bz;  // Controlled_Buffer controlled_buffer_1
  assign controlled_buffer_1_out = PRAMo ? Program_RAM_dout : 8'bz;  // Controlled_Buffer controlled_buffer_2
  Multiplexer #(.select(3), .width(8)) multiplexer_1 (
    .in0(and_1_out), .in1(or_3_out), .in2(xor_2_out), .in3(nor_1_out), .in4(shifter_1_out),
    .in5(shifter_2_out), .in6(adder_1_out), .in7(pull_resistor_1_node), .out(multiplexer_1_out),
    .sel(undriven_4));
  or or_4 (FLG_Z, multiplexer_1_out[7], multiplexer_1_out[6], multiplexer_1_out[5], multiplexer_1_out[4], multiplexer_1_out[3], multiplexer_1_out[2], multiplexer_1_out[1], multiplexer_1_out[0]);
  Register register_4 (.D(controlled_buffer_1_out), .en(Aw), .clk(clock_7_out), .Q(register_4_q), .clr(rst));
  Clock clock_7 (.out(clock_7_out));
  Register register_5 (.D(controlled_buffer_1_out), .en(Bw), .clk(clock_8_out), .Q(register_5_q), .clr(rst));
  Clock clock_8 (.out(clock_8_out));
  Register register_6 (.D(controlled_buffer_1_out), .en(Xw), .clk(clock_9_out), .Q(register_6_q), .clr(rst));
  Clock clock_9 (.out(clock_9_out));
  Register register_7 (.D(controlled_buffer_1_out), .en(Yw), .clk(clock_10_out), .Q(register_7_q), .clr(rst));
  Clock clock_10 (.out(clock_10_out));
  Register register_8 (.D(controlled_buffer_1_out), .en(IRw), .clk(clock_11_out), .Q(register_8_q), .clr(rst));
  Clock clock_11 (.out(clock_11_out));
  Pull_Resistor pull_resistor_2 (.node(controlled_buffer_1_out[7]));
  assign controlled_buffer_1_out = So ? multiplexer_1_out : 8'bz;  // Controlled_Buffer controlled_buffer_3
  assign controlled_buffer_1_out = Ao ? register_4_q : 8'bz;  // Controlled_Buffer controlled_buffer_4
  assign controlled_buffer_1_out = Bo ? register_5_q : 8'bz;  // Controlled_Buffer controlled_buffer_5
  assign controlled_buffer_1_out = Xo ? register_6_q : 8'bz;  // Controlled_Buffer controlled_buffer_6
  assign controlled_buffer_1_out = Yo ? register_7_q : 8'bz;  // Controlled_Buffer controlled_buffer_7
  assign controlled_buffer_1_out = Stko ? ram_1_dout : 8'bz;  // Controlled_Buffer controlled_buffer_8
  Pull_Resistor pull_resistor_3 (.node(controlled_buffer_1_out[6]));
  Pull_Resistor pull_resistor_4 (.node(controlled_buffer_1_out[5]));
  Pull_Resistor pull_resistor_5 (.node(controlled_buffer_1_out[4]));
  Pull_Resistor pull_resistor_6 (.node(controlled_buffer_1_out[3]));
  Pull_Resistor pull_resistor_7 (.node(controlled_buffer_1_out[2]));
  Pull_Resistor pull_resistor_8 (.node(controlled_buffer_1_out[1]));
  Pull_Resistor pull_resistor_9 (.node(controlled_buffer_1_out[0]));
endmodule

module Register_8_Bit (
  input  Reset,
  input  WE,
  input  [7:0] Bus_in,
  input  OE,
  output [7:0] Bus_out,
  output out_6,
  output out_7,
  output out_8,
  output out_9,
  output out_10,
  output out_11,
  output out_12,
  output out_13
);

  wire clock_1_out;

  Register register_1 (
    .D(Bus_in), .en(WE), .clk(clock_1_out), .Q({out_6, out_7, out_8, out_9, out_10, out_11, out_12, out_13}),
    .clr(Reset));
  Clock clock_1 (.out(clock_1_out));
  assign Bus_out = OE ? {out_6, out_7, out_8, out_9, out_10, out_11, out_12, out_13} : 8'bz;  // Controlled_Buffer controlled_buffer_1
endmodule

module Control_Logic (
  input  [7:0] Instruction,
  input  [3:0] Flags,
  input  Int,
  input  step_rst
);

  wire clock_1_out, not_1_out;
  wire [3:0] counter_1_q;

  Counter #(.max('hf), .width(4)) counter_1 (
    .clr(step_rst), .clk(not_1_out), .Q(counter_1_q));  // open: load, up, count, D, carry
  Clock clock_1 (.out(clock_1_out));
  not not_1 (not_1_out, clock_1_out);
  ROM #(.addrWidth(12), .dataWidth(32)) rom_1 (.addr({counter_1_q, Instruction}));  // open: data
endmodule

module IO_Handler (
  input  IO_in,
  input  [7:0] main_bus,
  input  IO_send,
  input  n3xt,
  input  IO_reset,
  input  IO_out,
  input  IO_WE,
  input  clk_in0,
  input  in_9,
  input  in_10,
  input  in_11,
  input  in_12,
  input  data_in0,
  input  in_14,
  input  in_15,
  input  in_16,
  input  in_17,
  input  in_18,
  output [7:0] main_bus_out,
  output Int
);

  wire and_2_out, and_3_out, and_4_out, and_5_out, and_6_out, and_7_out, and_8_out, and_9_out, clock_1_out,
       clock_2_out, clock_3_out, clock_4_out, clock_5_out, controlled_buffer_5_out, controlled_buffer_6_out,
       controlled_buffer_7_out, controlled_buffer_8_out, d_ff_1_q, d_ff_1_qn, decoder_1_out0, decoder_1_out5,
       decoder_2_out0, decoder_2_out1, decoder_2_out2, decoder_2_out3, n74165_1_pin9, not_1_out, or_1_out,
       or_2_out, or_3_out, or_4_out, or_5_out, shift_register_1_p1, shift_register_1_p2, shift_register_1_p3,
       shift_register_1_p4, shift_register_2_p4, undriven, undriven_2, undriven_3, undriven_4, undriven_7;
  wire [1:0] shift_register_2_p2;
  wire [2:0] counter_1_q;
  wire [7:0] controlled_buffer_1_out, register_1_q, register_2_q, register_3_q, register_4_q, register_5_q,
       register_6_q, shift_register_1_p15, undriven_5, undriven_6;

  and and_1 (Int, or_1_out, shift_register_1_p1);
  Clock clock_1 (.out(clock_1_out));
  and and_2 (and_2_out, n3xt, or_1_out);
  Clock clock_2 (.out(clock_2_out));
  and and_3 (and_3_out, clock_2_out, not_1_out);
  not not_1 (not_1_out, or_1_out);
  or or_1 (or_1_out, d_ff_1_q, undriven, undriven_2, undriven_3);
  Counter #(.max('h7), .width(3)) counter_1 (
    .clr(or_2_out), .clk(or_3_out), .Q(counter_1_q));  // open: load, up, count, D, carry
  or or_2 (or_2_out, IO_reset, decoder_1_out5);
  or or_3 (or_3_out, and_2_out, and_3_out);
  and and_4 (and_4_out, shift_register_1_p1, and_6_out);
  D_Flip_Flop d_ff_1 (.Q(d_ff_1_q), .Qn(d_ff_1_qn), .preset(and_4_out), .reset(or_4_out));  // open: D, clk
  or or_4 (or_4_out, and_5_out, IO_reset);
  // Shift_Register #(.length(25)) shift_register_1: pin names not known; wires that end beside it: shift_register_1_p1, shift_register_1_p2, shift_register_1_p3, shift_register_1_p4, or_4_out, clk_in0, data_in0, undriven_5[1], undriven_5[2], undriven_5[3], undriven_5[4], undriven_5[5], undriven_5[6], undriven_5[7], shift_register_1_p15[0], shift_register_1_p15[1], shift_register_1_p15[2], shift_register_1_p15[3]
  and and_5 (and_5_out, d_ff_1_q, shift_register_1_p4);
  Decoder #(.select(3)) decoder_1 (
    .out0(decoder_1_out0), .out1(shift_register_1_p1), .out2(shift_register_1_p2),
    .out3(shift_register_1_p3), .out4(shift_register_1_p4), .out5(decoder_1_out5), .sel(counter_1_q),
    .en(1'b1));  // open: out6, out7
  and and_6 (and_6_out, undriven_4, or_5_out);
  or or_5 (or_5_out, undriven_5[0], undriven_5[1], undriven_5[2], undriven_5[3], undriven_5[4], undriven_5[5], undriven_5[6], undriven_5[7]);
  Register register_1 (.D(controlled_buffer_1_out), .en(IO_WE), .clk(clock_3_out), .Q(register_1_q), .clr(IO_reset));
  Clock clock_3 (.out(clock_3_out));
  assign controlled_buffer_1_out = and_7_out ? undriven_5 : 8'bz;  // Controlled_Buffer controlled_buffer_1
  assign controlled_buffer_1_out = and_8_out ? shift_register_1_p15 : 8'bz;  // Controlled_Buffer controlled_buffer_2
  assign controlled_buffer_1_out = and_9_out ? undriven_6 : 8'bz;  // Controlled_Buffer controlled_buffer_3
  assign main_bus_out = IO_out ? register_1_q : 8'bz;  // Controlled_Buffer controlled_buffer_4
  Counter #(.max('h8), .width(4)) counter_2 (.clr(IO_reset));  // open: load, up, count, clk, D, carry, Q
  and and_7 (and_7_out, d_ff_1_q, shift_register_1_p1);
  and and_8 (and_8_out, d_ff_1_q, shift_register_1_p2);
  and and_9 (and_9_out, d_ff_1_q, shift_register_1_p3);
  Register register_2 (.D(main_bus), .en(IO_in), .clk(clock_4_out), .Q(register_2_q), .clr(undriven_7));
  Clock clock_4 (.out(clock_4_out));
  assign controlled_buffer_5_out = d_ff_1_qn ? shift_register_1_p1 : 1'bz;  // Controlled_Buffer controlled_buffer_5
  assign controlled_buffer_6_out = d_ff_1_qn ? shift_register_1_p2 : 1'bz;  // Controlled_Buffer controlled_buffer_6
  assign controlled_buffer_7_out = d_ff_1_qn ? shift_register_1_p3 : 1'bz;  // Controlled_Buffer controlled_buffer_7
  assign controlled_buffer_8_out = d_ff_1_qn ? shift_register_1_p4 : 1'bz;  // Controlled_Buffer controlled_buffer_8
  Register register_3 (.D(register_2_q), .en(IO_in), .clk(clock_4_out), .Q(register_3_q), .clr(undriven_7));
  Controlled_Buffer #(.width(8)) controlled_buffer_9 (.in(register_2_q));  // open: out, en
  Register register_4 (.D(register_3_q), .en(IO_in), .clk(clock_4_out), .Q(register_4_q), .clr(undriven_7));
  Controlled_Buffer #(.width(8)) controlled_buffer_10 (.in(register_3_q));  // open: out, en
  Controlled_Buffer #(.width(8)) controlled_buffer_11 (.in(register_4_q));  // open: out, en
  Clock clock_5 (.out(clock_5_out));
  Register register_5 (.D(register_4_q), .en(IO_in), .clk(clock_4_out), .Q(register_5_q), .clr(undriven_7));
  Controlled_Buffer #(.width(8)) controlled_buffer_12 (.in(register_5_q));  // open: out, en
  Register register_6 (.D(register_5_q), .en(IO_in), .clk(clock_4_out), .Q(register_6_q), .clr(undriven_7));
  Controlled_Buffer #(.width(8)) controlled_buffer_13 (.in(register_6_q));  // open: out, en
  _74165 #(.ShowInternalStructure("true")) u_74165_1 (
    .pin1(in_14), .pin2(clock_5_out), .pin3(in_15), .pin4(in_16), .pin5(in_17), .pin6(in_18), .pin14(in_9),
    .pin13(in_10), .pin12(in_11), .pin11(in_12), .pin9(n74165_1_pin9));  // open: pin7, pin15, pin10
  Decoder #(.select(2)) decoder_2 (
    .out0(decoder_2_out0), .out1(decoder_2_out1), .out2(decoder_2_out2), .out3(decoder_2_out3),
    .sel(shift_register_2_p2));  // open: en
  // Shift_Register #(.length(40)) shift_register_2: pin names not known; wires that end beside it: n74165_1_pin9, shift_register_2_p2, clock_1_out, shift_register_2_p4
endmodule
