// Logisim project Dragon_3_2.circ as structural Verilog: 1 circuit, main circuit main
module main (
  input  in_1
);

  wire and_1_out, and_2_out, and_4_out, button_1_out, button_2_out, clk, clk_inv, clock_1_out,
       controlled_buffer_23_out, Ctrl_A_const, Ctrl_L_const, Ctrl_noFetch, Ctrl_PC_A_addr_BUS,
       Ctrl_PC_A_Xfer_BUS, Ctrl_PC_dec, Ctrl_PC_inc, Ctrl_PC_L, Ctrl_SP_A_addr_BUS, Ctrl_SP_A_Xfer_BUS,
       Ctrl_Xfer_A_Addr_BUS, Ctrl_Xfer_A_MAIN_BUS_L, Ctrl_Xfer_A_MAIN_BUS_R, Ctrl_Xfer_A_Xfer_BUS,
       Ctrl_Xfer_L_L, Ctrl_Xfer_R_L, Flag_1, Flag_2, Flag_3, Flag_4, Flag_5, Flag_6, Flag_7,
       GPR_A_ALU_LEFT_out, GPR_A_ALU_RIGHT_out, GPR_A_MAIN_out, GPR_A_write, GPR_B_ALU_LEFT_out,
       GPR_B_ALU_RIGHT_out, GPR_B_MAIN_out, GPR_B_write, GPR_C_ALU_LEFT_out, GPR_C_ALU_RIGHT_out,
       GPR_C_MAIN_out, GPR_C_write, GPR_D_ALU_LEFT_out, GPR_D_ALU_RIGHT_out, GPR_D_MAIN_out, GPR_D_write,
       NIL, not_2_out, not_3_out, or_1_out, or_2_out, or_5_out, or_6_out, PCdec, PCinc, PCload, por_1_out,
       por_2_out, RAMwrite, reset;
  wire [2:0] Ctrl_GPR_A, Ctrl_GPR_ALU_L, Ctrl_GPR_ALU_R, Ctrl_GPR_L;
  wire [7:0] ALU_LEFT, ALU_RIGHT, controlled_buffer_22_out, controlled_buffer_24_out, MAIN_BUS, Memory_BUS,
       register_1_q, register_2_q, register_3_q, register_5_q, register_6_q, register_10_q, register_11_q,
       register_13_q, register_14_q, register_15_q, rom_1_data, rom_2_data, rom_3_data, rom_4_data,
       rom_5_data, rom_6_data, undriven, undriven_2;
  wire [15:0] Address_BUS, controlled_buffer_26_out, controlled_buffer_27_out, counter_1_q, counter_2_q,
       counter_3_q, counter_4_q, PC_q, register_4_q, register_7_q, register_8_q, Xfer_BUS;
  wire [15:2] register_9_q;
  wire [15:4] register_12_q;

  LED led_1 (.in(clk));
  Button button_1 (.out(button_1_out));
  Register register_1 (.D(MAIN_BUS), .en(GPR_A_write), .clk(clk), .Q(register_1_q), .clr(reset));
  Register register_2 (.D(MAIN_BUS), .en(GPR_B_write), .clk(clk), .Q(register_2_q), .clr(reset));
  Register register_3 (.D(Memory_BUS), .en(Ctrl_L_const), .clk(clk), .Q(register_3_q), .clr(reset));
  Pull_Resistor pull_resistor_1 (.node(Ctrl_PC_dec));
  Counter #(.max('hffff), .width(16)) counter_1 (
    .clr(reset), .load(Ctrl_PC_L), .up(Ctrl_PC_inc), .count(1'b1), .clk(or_1_out), .D(Xfer_BUS),
    .Q(counter_1_q));  // open: carry
  or or_1 (or_1_out, Ctrl_PC_inc, Ctrl_PC_dec);
  Counter #(.max('hffff), .width(16)) counter_2 (
    .clr(reset), .load(NIL), .up(NIL), .count(1'b1), .clk(or_2_out), .D(Xfer_BUS), .Q(counter_2_q));  // open: carry
  or or_2 (or_2_out, NIL, NIL);
  Clock clock_1 (.out(clock_1_out));
  and and_1 (and_1_out, button_1_out, in_1);
  and and_2 (and_2_out, ~in_1, clock_1_out);  // AND_Gate
  or or_3 (clk, and_1_out, and_2_out);
  not not_1 (clk_inv, clk);
  and and_3 (Ctrl_PC_inc, clk_inv, 1'b1);
  assign MAIN_BUS = GPR_A_MAIN_out ? register_1_q : 8'bz;  // Controlled_Buffer controlled_buffer_1
  assign ALU_LEFT = GPR_A_ALU_LEFT_out ? register_1_q : 8'bz;  // Controlled_Buffer controlled_buffer_2
  assign ALU_RIGHT = GPR_A_ALU_RIGHT_out ? register_1_q : 8'bz;  // Controlled_Buffer controlled_buffer_3
  assign MAIN_BUS = GPR_B_MAIN_out ? register_2_q : 8'bz;  // Controlled_Buffer controlled_buffer_4
  assign ALU_LEFT = GPR_B_ALU_LEFT_out ? register_2_q : 8'bz;  // Controlled_Buffer controlled_buffer_5
  assign ALU_RIGHT = GPR_B_ALU_RIGHT_out ? register_2_q : 8'bz;  // Controlled_Buffer controlled_buffer_6
  assign MAIN_BUS = Ctrl_A_const ? register_3_q : 8'bz;  // Controlled_Buffer controlled_buffer_7
  Pull_Resistor pull_resistor_2 (.node(Ctrl_A_const));
  Button button_2 (.out(button_2_out));
  buf or_4 (reset, button_2_out);  // OR_Gate
  and and_4 (and_4_out, ~por_1_out, por_2_out);  // AND_Gate
  LedBar #(.matrixcols(16)) ledbar_1 (
    .led0(PC_q[15]), .led1(PC_q[14]), .led2(PC_q[13]), .led3(PC_q[12]), .led4(PC_q[11]), .led5(PC_q[10]),
    .led6(PC_q[9]), .led7(PC_q[8]), .led8(PC_q[7]), .led9(PC_q[6]), .led10(PC_q[5]), .led11(PC_q[4]),
    .led12(PC_q[3]), .led13(PC_q[2]), .led14(PC_q[1]), .led15(PC_q[0]));
  assign Xfer_BUS = Ctrl_PC_A_Xfer_BUS ? PC_q : 16'bz;  // Controlled_Buffer controlled_buffer_8
  assign Address_BUS = Ctrl_PC_A_addr_BUS ? PC_q : 16'bz;  // Controlled_Buffer controlled_buffer_9
  Register #(.width(16)) PC (.D(counter_1_q), .en(clk), .clk(clk), .Q(PC_q), .clr(reset));
  LedBar #(.matrixcols(16)) ledbar_2 (
    .led0(register_4_q[15]), .led1(register_4_q[14]), .led2(register_4_q[13]), .led3(register_4_q[12]),
    .led4(register_4_q[11]), .led5(register_4_q[10]), .led6(register_4_q[9]), .led7(register_4_q[8]),
    .led8(register_4_q[7]), .led9(register_4_q[6]), .led10(register_4_q[5]), .led11(register_4_q[4]),
    .led12(register_4_q[3]), .led13(register_4_q[2]), .led14(register_4_q[1]), .led15(register_4_q[0]));
  assign Xfer_BUS = NIL ? register_4_q : 16'bz;  // Controlled_Buffer controlled_buffer_10
  assign Address_BUS = NIL ? register_4_q : 16'bz;  // Controlled_Buffer controlled_buffer_11
  Register #(.width(16)) register_4 (.D(counter_2_q), .en(clk), .clk(clk), .Q(register_4_q), .clr(reset));
  POR #(.PorHighDuration(1)) por_1 (.out(por_1_out));
  POR por_2 (.out(por_2_out));
  Register register_5 (.D(MAIN_BUS), .en(GPR_C_write), .clk(clk), .Q(register_5_q), .clr(reset));
  Register register_6 (.D(MAIN_BUS), .en(GPR_D_write), .clk(clk), .Q(register_6_q), .clr(reset));
  assign MAIN_BUS = GPR_C_MAIN_out ? register_5_q : 8'bz;  // Controlled_Buffer controlled_buffer_12
  assign ALU_LEFT = GPR_C_ALU_LEFT_out ? register_5_q : 8'bz;  // Controlled_Buffer controlled_buffer_13
  assign ALU_RIGHT = GPR_C_ALU_RIGHT_out ? register_5_q : 8'bz;  // Controlled_Buffer controlled_buffer_14
  assign MAIN_BUS = GPR_D_MAIN_out ? register_6_q : 8'bz;  // Controlled_Buffer controlled_buffer_15
  assign ALU_LEFT = GPR_D_ALU_LEFT_out ? register_6_q : 8'bz;  // Controlled_Buffer controlled_buffer_16
  assign ALU_RIGHT = GPR_D_ALU_RIGHT_out ? register_6_q : 8'bz;  // Controlled_Buffer controlled_buffer_17
  or or_5 (or_5_out, PCinc, PCdec);
  or or_6 (or_6_out, NIL, NIL);
  Pull_Resistor pull_resistor_3 (.node(NIL));
  Counter #(.max('hffff), .width(16)) counter_3 (
    .clr(reset), .load(PCload), .up(PCinc), .count(1'b1), .clk(or_5_out), .D(Xfer_BUS), .Q(counter_3_q));  // open: carry
  Counter #(.max('hffff), .width(16)) counter_4 (
    .clr(reset), .load(NIL), .up(NIL), .count(1'b1), .clk(or_6_out), .D(Xfer_BUS), .Q(counter_4_q));  // open: carry
  LedBar #(.matrixcols(16)) ledbar_3 (
    .led0(Address_BUS[15]), .led1(Address_BUS[14]), .led2(Address_BUS[13]), .led3(Address_BUS[12]),
    .led4(Address_BUS[11]), .led5(Address_BUS[10]), .led6(Address_BUS[9]), .led7(Address_BUS[8]),
    .led8(Address_BUS[7]), .led9(Address_BUS[6]), .led10(Address_BUS[5]), .led11(Address_BUS[4]),
    .led12(Address_BUS[3]), .led13(Address_BUS[2]), .led14(Address_BUS[1]), .led15(Address_BUS[0]));
  LedBar #(.matrixcols(16)) ledbar_4 (
    .led0(register_7_q[15]), .led1(register_7_q[14]), .led2(register_7_q[13]), .led3(register_7_q[12]),
    .led4(register_7_q[11]), .led5(register_7_q[10]), .led6(register_7_q[9]), .led7(register_7_q[8]),
    .led8(register_7_q[7]), .led9(register_7_q[6]), .led10(register_7_q[5]), .led11(register_7_q[4]),
    .led12(register_7_q[3]), .led13(register_7_q[2]), .led14(register_7_q[1]), .led15(register_7_q[0]));
  Register #(.width(16)) register_7 (.D(counter_3_q), .en(clk), .clk(clk), .Q(register_7_q), .clr(reset));
  LedBar #(.matrixcols(16)) ledbar_5 (
    .led0(register_8_q[15]), .led1(register_8_q[14]), .led2(register_8_q[13]), .led3(register_8_q[12]),
    .led4(register_8_q[11]), .led5(register_8_q[10]), .led6(register_8_q[9]), .led7(register_8_q[8]),
    .led8(register_8_q[7]), .led9(register_8_q[6]), .led10(register_8_q[5]), .led11(register_8_q[4]),
    .led12(register_8_q[3]), .led13(register_8_q[2]), .led14(register_8_q[1]), .led15(register_8_q[0]));
  Register #(.width(16)) register_8 (.D(counter_4_q), .en(clk), .clk(clk), .Q(register_8_q), .clr(reset));
  LedBar ledbar_6 (
    .led0(Memory_BUS[7]), .led1(Memory_BUS[6]), .led2(Memory_BUS[5]), .led3(Memory_BUS[4]),
    .led4(Memory_BUS[3]), .led5(Memory_BUS[2]), .led6(Memory_BUS[1]), .led7(Memory_BUS[0]));
  Pull_Resistor pull_resistor_4 (.node(Flag_1));
  Pull_Resistor pull_resistor_5 (.node(Flag_2));
  Pull_Resistor pull_resistor_6 (.node(Flag_3));
  Pull_Resistor pull_resistor_7 (.node(Flag_4));
  Pull_Resistor pull_resistor_8 (.node(Flag_5));
  Pull_Resistor pull_resistor_9 (.node(Flag_6));
  Pull_Resistor pull_resistor_10 (.node(Flag_7));
  assign Xfer_BUS = Ctrl_SP_A_Xfer_BUS ? register_7_q : 16'bz;  // Controlled_Buffer controlled_buffer_18
  Controlled_Buffer #(.width(16)) controlled_buffer_19 (.in(register_7_q), .en(Ctrl_SP_A_addr_BUS));  // open: out
  assign Xfer_BUS = NIL ? register_8_q : 16'bz;  // Controlled_Buffer controlled_buffer_20
  assign Address_BUS = NIL ? register_8_q : 16'bz;  // Controlled_Buffer controlled_buffer_21
  Pull_Resistor pull_resistor_11 (.node(Address_BUS));
  Pull_Resistor pull_resistor_12 (.node(Memory_BUS));
  assign controlled_buffer_22_out = not_2_out ? Memory_BUS : 8'bz;  // Controlled_Buffer controlled_buffer_22
  not not_2 (not_2_out, Ctrl_noFetch);
  Pull_Resistor pull_resistor_13 (.node(controlled_buffer_22_out));
  LedBar ledbar_7 (
    .led0(controlled_buffer_22_out[7]), .led1(controlled_buffer_22_out[6]),
    .led2(controlled_buffer_22_out[5]), .led3(controlled_buffer_22_out[4]),
    .led4(controlled_buffer_22_out[3]), .led5(controlled_buffer_22_out[2]),
    .led6(controlled_buffer_22_out[1]), .led7(controlled_buffer_22_out[0]));
  LedBar ledbar_8 (
    .led0(register_10_q[7]), .led1(register_10_q[6]), .led2(register_10_q[5]), .led3(register_10_q[4]),
    .led4(register_10_q[3]), .led5(register_10_q[2]), .led6(register_10_q[1]), .led7(register_10_q[0]));
  ROM #(.addrWidth(15)) rom_1 (
    .addr({Flag_7, Flag_6, Flag_5, Flag_4, Flag_3, Flag_2, Flag_1, controlled_buffer_22_out}),
    .data(rom_1_data));
  LedBar #(.matrixcols(16)) ledbar_9 (
    .led0(Address_BUS[15]), .led1(Address_BUS[14]), .led2(Address_BUS[13]), .led3(Address_BUS[12]),
    .led4(Address_BUS[11]), .led5(Address_BUS[10]), .led6(Address_BUS[9]), .led7(Address_BUS[8]),
    .led8(Address_BUS[7]), .led9(Address_BUS[6]), .led10(Address_BUS[5]), .led11(Address_BUS[4]),
    .led12(Address_BUS[3]), .led13(Address_BUS[2]), .led14(Address_BUS[1]), .led15(Address_BUS[0]));
  Hex_Digit_Display #(.decimalPoint("false")) hex_digit_display_1 (.value(Address_BUS[15:12]));
  Hex_Digit_Display #(.decimalPoint("false")) hex_digit_display_2 (.value(Address_BUS[11:8]));
  Pull_Resistor pull_resistor_14 (.node(RAMwrite));
  LedBar ledbar_10 (
    .led0(register_14_q[7]), .led1(register_14_q[6]), .led2(register_14_q[5]), .led3(register_14_q[4]),
    .led4(register_14_q[3]), .led5(register_14_q[2]), .led6(register_14_q[1]), .led7(register_14_q[0]));
  Hex_Digit_Display #(.decimalPoint("false")) hex_digit_display_3 (.value(Address_BUS[7:4]));
  Hex_Digit_Display #(.decimalPoint("false")) hex_digit_display_4 (.value(Address_BUS[3:0]));
  RAM #(.addrWidth(16), .asyncread("true"), .\type ("nonvolatile")) ram_1 (
    .addr(Address_BUS), .oe(1'b1), .clk(clk), .din(Memory_BUS), .dout(Memory_BUS));  // open: we
  Register #(.width(16)) register_9 (
    .D({rom_1_data, rom_2_data}), .en(clk), .clk(clk), .Q({register_9_q, Ctrl_L_const, Ctrl_noFetch}));  // open: clr
  LedBar #(.matrixcols(16)) ledbar_11 (
    .led0(register_9_q[15]), .led1(register_9_q[14]), .led2(register_9_q[13]), .led3(register_9_q[12]),
    .led4(register_9_q[11]), .led5(register_9_q[10]), .led6(register_9_q[9]), .led7(register_9_q[8]),
    .led8(register_9_q[7]), .led9(register_9_q[6]), .led10(register_9_q[5]), .led11(register_9_q[4]),
    .led12(register_9_q[3]), .led13(register_9_q[2]), .led14(Ctrl_L_const), .led15(Ctrl_noFetch));
  LedBar ledbar_12 (
    .led0(Memory_BUS[7]), .led1(Memory_BUS[6]), .led2(Memory_BUS[5]), .led3(Memory_BUS[4]),
    .led4(Memory_BUS[3]), .led5(Memory_BUS[2]), .led6(Memory_BUS[1]), .led7(Memory_BUS[0]));
  Hex_Digit_Display #(.decimalPoint("false")) hex_digit_display_5 (.value(Memory_BUS[7:4]));
  ROM #(.addrWidth(15)) rom_2 (
    .addr({Flag_7, Flag_6, Flag_5, Flag_4, Flag_3, Flag_2, Flag_1, controlled_buffer_22_out}),
    .data(rom_2_data));
  Hex_Digit_Display #(.decimalPoint("false")) hex_digit_display_6 (.value(Memory_BUS[3:0]));
  Pull_Resistor pull_resistor_15 (.node(Memory_BUS));
  assign controlled_buffer_23_out = Ctrl_noFetch ? clk : 1'bz;  // Controlled_Buffer controlled_buffer_23
  Register register_10 (.D(controlled_buffer_22_out), .en(clk), .clk(clk), .Q(register_10_q), .clr(reset));
  not not_3 (not_3_out, controlled_buffer_23_out);
  or or_7 (Ctrl_PC_A_addr_BUS, not_3_out, controlled_buffer_23_out);
  Pull_Resistor pull_resistor_16 (.node(controlled_buffer_23_out));
  ROM #(.addrWidth(15)) rom_3 (
    .addr({Flag_7, Flag_6, Flag_5, Flag_4, Flag_3, Flag_2, Flag_1, register_10_q}), .data(rom_3_data));
  Register register_11 (.D(undriven), .en(Ctrl_Xfer_L_L), .clk(clk), .Q(register_11_q), .clr(reset));
  Register #(.width(16)) register_12 (
    .D({rom_3_data, rom_4_data}), .en(clk), .clk(clk), .Q({register_12_q, Ctrl_A_const, Ctrl_GPR_L}));  // open: clr
  LedBar #(.matrixcols(16)) ledbar_13 (
    .led0(register_12_q[15]), .led1(register_12_q[14]), .led2(register_12_q[13]), .led3(register_12_q[12]),
    .led4(register_12_q[11]), .led5(register_12_q[10]), .led6(register_12_q[9]), .led7(register_12_q[8]),
    .led8(register_12_q[7]), .led9(register_12_q[6]), .led10(register_12_q[5]), .led11(register_12_q[4]),
    .led12(Ctrl_A_const), .led13(Ctrl_GPR_L[2]), .led14(Ctrl_GPR_L[1]), .led15(Ctrl_GPR_L[0]));
  Register register_13 (.D(undriven_2), .en(Ctrl_Xfer_R_L), .clk(clk), .Q(register_13_q), .clr(reset));
  ROM #(.addrWidth(15)) rom_4 (
    .addr({Flag_7, Flag_6, Flag_5, Flag_4, Flag_3, Flag_2, Flag_1, register_10_q}), .data(rom_4_data));
  assign controlled_buffer_24_out = Ctrl_Xfer_A_MAIN_BUS_R ? register_13_q : 8'bz;  // Controlled_Buffer controlled_buffer_24
  assign controlled_buffer_24_out = Ctrl_Xfer_A_MAIN_BUS_L ? register_11_q : 8'bz;  // Controlled_Buffer controlled_buffer_25
  assign controlled_buffer_26_out = Ctrl_Xfer_A_Xfer_BUS ? {register_11_q, register_13_q} : 16'bz;  // Controlled_Buffer controlled_buffer_26
  assign controlled_buffer_27_out = Ctrl_Xfer_A_Addr_BUS ? {register_11_q, register_13_q} : 16'bz;  // Controlled_Buffer controlled_buffer_27
  Register register_14 (.D(register_10_q), .en(clk), .clk(clk), .Q(register_14_q), .clr(reset));
  Register register_15 (.D(register_14_q), .en(clk_inv), .clk(clk_inv), .Q(register_15_q), .clr(reset));
  LedBar ledbar_14 (
    .led0(register_15_q[7]), .led1(register_15_q[6]), .led2(register_15_q[5]), .led3(register_15_q[4]),
    .led4(register_15_q[3]), .led5(register_15_q[2]), .led6(register_15_q[1]), .led7(register_15_q[0]));
  ROM #(.addrWidth(15)) rom_5 (
    .addr({Flag_7, Flag_6, Flag_5, Flag_4, Flag_3, Flag_2, Flag_1, register_15_q}), .data(rom_5_data));
  LedBar #(.matrixcols(16)) ledbar_15 (
    .led0(rom_5_data[7]), .led1(rom_5_data[6]), .led2(rom_5_data[5]), .led3(rom_5_data[4]),
    .led4(rom_5_data[3]), .led5(rom_5_data[2]), .led6(rom_5_data[1]), .led7(rom_5_data[0]),
    .led8(rom_6_data[7]), .led9(rom_6_data[6]), .led10(rom_6_data[5]), .led11(rom_6_data[4]),
    .led12(rom_6_data[3]), .led13(rom_6_data[2]), .led14(rom_6_data[1]), .led15(rom_6_data[0]));
  ROM #(.addrWidth(15)) rom_6 (
    .addr({Flag_7, Flag_6, Flag_5, Flag_4, Flag_3, Flag_2, Flag_1, register_15_q}), .data(rom_6_data));
  Pull_Resistor pull_resistor_17 (.node(Ctrl_GPR_ALU_R));
  Pull_Resistor pull_resistor_18 (.node(Ctrl_GPR_ALU_L));
  Decoder #(.select(3)) decoder_1 (
    .out1(GPR_A_ALU_RIGHT_out), .out2(GPR_B_ALU_RIGHT_out), .out3(GPR_C_ALU_RIGHT_out),
    .out4(GPR_D_ALU_RIGHT_out), .sel(Ctrl_GPR_ALU_L));  // open: out0, out5, out6, out7, en
  Pull_Resistor pull_resistor_19 (.node(Ctrl_GPR_L));
  Decoder #(.select(3)) decoder_2 (
    .out1(GPR_A_ALU_LEFT_out), .out2(GPR_B_ALU_LEFT_out), .out3(GPR_C_ALU_LEFT_out),
    .out4(GPR_D_ALU_LEFT_out), .sel(Ctrl_GPR_ALU_R));  // open: out0, out5, out6, out7, en
  Pull_Resistor pull_resistor_20 (.node(Ctrl_GPR_A));
  Decoder #(.select(3)) decoder_3 (
    .out1(GPR_A_write), .out2(GPR_B_write), .out3(GPR_C_write), .out4(GPR_D_write), .sel(Ctrl_GPR_L));  // open: out0, out5, out6, out7, en
  Decoder #(.select(3)) decoder_4 (
    .out1(GPR_A_MAIN_out), .out2(GPR_B_MAIN_out), .out3(GPR_C_MAIN_out), .out4(GPR_D_MAIN_out),
    .sel(Ctrl_GPR_A));  // open: out0, out5, out6, out7, en

  // Notes on the sheet:
  //   GPR_A
  //   GPR_B
  //   Constant Reg
  //   Program Counter
  //   16BIT Counter Reg 1
  //   GPR_C
  //   GPR_D
  //   Stack Pointer
  //   16BIT Counter Reg 2
  //   Stage #0
  //   Stage #1
  //   Stage #2
  //   contents of rom_2 (hex, n*v repeats v):
  //   0 1
  //   contents of rom_4 (hex, n*v repeats v):
  //   0 11
  //   Stage #2
endmodule
