// Logisim project Dragon_4.circ as structural Verilog: 1 circuit, main circuit main
module main (
  input  in_1,
  input  manuel_write,
  input  manuel_write_enable
);

  wire and_1_out, and_2_out, and_3_out, and_4_out, and_5_out, and_6_out, and_7_out, and_9_out, and_10_out,
       and_11_out, and_12_out, and_13_out, and_14_out, and_15_out, and_16_out, and_17_out, and_18_out,
       button_1_out, button_2_out, clk, clk_inv, clock_1_out, Ctrl_A_const, Ctrl_ALU_A, Ctrl_CREG1_A_addr,
       Ctrl_CREG1_A_Xfer, Ctrl_CREG1_dec, Ctrl_CREG1_inc, Ctrl_CREG1_L_Xfer, Ctrl_flags, Ctrl_hlt, Ctrl_IR_L,
       Ctrl_L_const, Ctrl_mem_A_MAIN_BUS, Ctrl_PC_A_addr_BUS, Ctrl_PC_A_Xfer_BUS, Ctrl_PC_dec, Ctrl_PC_inc,
       Ctrl_PC_L_Xfer, Ctrl_RAM_L, Ctrl_rst_Step, Ctrl_SP_A_addr_BUS, Ctrl_SP_A_Xfer_BUS, Ctrl_SP_dec,
       Ctrl_SP_inc, Ctrl_SP_L_Xfer, Ctrl_Xfer_A_addr, Ctrl_Xfer_A_Xfer, Ctrl_Xfer_L_Xfer,
       Ctrl_XferL_A_MAIN_BUS, Ctrl_XferL_L_MAIN_BUS, Ctrl_XferR_A_MAIN_BUS, Ctrl_XferR_L_MAIN_BUS,
       decoder_1_out0, decoder_1_out1, decoder_1_out2, decoder_1_out3, decoder_1_out4, decoder_1_out5,
       decoder_1_out6, decoder_1_out7, decoder_1_out8, decoder_1_out9, decoder_1_out10, decoder_1_out11,
       decoder_1_out12, decoder_1_out13, decoder_1_out14, decoder_1_out15, decoder_7_out10, decoder_8_out11,
       GPR_A_ALU_LEFT_out, GPR_A_ALU_RIGHT_out, GPR_A_MAIN_out, GPR_A_write, GPR_B_ALU_LEFT_out,
       GPR_B_ALU_RIGHT_out, GPR_B_MAIN_out, GPR_B_write, GPR_C_ALU_LEFT_out, GPR_C_ALU_RIGHT_out,
       GPR_C_MAIN_out, GPR_C_write, GPR_D_ALU_LEFT_out, GPR_D_ALU_RIGHT_out, GPR_D_MAIN_out, GPR_D_write,
       GPR_X_ALU_LEFT_out, GPR_X_ALU_RIGHT_out, GPR_X_MAIN_out, GPR_X_write, nand_3_out, nand_4_out,
       nand_5_out, nand_6_out, nand_7_out, NIL, nor_1_out, nor_2_out, not_1_out, not_2_out, not_4_out,
       not_5_out, not_6_out, not_7_out, not_8_out, not_9_out, not_10_out, not_11_out, not_12_out, not_13_out,
       not_14_out, not_15_out, not_16_out, not_17_out, not_18_out, not_19_out, not_20_out, not_21_out,
       not_22_out, not_23_out, not_24_out, not_25_out, not_26_out, not_27_out, not_28_out, or_1_out,
       or_2_out, or_3_out, or_5_out, or_7_out, or_8_out, or_9_out, or_10_out, or_11_out, or_14_out,
       or_15_out, or_16_out, or_17_out, or_19_out, or_20_out, or_21_out, or_22_out, or_23_out, por_1_out,
       por_2_out, reset;
  wire [0:0] pull_resistor_10_node;
  wire [1:0] adder_1_cout, Ctrl_CREG_dec, Ctrl_CREG_inc;
  wire [2:0] Ctrl_CREG_A_addr, Ctrl_GPR_A_ALU_L, Ctrl_GPR_A_ALU_R, flags;
  wire [3:0] controlled_buffer_40_out, controlled_buffer_40_out_2, Ctrl_ALU_OP, Ctrl_REG_A, Ctrl_REG_L,
       ram_3_data, ram_3_data_2;
  wire [3:3] Step_q;
  wire [5:4] rom_4_data;
  wire [7:0] adder_1_out, ALU_LEFT, ALU_RIGHT, and_8_out, bit_extender_1_out, controlled_buffer_29_out,
       controlled_buffer_49_out, Instruction_Reg_q, MAIN_BUS, Memory_BUS, nand_1_out, nor_3_out, or_12_out,
       or_13_out, or_18_out, ram_1_data, ram_2_data, register_1_q, register_2_q, register_3_q, register_4_q,
       register_5_q, register_6_q, register_10_q, register_11_q, register_12_q, xnor_1_out, xor_1_out,
       xor_2_out;
  wire [7:6] rom_3_data;
  wire [7:7] pull_resistor_11_node;
  wire [14:0] Step_q_2;
  wire [15:0] Address_BUS, counter_1_q, counter_2_q, counter_3_q, counter_4_q, PC_q, register_7_q,
       register_8_q, register_9_q, Xfer_BUS;

  LED led_1 (.in(clk));
  Button button_1 (.out(button_1_out));
  Pull_Resistor pull_resistor_1 (.node(MAIN_BUS));
  Pull_Resistor pull_resistor_2 (.node(Address_BUS));
  Pull_Resistor pull_resistor_3 (.node(Xfer_BUS));
  Pull_Resistor pull_resistor_4 (.node(ALU_LEFT));
  Pull_Resistor pull_resistor_5 (.node(ALU_RIGHT));
  Register register_1 (.D(MAIN_BUS), .en(GPR_A_write), .clk(clk_inv), .Q(register_1_q), .clr(reset));
  Register register_2 (.D(MAIN_BUS), .en(GPR_B_write), .clk(clk_inv), .Q(register_2_q), .clr(reset));
  Register register_3 (.D(Memory_BUS), .en(Ctrl_L_const), .clk(clk_inv), .Q(register_3_q), .clr(reset));
  // Digital_Oscilloscope digital_oscilloscope_1: pin names not known; wires that end beside it: Ctrl_PC_L_Xfer, clk, clk_inv, Ctrl_PC_inc
  Counter #(.max('hffff), .width(16)) counter_1 (
    .clr(reset), .load(Ctrl_PC_L_Xfer), .up(Ctrl_PC_inc), .count(1'b1), .clk(and_1_out), .D(Xfer_BUS),
    .Q(counter_1_q));  // open: carry
  or or_1 (or_1_out, Ctrl_PC_inc, Ctrl_PC_dec);
  and and_1 (and_1_out, or_1_out, clk_inv);
  not not_1 (not_1_out, Ctrl_PC_inc);
  or or_2 (or_2_out, not_1_out, clk_inv);
  not not_2 (not_2_out, Ctrl_PC_dec);
  or or_3 (or_3_out, not_2_out, clk_inv);
  Clock clock_1 (.out(clock_1_out));
  and and_2 (and_2_out, button_1_out, in_1);
  and and_3 (and_3_out, ~in_1, clock_1_out);  // AND_Gate
  or or_4 (clk, and_2_out, and_3_out);
  not not_3 (clk_inv, clk);
  assign MAIN_BUS = GPR_A_MAIN_out ? register_1_q : 8'bz;  // Controlled_Buffer controlled_buffer_1
  assign ALU_LEFT = GPR_A_ALU_LEFT_out ? register_1_q : 8'bz;  // Controlled_Buffer controlled_buffer_2
  assign ALU_RIGHT = GPR_A_ALU_RIGHT_out ? register_1_q : 8'bz;  // Controlled_Buffer controlled_buffer_3
  assign MAIN_BUS = GPR_B_MAIN_out ? register_2_q : 8'bz;  // Controlled_Buffer controlled_buffer_4
  assign ALU_LEFT = GPR_B_ALU_LEFT_out ? register_2_q : 8'bz;  // Controlled_Buffer controlled_buffer_5
  assign ALU_RIGHT = GPR_B_ALU_RIGHT_out ? register_2_q : 8'bz;  // Controlled_Buffer controlled_buffer_6
  assign MAIN_BUS = Ctrl_A_const ? register_3_q : 8'bz;  // Controlled_Buffer controlled_buffer_7
  or or_5 (or_5_out, Ctrl_CREG1_L_Xfer, Ctrl_CREG1_inc, Ctrl_CREG1_dec);
  Button button_2 (.out(button_2_out));
  or or_6 (reset, button_2_out, and_5_out);
  Counter #(.max('hffff), .width(16)) counter_2 (
    .clr(reset), .load(Ctrl_CREG1_L_Xfer), .up(Ctrl_CREG1_inc), .count(1'b1), .clk(and_4_out), .D(Xfer_BUS),
    .Q(counter_2_q));  // open: carry
  and and_4 (and_4_out, or_5_out, clk_inv);
  and and_5 (and_5_out, ~por_1_out, por_2_out);  // AND_Gate
  LedBar #(.matrixcols(16)) ledbar_1 (
    .led0(PC_q[15]), .led1(PC_q[14]), .led2(PC_q[13]), .led3(PC_q[12]), .led4(PC_q[11]), .led5(PC_q[10]),
    .led6(PC_q[9]), .led7(PC_q[8]), .led8(PC_q[7]), .led9(PC_q[6]), .led10(PC_q[5]), .led11(PC_q[4]),
    .led12(PC_q[3]), .led13(PC_q[2]), .led14(PC_q[1]), .led15(PC_q[0]));
  Register #(.width(16)) PC (.D(counter_1_q), .en(clk), .clk(clk), .Q(PC_q), .clr(reset));
  POR #(.PorHighDuration(1)) por_1 (.out(por_1_out));
  POR por_2 (.out(por_2_out));
  Register register_4 (.D(MAIN_BUS), .en(GPR_C_write), .clk(clk_inv), .Q(register_4_q), .clr(reset));
  Register register_5 (.D(MAIN_BUS), .en(GPR_D_write), .clk(clk_inv), .Q(register_5_q), .clr(reset));
  Register register_6 (.D(MAIN_BUS), .en(GPR_X_write), .clk(clk_inv), .Q(register_6_q), .clr(reset));
  assign Xfer_BUS = Ctrl_PC_A_Xfer_BUS ? PC_q : 16'bz;  // Controlled_Buffer controlled_buffer_8
  assign Address_BUS = Ctrl_PC_A_addr_BUS ? PC_q : 16'bz;  // Controlled_Buffer controlled_buffer_9
  LedBar #(.matrixcols(16)) ledbar_2 (
    .led0(register_7_q[15]), .led1(register_7_q[14]), .led2(register_7_q[13]), .led3(register_7_q[12]),
    .led4(register_7_q[11]), .led5(register_7_q[10]), .led6(register_7_q[9]), .led7(register_7_q[8]),
    .led8(register_7_q[7]), .led9(register_7_q[6]), .led10(register_7_q[5]), .led11(register_7_q[4]),
    .led12(register_7_q[3]), .led13(register_7_q[2]), .led14(register_7_q[1]), .led15(register_7_q[0]));
  Register #(.width(16)) register_7 (.D(counter_2_q), .en(clk), .clk(clk), .Q(register_7_q), .clr(reset));
  assign MAIN_BUS = GPR_C_MAIN_out ? register_4_q : 8'bz;  // Controlled_Buffer controlled_buffer_10
  assign ALU_LEFT = GPR_C_ALU_LEFT_out ? register_4_q : 8'bz;  // Controlled_Buffer controlled_buffer_11
  assign ALU_RIGHT = GPR_C_ALU_RIGHT_out ? register_4_q : 8'bz;  // Controlled_Buffer controlled_buffer_12
  assign MAIN_BUS = GPR_D_MAIN_out ? register_5_q : 8'bz;  // Controlled_Buffer controlled_buffer_13
  assign ALU_LEFT = GPR_D_ALU_LEFT_out ? register_5_q : 8'bz;  // Controlled_Buffer controlled_buffer_14
  assign ALU_RIGHT = GPR_D_ALU_RIGHT_out ? register_5_q : 8'bz;  // Controlled_Buffer controlled_buffer_15
  assign MAIN_BUS = GPR_X_MAIN_out ? register_6_q : 8'bz;  // Controlled_Buffer controlled_buffer_16
  assign ALU_LEFT = GPR_X_ALU_LEFT_out ? register_6_q : 8'bz;  // Controlled_Buffer controlled_buffer_17
  assign ALU_RIGHT = GPR_X_ALU_RIGHT_out ? register_6_q : 8'bz;  // Controlled_Buffer controlled_buffer_18
  assign Xfer_BUS = Ctrl_CREG1_A_Xfer ? register_7_q : 16'bz;  // Controlled_Buffer controlled_buffer_19
  assign Address_BUS = Ctrl_CREG1_A_addr ? register_7_q : 16'bz;  // Controlled_Buffer controlled_buffer_20
  Pull_Resistor pull_resistor_6 (.node(NIL));
  or or_7 (or_7_out, Ctrl_rst_Step, Step_q[3]);
  Counter #(.max('hffff), .width(16)) counter_3 (
    .clr(reset), .load(Ctrl_SP_L_Xfer), .up(Ctrl_SP_inc), .count(1'b1), .clk(and_6_out), .D(Xfer_BUS),
    .Q(counter_3_q));  // open: carry
  or or_8 (or_8_out, Ctrl_SP_inc, Ctrl_SP_dec);
  and and_6 (and_6_out, or_8_out, clk_inv);
  Counter #(.max('hf), .width(4)) Step (
    .clr(or_9_out), .load(1'b0), .up(1'b1), .count(clk), .clk(clk), .Q({Step_q[3], Step_q_2[2:0]}));  // open: D, carry
  or or_9 (or_9_out, reset, or_7_out);
  not not_4 (not_4_out, Ctrl_PC_dec);
  nor nor_1 (nor_1_out, not_4_out, clk);
  LedBar #(.matrixcols(16)) ledbar_3 (
    .led0(Address_BUS[15]), .led1(Address_BUS[14]), .led2(Address_BUS[13]), .led3(Address_BUS[12]),
    .led4(Address_BUS[11]), .led5(Address_BUS[10]), .led6(Address_BUS[9]), .led7(Address_BUS[8]),
    .led8(Address_BUS[7]), .led9(Address_BUS[6]), .led10(Address_BUS[5]), .led11(Address_BUS[4]),
    .led12(Address_BUS[3]), .led13(Address_BUS[2]), .led14(Address_BUS[1]), .led15(Address_BUS[0]));
  LedBar #(.matrixcols(16)) ledbar_4 (
    .led0(register_8_q[15]), .led1(register_8_q[14]), .led2(register_8_q[13]), .led3(register_8_q[12]),
    .led4(register_8_q[11]), .led5(register_8_q[10]), .led6(register_8_q[9]), .led7(register_8_q[8]),
    .led8(register_8_q[7]), .led9(register_8_q[6]), .led10(register_8_q[5]), .led11(register_8_q[4]),
    .led12(register_8_q[3]), .led13(register_8_q[2]), .led14(register_8_q[1]), .led15(register_8_q[0]));
  Register #(.width(16)) register_8 (.D(counter_3_q), .en(clk), .clk(clk), .Q(register_8_q), .clr(reset));
  not not_5 (not_5_out, Ctrl_PC_inc);
  not not_6 (not_6_out, Ctrl_PC_L_Xfer);
  nor nor_2 (nor_2_out, not_5_out, clk);
  LedBar ledbar_5 (
    .led0(Memory_BUS[7]), .led1(Memory_BUS[6]), .led2(Memory_BUS[5]), .led3(Memory_BUS[4]),
    .led4(Memory_BUS[3]), .led5(Memory_BUS[2]), .led6(Memory_BUS[1]), .led7(Memory_BUS[0]));
  assign Xfer_BUS = Ctrl_SP_A_Xfer_BUS ? register_8_q : 16'bz;  // Controlled_Buffer controlled_buffer_21
  assign Address_BUS = Ctrl_SP_A_addr_BUS ? register_8_q : 16'bz;  // Controlled_Buffer controlled_buffer_22
  or or_10 (or_10_out, not_6_out, clk);
  and and_7 (and_7_out, ~nor_1_out, nor_2_out);  // AND_Gate
  Pull_Resistor pull_resistor_7 (.node(Address_BUS));
  Pull_Resistor pull_resistor_8 (.node(Memory_BUS));
  Counter #(.max('hffff), .width(16)) counter_4 (
    .clr(reset), .load(not_7_out), .up(and_7_out), .count(1'b1), .clk(or_11_out), .D(Xfer_BUS),
    .Q(counter_4_q));  // open: carry
  not not_7 (not_7_out, or_10_out);
  or or_11 (or_11_out, ~or_10_out, nor_2_out, nor_1_out);  // OR_Gate
  Register Instruction_Reg (.D(Memory_BUS), .en(Ctrl_IR_L), .clk(clk), .Q(Instruction_Reg_q), .clr(reset));
  Pull_Resistor pull_resistor_9 (.node(Step_q_2[14]));
  LedBar #(.matrixcols(16)) ledbar_6 (
    .led0(register_9_q[15]), .led1(register_9_q[14]), .led2(register_9_q[13]), .led3(register_9_q[12]),
    .led4(register_9_q[11]), .led5(register_9_q[10]), .led6(register_9_q[9]), .led7(register_9_q[8]),
    .led8(register_9_q[7]), .led9(register_9_q[6]), .led10(register_9_q[5]), .led11(register_9_q[4]),
    .led12(register_9_q[3]), .led13(register_9_q[2]), .led14(register_9_q[1]), .led15(register_9_q[0]));
  Register #(.width(16)) register_9 (.D(counter_4_q), .en(clk), .clk(clk), .Q(register_9_q), .clr(reset));
  ROM #(.addrWidth(15)) rom_1 (
    .addr({Step_q_2[14], flags, Instruction_Reg_q, Step_q_2[2:0]}), .data({Ctrl_REG_L, Ctrl_REG_A}));
  ROM #(.addrWidth(15)) rom_2 (
    .addr({Step_q_2[14], flags, Instruction_Reg_q, Step_q_2[2:0]}),
    .data({Ctrl_flags, Ctrl_CREG_dec, Ctrl_CREG_inc, Ctrl_CREG_A_addr}));
  ROM #(.addrWidth(15)) rom_3 (
    .addr({Step_q_2[14], flags, Instruction_Reg_q, Step_q_2[2:0]}),
    .data({rom_3_data, Ctrl_GPR_A_ALU_L, Ctrl_GPR_A_ALU_R}));
  ROM #(.addrWidth(15)) rom_4 (
    .addr({Step_q_2[14], flags, Instruction_Reg_q, Step_q_2[2:0]}),
    .data({Ctrl_rst_Step, Ctrl_hlt, rom_4_data, Ctrl_ALU_OP}));
  LedBar ledbar_7 (
    .led0(ALU_RIGHT[7]), .led1(ALU_RIGHT[6]), .led2(ALU_RIGHT[5]), .led3(ALU_RIGHT[4]), .led4(ALU_RIGHT[3]),
    .led5(ALU_RIGHT[2]), .led6(ALU_RIGHT[1]), .led7(ALU_RIGHT[0]));
  LedBar ledbar_8 (
    .led0(ALU_LEFT[7]), .led1(ALU_LEFT[6]), .led2(ALU_LEFT[5]), .led3(ALU_LEFT[4]), .led4(ALU_LEFT[3]),
    .led5(ALU_LEFT[2]), .led6(ALU_LEFT[1]), .led7(ALU_LEFT[0]));
  assign Xfer_BUS = Ctrl_PC_A_Xfer_BUS ? register_9_q : 16'bz;  // Controlled_Buffer controlled_buffer_23
  assign Address_BUS = Ctrl_PC_A_addr_BUS ? register_9_q : 16'bz;  // Controlled_Buffer controlled_buffer_24
  assign or_12_out = MAIN_BUS | Xfer_BUS[7:0];  // OR_Gate or_12, 8 bits wide
  assign or_13_out = MAIN_BUS | Xfer_BUS[15:8];  // OR_Gate or_13, 8 bits wide
  Register register_10 (.D(or_13_out), .en(or_14_out), .clk(clk_inv), .Q(register_10_q), .clr(reset));
  or or_14 (or_14_out, Ctrl_XferL_L_MAIN_BUS, Ctrl_Xfer_L_Xfer);
  or or_15 (or_15_out, Ctrl_Xfer_L_Xfer, Ctrl_XferR_L_MAIN_BUS);
  LedBar #(.matrixcols(4)) ledbar_9 (
    .led0(Ctrl_ALU_OP[3]), .led1(Ctrl_ALU_OP[2]), .led2(Ctrl_ALU_OP[1]), .led3(Ctrl_ALU_OP[0]));
  Decoder #(.select(4)) decoder_1 (
    .out0(decoder_1_out0), .out1(decoder_1_out1), .out2(decoder_1_out2), .out3(decoder_1_out3),
    .out4(decoder_1_out4), .out5(decoder_1_out5), .out6(decoder_1_out6), .out7(decoder_1_out7),
    .out8(decoder_1_out8), .out9(decoder_1_out9), .out10(decoder_1_out10), .out11(decoder_1_out11),
    .out12(decoder_1_out12), .out13(decoder_1_out13), .out14(decoder_1_out14), .out15(decoder_1_out15),
    .sel(Ctrl_ALU_OP));  // open: en
  Register register_11 (.D(or_12_out), .en(or_15_out), .clk(clk_inv), .Q(register_11_q), .clr(reset));
  assign MAIN_BUS = Ctrl_XferR_A_MAIN_BUS ? register_11_q : 8'bz;  // Controlled_Buffer controlled_buffer_25
  assign MAIN_BUS = Ctrl_XferL_A_MAIN_BUS ? register_10_q : 8'bz;  // Controlled_Buffer controlled_buffer_26
  assign Xfer_BUS = Ctrl_Xfer_A_Xfer ? {register_10_q, register_11_q} : 16'bz;  // Controlled_Buffer controlled_buffer_27
  assign Address_BUS = Ctrl_Xfer_A_addr ? {register_10_q, register_11_q} : 16'bz;  // Controlled_Buffer controlled_buffer_28
  or or_16 (or_16_out, decoder_1_out14, decoder_1_out7, decoder_1_out3, decoder_1_out2, decoder_1_out1, decoder_1_out0, decoder_1_out15);
  assign bit_extender_1_out = {{7{or_17_out}}, or_17_out};  // Bit_Extender bit_extender_1
  or or_17 (or_17_out, decoder_1_out2, decoder_1_out3, decoder_1_out14, decoder_1_out15);
  Pull_Resistor pull_resistor_10 (.node(pull_resistor_10_node[0]));
  Pull_Resistor pull_resistor_11 (.node(pull_resistor_11_node[7]));
  assign and_8_out = ALU_RIGHT & ALU_LEFT;  // AND_Gate and_8, 8 bits wide
  assign or_18_out = ALU_RIGHT | ALU_LEFT;  // OR_Gate or_18, 8 bits wide
  and and_9 (and_9_out, decoder_1_out1, flags[0]);
  or or_19 (or_19_out, decoder_1_out14, decoder_1_out7, and_9_out, decoder_1_out2, and_10_out);
  assign xor_1_out = ALU_LEFT ^ bit_extender_1_out;  // XOR_Gate xor_1, 8 bits wide
  assign controlled_buffer_29_out = decoder_1_out4 ? {ALU_RIGHT[6:0], pull_resistor_10_node[0]} : 8'bz;  // Controlled_Buffer controlled_buffer_29
  assign controlled_buffer_29_out = decoder_1_out5 ? {{2{ALU_RIGHT[7]}}, ALU_RIGHT[6:1]} : 8'bz;  // Controlled_Buffer controlled_buffer_30
  assign controlled_buffer_29_out = decoder_1_out6 ? {pull_resistor_11_node[7], ALU_RIGHT[7:1]} : 8'bz;  // Controlled_Buffer controlled_buffer_31
  assign controlled_buffer_29_out = decoder_1_out8 ? and_8_out : 8'bz;  // Controlled_Buffer controlled_buffer_32
  assign controlled_buffer_29_out = decoder_1_out9 ? or_18_out : 8'bz;  // Controlled_Buffer controlled_buffer_33
  assign xor_2_out = ALU_RIGHT ^ ALU_LEFT;  // XOR_Gate xor_2, 8 bits wide
  assign controlled_buffer_29_out = decoder_1_out10 ? xor_2_out : 8'bz;  // Controlled_Buffer controlled_buffer_34
  assign nand_1_out = ~(ALU_RIGHT & ALU_LEFT);  // NAND_Gate nand_1, 8 bits wide
  assign controlled_buffer_29_out = decoder_1_out11 ? nand_1_out : 8'bz;  // Controlled_Buffer controlled_buffer_35
  assign nor_3_out = ~(ALU_RIGHT | ALU_LEFT);  // NOR_Gate nor_3, 8 bits wide
  assign controlled_buffer_29_out = decoder_1_out12 ? nor_3_out : 8'bz;  // Controlled_Buffer controlled_buffer_36
  assign xnor_1_out = ~(ALU_RIGHT ^ ALU_LEFT);  // XNOR_Gate xnor_1, 8 bits wide
  assign controlled_buffer_29_out = decoder_1_out13 ? xnor_1_out : 8'bz;  // Controlled_Buffer controlled_buffer_37
  Pull_Resistor pull_resistor_12 (.node(Ctrl_GPR_A_ALU_L));
  Decoder #(.select(3)) decoder_2 (
    .out1(GPR_A_ALU_LEFT_out), .out2(GPR_B_ALU_LEFT_out), .out3(GPR_C_ALU_LEFT_out),
    .out4(GPR_D_ALU_LEFT_out), .out5(GPR_X_ALU_LEFT_out), .sel(Ctrl_GPR_A_ALU_L));  // open: out0, out6, out7, en
  and and_10 (and_10_out, decoder_1_out3, flags[0]);
  assign controlled_buffer_29_out = or_16_out ? adder_1_out : 8'bz;  // Controlled_Buffer controlled_buffer_38
  Adder adder_1 (.a(ALU_RIGHT), .b(xor_1_out), .out(adder_1_out), .cin(or_19_out), .cout(adder_1_cout[0]));
  Pull_Resistor pull_resistor_13 (.node(Ctrl_GPR_A_ALU_R));
  Decoder #(.select(3)) decoder_3 (
    .out1(GPR_A_ALU_RIGHT_out), .out2(GPR_B_ALU_RIGHT_out), .out3(GPR_C_ALU_RIGHT_out),
    .out4(GPR_D_ALU_RIGHT_out), .out5(GPR_X_ALU_RIGHT_out), .sel(Ctrl_GPR_A_ALU_R));  // open: out0, out6, out7, en
  nand nand_2 (adder_1_cout[1], controlled_buffer_29_out[7], controlled_buffer_29_out[6], controlled_buffer_29_out[5], controlled_buffer_29_out[4], controlled_buffer_29_out[2], controlled_buffer_29_out[1], controlled_buffer_29_out[0], controlled_buffer_29_out[3]);
  Register register_12 (.D(controlled_buffer_29_out), .en(clk), .clk(clk), .Q(register_12_q), .clr(reset));
  Pull_Resistor pull_resistor_14 (.node(Ctrl_CREG_dec));
  Decoder #(.select(2)) decoder_4 (
    .out1(Ctrl_PC_dec), .out2(Ctrl_SP_dec), .out3(Ctrl_CREG1_dec), .sel(Ctrl_CREG_dec));  // open: out0, en
  Pull_Resistor pull_resistor_15 (.node(Ctrl_CREG_A_addr));
  Decoder #(.select(3)) decoder_5 (
    .out1(Ctrl_PC_A_addr_BUS), .out2(Ctrl_SP_A_addr_BUS), .out3(Ctrl_CREG1_A_addr), .out4(Ctrl_Xfer_A_addr),
    .sel(Ctrl_CREG_A_addr));  // open: out0, out5, out6, out7, en
  Pull_Resistor pull_resistor_16 (.node(Ctrl_CREG_inc));
  Decoder #(.select(2)) decoder_6 (
    .out1(Ctrl_PC_inc), .out2(Ctrl_SP_inc), .out3(Ctrl_CREG1_inc), .sel(Ctrl_CREG_inc));  // open: out0, en
  LedBar ledbar_10 (
    .led0(register_12_q[7]), .led1(register_12_q[6]), .led2(register_12_q[5]), .led3(register_12_q[4]),
    .led4(register_12_q[3]), .led5(register_12_q[2]), .led6(register_12_q[1]), .led7(register_12_q[0]));
  Pull_Resistor pull_resistor_17 (.node(Ctrl_REG_L));
  Decoder #(.select(4)) decoder_7 (
    .out1(GPR_A_write), .out2(GPR_B_write), .out3(GPR_C_write), .out4(GPR_D_write), .out5(GPR_X_write),
    .out6(Ctrl_PC_L_Xfer), .out7(Ctrl_SP_L_Xfer), .out8(Ctrl_CREG1_L_Xfer), .out9(Ctrl_RAM_L),
    .out10(decoder_7_out10), .out11(Ctrl_IR_L), .out12(Ctrl_Xfer_L_Xfer), .out13(Ctrl_XferR_L_MAIN_BUS),
    .out14(Ctrl_XferL_L_MAIN_BUS), .out15(Ctrl_L_const), .sel(Ctrl_REG_L));  // open: out0, en
  assign MAIN_BUS = Ctrl_ALU_A ? register_12_q : 8'bz;  // Controlled_Buffer controlled_buffer_39
  Register #(.width(3)) register_13 (
    .D({controlled_buffer_29_out[7], adder_1_cout}), .en(Ctrl_flags), .clk(clk), .Q(flags), .clr(reset));
  Pull_Resistor pull_resistor_18 (.node(Ctrl_REG_A));
  Decoder #(.select(4)) decoder_8 (
    .out1(GPR_A_MAIN_out), .out2(GPR_B_MAIN_out), .out3(GPR_C_MAIN_out), .out4(GPR_D_MAIN_out),
    .out5(GPR_X_MAIN_out), .out6(Ctrl_PC_A_Xfer_BUS), .out7(Ctrl_SP_A_Xfer_BUS), .out8(Ctrl_CREG1_A_Xfer),
    .out9(Ctrl_ALU_A), .out10(Ctrl_mem_A_MAIN_BUS), .out11(decoder_8_out11), .out12(Ctrl_Xfer_A_Xfer),
    .out13(Ctrl_XferR_A_MAIN_BUS), .out14(Ctrl_XferL_A_MAIN_BUS), .out15(Ctrl_A_const), .sel(Ctrl_REG_A));  // open: out0, en
  LedBar #(.matrixcols(3)) ledbar_11 (.led0(flags[2]), .led1(flags[1]), .led2(flags[0]));
  not not_8 (not_8_out, not_17_out);
  not not_9 (not_9_out, nand_7_out);
  nand nand_3 (nand_3_out, Address_BUS[15], not_8_out);
  nand nand_4 (nand_4_out, not_9_out, Address_BUS[15]);
  RAM #(.addrWidth(15), .asyncread("true"), .databus("bidir"), .\type ("nonvolatile")) ram_1 (
    .addr(Address_BUS[14:0]), .we(and_11_out), .oe(and_12_out), .clk(not_10_out), .data(ram_1_data));
  and and_11 (and_11_out, ~not_11_out, ~nand_4_out);  // AND_Gate
  and and_12 (and_12_out, ~not_11_out, ~nand_3_out);  // AND_Gate
  not not_10 (not_10_out, nand_4_out);
  not not_11 (not_11_out, Address_BUS[15]);
  not not_12 (not_12_out, not_17_out);
  or or_20 (or_20_out, Address_BUS[15], ~not_12_out);  // OR_Gate
  assign {controlled_buffer_40_out_2, controlled_buffer_40_out} = and_12_out ? ram_1_data : 8'bz;  // Controlled_Buffer controlled_buffer_40
  assign ram_1_data = and_11_out ? {controlled_buffer_40_out_2, controlled_buffer_40_out} : 8'bz;  // Controlled_Buffer controlled_buffer_41
  LedBar #(.matrixcols(16)) ledbar_12 (
    .led0(Address_BUS[15]), .led1(Address_BUS[14]), .led2(Address_BUS[13]), .led3(Address_BUS[12]),
    .led4(Address_BUS[11]), .led5(Address_BUS[10]), .led6(Address_BUS[9]), .led7(Address_BUS[8]),
    .led8(Address_BUS[7]), .led9(Address_BUS[6]), .led10(Address_BUS[5]), .led11(Address_BUS[4]),
    .led12(Address_BUS[3]), .led13(Address_BUS[2]), .led14(Address_BUS[1]), .led15(Address_BUS[0]));
  not not_13 (not_13_out, nand_7_out);
  not not_14 (not_14_out, Address_BUS[15]);
  nand nand_5 (nand_5_out, not_13_out, not_14_out);
  Hex_Digit_Display #(.decimalPoint("false")) hex_digit_display_1 (.value(Address_BUS[15:12]));
  Hex_Digit_Display #(.decimalPoint("false")) hex_digit_display_2 (.value(Address_BUS[11:8]));
  RAM #(.addrWidth(15), .asyncread("true"), .databus("bidir"), .\type ("nonvolatile")) ram_2 (
    .addr(Address_BUS[14:0]), .we(and_13_out), .oe(and_14_out), .clk(not_15_out), .data(ram_2_data));
  and and_13 (and_13_out, ~Address_BUS[15], ~nand_5_out);  // AND_Gate
  and and_14 (and_14_out, ~Address_BUS[15], ~or_20_out);  // AND_Gate
  not not_15 (not_15_out, nand_5_out);
  Hex_Digit_Display #(.decimalPoint("false")) hex_digit_display_3 (.value(Address_BUS[7:4]));
  Hex_Digit_Display #(.decimalPoint("false")) hex_digit_display_4 (.value(Address_BUS[3:0]));
  RAM #(.addrWidth(16), .asyncread("true"), .databus("bidir"), .\type ("nonvolatile")) ram_3 (
    .addr(Address_BUS), .we(Ctrl_RAM_L), .oe(not_16_out), .clk(clk), .data({ram_3_data_2, ram_3_data}));
  not not_16 (not_16_out, Ctrl_RAM_L);
  nand nand_6 (nand_6_out, not_28_out, not_27_out);
  LedBar ledbar_13 (
    .led0(ram_3_data_2[3]), .led1(ram_3_data_2[2]), .led2(ram_3_data_2[1]), .led3(ram_3_data_2[0]),
    .led4(ram_3_data[3]), .led5(ram_3_data[2]), .led6(ram_3_data[1]), .led7(ram_3_data[0]));
  Hex_Digit_Display #(.decimalPoint("false")) hex_digit_display_5 (.value(ram_3_data_2));
  or or_21 (or_21_out, manuel_write_enable, nand_6_out);
  Hex_Digit_Display #(.decimalPoint("false")) hex_digit_display_6 (.value(ram_3_data));
  not not_17 (not_17_out, and_17_out);
  nand nand_7 (nand_7_out, clk_inv, or_22_out);
  assign ram_2_data = and_13_out ? {controlled_buffer_40_out_2, controlled_buffer_40_out} : 8'bz;  // Controlled_Buffer controlled_buffer_42
  assign MAIN_BUS = and_16_out ? {controlled_buffer_40_out_2, controlled_buffer_40_out} : 8'bz;  // Controlled_Buffer controlled_buffer_43
  assign {controlled_buffer_40_out_2, controlled_buffer_40_out} = and_15_out ? MAIN_BUS : 8'bz;  // Controlled_Buffer controlled_buffer_44
  and and_15 (and_15_out, not_20_out, or_21_out);
  and and_16 (and_16_out, not_21_out, or_21_out);
  not not_18 (not_18_out, manuel_write_enable);
  and and_17 (and_17_out, not_18_out, not_19_out);
  not not_19 (not_19_out, or_22_out);
  or or_22 (or_22_out, not_24_out, manuel_write);
  assign {controlled_buffer_40_out_2, controlled_buffer_40_out} = and_14_out ? ram_2_data : 8'bz;  // Controlled_Buffer controlled_buffer_45
  not not_20 (not_20_out, not_21_out);
  not not_21 (not_21_out, or_23_out);
  or or_23 (or_23_out, not_22_out, not_27_out);
  not not_22 (not_22_out, not_28_out);
  Controlled_Buffer #(.width(8)) controlled_buffer_46 (.in({ram_3_data_2, ram_3_data}), .en(not_23_out));  // open: out
  not not_23 (not_23_out, Ctrl_RAM_L);
  Controlled_Buffer #(.width(8)) controlled_buffer_47 (.out({ram_3_data_2, ram_3_data}), .en(Ctrl_RAM_L));  // open: in
  not not_24 (not_24_out, not_26_out);
  not not_25 (not_25_out, manuel_write_enable);
  assign Memory_BUS = and_18_out ? {controlled_buffer_40_out_2, controlled_buffer_40_out} : 8'bz;  // Controlled_Buffer controlled_buffer_48
  and and_18 (and_18_out, not_28_out, not_25_out);
  assign controlled_buffer_49_out = Ctrl_mem_A_MAIN_BUS ? {ram_3_data_2, ram_3_data} : 8'bz;  // Controlled_Buffer controlled_buffer_49
  not not_26 (not_26_out, Ctrl_RAM_L);
  not not_27 (not_27_out, Ctrl_mem_A_MAIN_BUS);
  not not_28 (not_28_out, Ctrl_RAM_L);
  LedBar #(.matrixcols(16)) ledbar_14 (
    .led0(Address_BUS[15]), .led1(Address_BUS[14]), .led2(Address_BUS[13]), .led3(Address_BUS[12]),
    .led4(Address_BUS[11]), .led5(Address_BUS[10]), .led6(Address_BUS[9]), .led7(Address_BUS[8]),
    .led8(Address_BUS[7]), .led9(Address_BUS[6]), .led10(Address_BUS[5]), .led11(Address_BUS[4]),
    .led12(Address_BUS[3]), .led13(Address_BUS[2]), .led14(Address_BUS[1]), .led15(Address_BUS[0]));
  Hex_Digit_Display #(.decimalPoint("false")) hex_digit_display_7 (.value(Address_BUS[15:12]));
  Hex_Digit_Display #(.decimalPoint("false")) hex_digit_display_8 (.value(Address_BUS[11:8]));
  DipSwitch dipswitch_1 (
    .sw1(MAIN_BUS[7]), .sw2(MAIN_BUS[6]), .sw3(MAIN_BUS[5]), .sw4(MAIN_BUS[4]), .sw5(MAIN_BUS[3]),
    .sw6(MAIN_BUS[2]), .sw7(MAIN_BUS[1]), .sw8(MAIN_BUS[0]));
  Hex_Digit_Display #(.decimalPoint("false")) hex_digit_display_9 (.value(Address_BUS[7:4]));
  Hex_Digit_Display #(.decimalPoint("false")) hex_digit_display_10 (.value(Address_BUS[3:0]));
  LedBar ledbar_15 (
    .led0(MAIN_BUS[7]), .led1(MAIN_BUS[6]), .led2(MAIN_BUS[5]), .led3(MAIN_BUS[4]), .led4(MAIN_BUS[3]),
    .led5(MAIN_BUS[2]), .led6(MAIN_BUS[1]), .led7(MAIN_BUS[0]));
  Hex_Digit_Display #(.decimalPoint("false")) hex_digit_display_11 (.value(MAIN_BUS[7:4]));
  Hex_Digit_Display #(.decimalPoint("false")) hex_digit_display_12 (.value(MAIN_BUS[3:0]));
  LedBar ledbar_16 (
    .led0(controlled_buffer_40_out_2[3]), .led1(controlled_buffer_40_out_2[2]),
    .led2(controlled_buffer_40_out_2[1]), .led3(controlled_buffer_40_out_2[0]),
    .led4(controlled_buffer_40_out[3]), .led5(controlled_buffer_40_out[2]),
    .led6(controlled_buffer_40_out[1]), .led7(controlled_buffer_40_out[0]));
  Hex_Digit_Display #(.decimalPoint("false")) hex_digit_display_13 (.value(controlled_buffer_40_out_2));
  Hex_Digit_Display #(.decimalPoint("false")) hex_digit_display_14 (.value(controlled_buffer_40_out));

  // Notes on the sheet:
  //   GPR_A
  //   GPR_B
  //   Constant Reg
  //   Program Counter
  //   16BIT Counter Reg 1
  //   GPR_C
  //   GPR_D
  //   GPR_X
  //   Stack Pointer
  //   contents of rom_1 (hex, n*v repeats v):
  //   b0 7*0 b0 0 0 1a 4*0 b0 0 0 2a 4*0 b0 0 0 3a 4*0 b0 0 0 4a 4*0 b0 0 0 5a 4*0 b0 0 0 da 4*0 b0 0 0 ea
  //   4*0 b0 0 12 5*0 b0 0 13 5*0 b0 0 14 5*0 b0 0 15 5*0 b0 0 1d 5*0 b0 0 1e 5*0 b0 0 21 5*0 b0 0 23 5*0
  //   b0 0 24 5*0 b0 0 25 5*0 b0 0 2d 5*0 b0 0 2e 5*0 b0 0 31 5*0 b0 0 32 5*0 b0 0 34 5*0 b0 0 35 5*0 b0 0
  //   3d 5*0 b0 0 3e 5*0 b0 0 41 5*0 b0 0 42 5*0 b0 0 43 5*0 b0 0 45 5*0 b0 0 4d 5*0 b0 0 4e 5*0 b0 0 51
  //   5*0 b0 0 52 5*0 b0 0 53 5*0 b0 0 54 5*0 b0 0 5d 5*0 b0 0 5e 5*0 b0 0 d1 5*0 b0 0 d2 5*0 b0 0 d3 5*0
  //   b0 0 d4 5*0 b0 0 d5 5*0 b0 0 de 5*0 b0 0 e1 5*0 b0 0 e2 5*0 b0 0 e3 5*0 b0 0 e4 5*0 b0 0 e5 5*0 b0 0
  //   ed 5*0 b0 0 6c 5*0 b0 0 67 5*0 b0 0 68 5*0 b0 0 7c 5*0 b0 0 76 5*0 b0 0 78 5*0 b0 0 8c 5*0 b0 0 86
  //   5*0 b0 0 87 5*0 b0 0 c6 5*0 b0 0 c7 5*0 b0 0 c8 5*0 b0 0 0 da ea 1a 0 0 b0 0 0 da ea 2a 0 0 b0 0 0
  //   da ea 3a 0 0 b0 0 0 da ea 4a 0 0 b0 0 0 da ea 5a 0 0 b0 0 0 da ea da 0 0 b0 0 0 da ea ea 0 0 b0 0 0
  //   da ea 91 0 0 b0 0 0 da ea 92 0 0 b0 0 0 da ea 93 0 0 b0 0 0 da ea 94 0 0 b0 0 0 da ea 95 0 0 b0 0 0
  //   da ea 6c 0 0 b0 0 6c 5*0 b0 0 67 5*0 b0 0 68 5*0 b0 7*0 b0 7*0 b0 7*0 b0 7*0 b0 0 0 da ea 6c 0 0 b0
  //   0 6c 5*0 b0 0 67 5*0 b0 0 68 5*0 b0 7*0 b0 7*0 b0 7*0 b0 7*0 b0 0 0 da ea 6c 0 0 b0 0 6c 5*0 b0 0 67
  //   5*0 b0 0 68 5*0 b0 7*0 b0 7*0 b0 7*0 b0 7*0 b0 0 0 da ea 6c 0 0 b0 0 6c 5*0 b0 0 67 5*0 b0 0 68 5*0
  //   b0 0 d6 e6 68 9d 9e 0 b0 0 da ea 6c 0 0 0 b0 0 0 da ea 8c 0 0 b0 7*0 b0 7*0 b0 7*0 b0 7*0 b0 7*0 b0
  //   7*0 b0 7*0 b0 7*0 b0 7*0 b0 7*0 b0 7*0 b0 7*0 b0 7*0 b0 7*0 b0 7*0 b0 7*0 b0 7*0 b0 7*0 b0 7*0 b0
  //   7*0 b0 7*0 b0 7*0 b0 7*0 b0 0 0 91 4*0 b0 0 0 92 4*0 b0 0 0 93 4*0 b0 0 0 94 4*0 b0 0 0 95 4*0 b0 0
  //   0 9d 4*0 b0 0 0 9e 4*0 b0 0 f0 1f 4*0 b0 0 f0 2f 4*0 b0 0 f0 3f 4*0 b0 0 f0 4f 4*0 b0 0 f0 5f 4*0 b0
  //   0 f0 df 4*0 b0 0 f0 ef 4*0 b0 0 0 19 4*0 b0 0 0 19 4*0 b0 0 0 19 4*0 b0 0 0 19 4*0 b0 0 0 29 4*0 b0
  //   0 0 29 4*0 b0 0 0 29 4*0 b0 0 0 39 4*0 b0 0 0 39 4*0 b0 0 0 49 4*0 b0 0 0 19 4*0 b0 0 0 19 4*0 b0 0
  //   0 19 4*0 b0 0 0 19 4*0 b0 0 0 29 4*0 b0 0 0 29 4*0 b0 0 0 29 4*0 b0 0 0 39 4*0 b0 0 0 39 4*0 b0 0 0
  //   49 4*0 b0 0 0 19 4*0 b0 0 0 19 4*0 b0 0 0 19 4*0 b0 0 0 19 4*0 b0 0 0 29 4*0 b0 0 0 29 4*0 b0 0 0 29
  //   4*0 b0 0 0 29 4*0 b0 0 0 39 4*0 b0 0 0 39 4*0 b0 0 0 39 4*0 b0 0 0 39 4*0 b0 0 0 49 4*0 b0 0 0 49
  //   4*0 b0 0 0 49 4*0 b0 0 0 49 4*0 b0 0 0 59 4*0 b0 0 0 59 4*0 b0 0 0 59 4*0 b0 0 0 59 4*0 b0 0 0 19
  //   4*0 b0 0 0 29 4*0 b0 0 0 19 4*0 b0 0 0 29 4*0 b0 0 0 39 4*0 b0 0 0 49 4*0 b0 0 0 59 4*0 b0 0 0 19
  //   4*0 b0 0 0 29 4*0 b0 0 0 39 4*0 b0 0 0 49 4*0 b0 0 0 59 4*0 b0 0 0 19 4*0 b0 0 0 29 4*0 b0 0 0 39
  //   4*0 b0 0 0 49 4*0 b0 0 0 59 4*0 b0 0 0 19 4*0 b0 0 0 29 4*0 b0 0 0 39 4*0 b0 0 0 49 4*0 b0 0 0 59
  //   4*0 b0 0 0 19 4*0 b0 0 0 19 4*0 b0 0 0 19 4*0 b0 0 0 19 4*0 b0 0 0 29 4*0 b0 0 0 29 4*0 b0 0 0 29
  //   4*0 b0 0 0 39 4*0 b0 0 0 39 4*0 b0 0 0 49 4*0 b0 0 0 19 4*0 b0 0 0 19 4*0 b0 0 0 19 4*0 b0 0 0 19
  //   4*0 b0 0 0 29 4*0 b0 0 0 29 4*0 b0 0 0 29 4*0 b0 0 0 39 4*0 b0 0 0 39 4*0 b0 0 0 49 4*0 b0 0 0 19
  //   4*0 b0 0 0 19 4*0 b0 0 0 19 4*0 b0 0 0 19 4*0 b0 0 0 29 4*0 b0 0 0 29 4*0 b0 0 0 29 4*0 b0 0 0 39
  //   4*0 b0 0 0 39 4*0 b0 0 0 49 4*0 b0 0 0 19 4*0 b0 0 0 19 4*0 b0 0 0 19 4*0 b0 0 0 19 4*0 b0 0 0 29
  //   4*0 b0 0 0 29 4*0 b0 0 0 29 4*0 b0 0 0 39 4*0 b0 0 0 39 4*0 b0 0 0 49 4*0 b0 0 0 19 4*0 b0 0 0 29
  //   4*0 b0 0 0 39 4*0 b0 0 0 49 4*0 b0 0 0 59 4*0 b0 0 0 19 4*0 b0 0 0 29 4*0 b0 0 0 39 4*0 b0 0 0 49
  //   4*0 b0 0 0 59 4*0 b0 0 0 19 4*0 b0 0 0 19 4*0 b0 7*0 b0 0 0 1a 4*0 b0 0 0 2a 4*0 b0 0 0 3a 4*0 b0 0
  //   0 4a 4*0 b0 0 0 5a 4*0 b0 0 0 da 4*0 b0 0 0 ea 4*0 b0 0 12 5*0 b0 0 13 5*0 b0 0 14 5*0 b0 0 15 5*0
  //   b0 0 1d 5*0 b0 0 1e 5*0 b0 0 21 5*0 b0 0 23 5*0 b0 0 24 5*0 b0 0 25 5*0 b0 0 2d 5*0 b0 0 2e 5*0 b0 0
  //   31 5*0 b0 0 32 5*0 b0 0 34 5*0 b0 0 35 5*0 b0 0 3d 5*0 b0 0 3e 5*0 b0 0 41 5*0 b0 0 42 5*0 b0 0 43
  //   5*0 b0 0 45 5*0 b0 0 4d 5*0 b0 0 4e 5*0 b0 0 51 5*0 b0 0 52 5*0 b0 0 53 5*0 b0 0 54 5*0 b0 0 5d 5*0
  //   b0 0 5e 5*0 b0 0 d1 5*0 b0 0 d2 5*0 b0 0 d3 5*0 b0 0 d4 5*0 b0 0 d5 5*0 b0 0 de 5*0 b0 0 e1 5*0 b0 0
  //   e2 5*0 b0 0 e3 5*0 b0 0 e4 5*0 b0 0 e5 5*0 b0 0 ed 5*0 b0 0 6c 5*0 b0 0 67 5*0 b0 0 68 5*0 b0 0 7c
  //   5*0 b0 0 76 5*0 b0 0 78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
  //   contents of rom_2 (hex, n*v repeats v):
  //   1 8 8 5*0 1 8 8 9 4*0 1 8 8 9 4*0 1 8 8 9 4*0 1 8 8 9 4*0 1 8 8 9 4*0 1 8 8 9 4*0 1 8 8 9 4*0 1 8 8
  //   5*0 1 8 8 5*0 1 8 8 5*0 1 8 8 5*0 1 8 8 5*0 1 8 8 5*0 1 8 8 5*0 1 8 8 5*0 1 8 8 5*0 1 8 8 5*0 1 8 8
  //   5*0 1 8 8 5*0 1 8 8 5*0 1 8 8 5*0 1 8 8 5*0 1 8 8 5*0 1 8 8 5*0 1 8 8 5*0 1 8 8 5*0 1 8 8 5*0 1 8 8
  //   5*0 1 8 8 5*0 1 8 8 5*0 1 8 8 5*0 1 8 8 5*0 1 8 8 5*0 1 8 8 5*0 1 8 8 5*0 1 8 8 5*0 1 8 8 5*0 1 8 8
  //   5*0 1 8 8 5*0 1 8 8 5*0 1 8 8 5*0 1 8 8 5*0 1 8 8 5*0 1 8 8 5*0 1 8 8 5*0 1 8 8 5*0 1 8 8 5*0 1 8 8
  //   5*0 1 8 8 5*0 1 8 8 5*0 1 8 8 5*0 1 8 8 5*0 1 8 8 5*0 1 8 8 5*0 1 8 8 5*0 1 8 8 5*0 1 8 8 5*0 1 8 8
  //   5*0 1 8 8 5*0 1 8 8 5*0 1 8 8 5*0 1 8 8 9 9 4 0 0 1 8 8 9 9 4 0 0 1 8 8 9 9 4 0 0 1 8 8 9 9 4 0 0 1
  //   8 8 9 9 4 0 0 1 8 8 9 9 4 0 0 1 8 8 9 9 4 0 0 1 8 8 9 9 4 0 0 1 8 8 9 9 4 0 0 1 8 8 9 9 4 0 0 1 8 8
  //   9 9 4 0 0 1 8 8 9 9 4 0 0 1 8 8 9 1 0 0 0 1 8 6*0 1 8 6*0 1 8 6*0 1 8 8 5*0 1 8 8 5*0 1 8 8 5*0 1 8
  //   8 5*0 1 8 8 9 1 0 0 0 1 8 6*0 1 8 6*0 1 8 6*0 1 8 8 5*0 1 8 8 5*0 1 8 8 5*0 1 8 8 5*0 1 8 8 9 1 0 0
  //   0 1 8 6*0 1 8 6*0 1 8 6*0 1 8 8 5*0 1 8 8 5*0 1 8 8 5*0 1 8 8 5*0 1 8 8 9 1 0 0 0 1 8 6*0 1 8 6*0 1
  //   8 6*0 1 8 0 0 40 42 2 0 1 8 12 12 0 8 0 0 1 8 8 9 9 0 0 0 1 8 8 5*0 1 8 8 5*0 1 8 8 5*0 1 8 8 5*0 1
  //   8 8 5*0 1 8 8 5*0 1 8 6*0 1 8 6*0 1 8 6*0 1 8 6*0 1 8 6*0 1 8 6*0 1 8 6*0 1 8 6*0 1 8 6*0 1 8 6*0 1
  //   8 6*0 1 8 6*0 1 8 6*0 1 8 6*0 1 8 6*0 1 8 6*0 1 8 6*0 1 8 40 2 4*0 1 8 40 2 4*0 1 8 40 2 4*0 1 8 40
  //   2 4*0 1 8 40 2 4*0 1 8 40 2 4*0 1 8 40 2 4*0 1 8 2 10 4*0 1 8 2 10 4*0 1 8 2 10 4*0 1 8 2 10 4*0 1 8
  //   2 10 4*0 1 8 2 10 4*0 1 8 2 10 4*0 1 8 88 5*0 1 8 88 5*0 1 8 88 5*0 1 8 88 5*0 1 8 88 5*0 1 8 88 5*0
  //   1 8 88 5*0 1 8 88 5*0 1 8 88 5*0 1 8 88 5*0 1 8 88 5*0 1 8 88 5*0 1 8 88 5*0 1 8 88 5*0 1 8 88 5*0 1
  //   8 88 5*0 1 8 88 5*0 1 8 88 5*0 1 8 88 5*0 1 8 88 5*0 1 8 88 5*0 1 8 88 5*0 1 8 88 5*0 1 8 88 5*0 1 8
  //   88 5*0 1 8 88 5*0 1 8 88 5*0 1 8 88 5*0 1 8 88 5*0 1 8 88 5*0 1 8 88 5*0 1 8 88 5*0 1 8 88 5*0 1 8
  //   88 5*0 1 8 88 5*0 1 8 88 5*0 1 8 88 5*0 1 8 88 5*0 1 8 88 5*0 1 8 88 5*0 1 8 88 5*0 1 8 88 5*0 1 8
  //   88 5*0 1 8 88 5*0 1 8 88 5*0 1 8 88 5*0 1 8 88 5*0 1 8 88 5*0 1 8 88 5*0 1 8 88 5*0 1 8 88 5*0 1 8
  //   88 5*0 1 8 88 5*0 1 8 88 5*0 1 8 88 5*0 1 8 88 5*0 1 8 88 5*0 1 8 88 5*0 1 8 88 5*0 1 8 88 5*0 1 8
  //   88 5*0 1 8 88 5*0 1 8 88 5*0 1 8 88 5*0 1 8 88 5*0 1 8 88 5*0 1 8 88 5*0 1 8 88 5*0 1 8 88 5*0 1 8
  //   88 5*0 1 8 88 5*0 1 8 88 5*0 1 8 88 5*0 1 8 88 5*0 1 8 88 5*0 1 8 88 5*0 1 8 88 5*0 1 8 88 5*0 1 8
  //   88 5*0 1 8 88 5*0 1 8 88 5*0 1 8 88 5*0 1 8 88 5*0 1 8 88 5*0 1 8 88 5*0 1 8 88 5*0 1 8 88 5*0 1 8
  //   88 5*0 1 8 88 5*0 1 8 88 5*0 1 8 88 5*0 1 8 88 5*0 1 8 88 5*0 1 8 88 5*0 1 8 88 5*0 1 8 88 5*0 1 8
  //   88 5*0 1 8 88 5*0 1 8 88 5*0 1 8 88 5*0 1 8 88 5*0 1 8 88 5*0 1 8 88 5*0 1 8 88 5*0 1 8 88 5*0 1 8
  //   88 5*0 1 8 88 5*0 1 8 88 5*0 1 8 88 5*0 1 8 88 5*0 1 8 88 5*0 1 8 88 5*0 1 8 88 5*0 1 8 88 5*0 1 8 8
  //   5*0 1 8 8 9 4*0 1 8 8 9 4*0 1 8 8 9 4*0 1 8 8 9 4*0 1 8 8 9 4*0 1 8 8 9 4*0 1 8 8 9 4*0 1 8 8 5*0 1
  //   8 8 5*0 1 8 8 5*0 1 8 8 5*0 1 8 8 5*0 1 8 8 5*0 1 8 8 5*0 1 8 8 5*0 1 8 8 5*0 1 8 8 5*0 1 8 8 5*0 1
  //   8 8 5*0 1 8 8 5*0 1 8 8 5*0 1 8 8 5*0 1 8 8 5*0 1 8 8 5*0 1 8 8 5*0 1 8 8 5*0 1 8 8 5*0 1 8 8 5*0 1
  //   8 8 5*0 1 8 8 5*0 1 8 8 5*0 1 8 8 5*0 1 8 8 5*0 1 8 8 5*0 1 8 8 5*0 1 8 8 5*0 1 8 8 5*0 1 8 8 5*0 1
  //   8 8 5*0 1 8 8 5*0 1 8 8 5*0 1 8 8 5*0 1 8 8 5*0 1 8 8 5*0 1 8 8 5*0 1 8 8 5*0 1 8 8 5*0 1 8 8 5*0 1
  //   8 8 5*0 1 8 8 5*0 1 8 8 5*0 1 8 8 5*0 1 8 8 5*0 1 8 8 5*0 1 8 8 5*0 1 8 8 5*0 1 8 8 5*0 1 8 8 5*0 1
  //   8 8 5*0 1 8 8 5*0 1 8 8 5*0 1 8 8 9 9 4 0 0 1 8 8 9 9 4 0 0 1 8 8 9 9 4 0 0 1 8 8 9 9 4 0 0 1 8 8 9
  //   9 4 0 0 1 8 8 9 9 4 0 0 1 8 8 9 9 4 0 0 1 8 8 9 9 4 0 0 1 8 8 9 9 4 0 0 1 8 8 9 9 4 0 0 1 8 8 9 9 4
  //   0 0 1 8 8 9 9 4 0 0 1 8 8 9 1 0 0 0 1 8 6*0 1 8 6*0 1 8 6*0 1 8 8 9 1 0 0 0 1 8 6*0 1 8 6*0 1 8 6*0
  //   1 8 8 9 1 0 0 0 1 8 6*0 1 8 6*0 1 8 6*0 1 8 8 5*0 1 8 8 5*0 1 8 8 5*0 1 8 8 5*0 1 8 8 9 1 0 0 0 1 8
  //   6*0 1 8 6*0 1 8 6*0 1 8 8 5*0 1 8 8 5*0 1 8 8 5*0 1 8 8 5*0 1 8 8 9 1 0 0 0 1 8 6*0 1 8 6*0 1 8 6*0
  //   1 8 0 0 40 42 2 0 1 8 12 12 0 8 0 0 1 8 8 9 9 0 0 0 1 8 8 5*0 1 8 8 5*0 1 8 8 5*0 1 8 8 5*0 1 8 8
  //   5*0 1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
  //   contents of rom_3 (hex, n*v repeats v):
  //   1138*0 11 7*0 19 7*0 21 7*0 29 7*0 1a 7*0 22 7*0 2a 7*0 23 7*0 2b 7*0 2c 7*0 11 7*0 19 7*0 21 7*0 29
  //   7*0 1a 7*0 22 7*0 2a 7*0 23 7*0 2b 7*0 2c 7*0 11 7*0 19 7*0 21 7*0 29 7*0 a 7*0 1a 7*0 22 7*0 2a 7*0
  //   b 7*0 13 7*0 23 7*0 2b 7*0 c 7*0 14 7*0 1c 7*0 2c 7*0 d 7*0 15 7*0 1d 7*0 25 7*0 11 7*0 a 7*0 1 7*0
  //   2 7*0 3 7*0 4 7*0 5 7*0 1 7*0 2 7*0 3 7*0 4 7*0 5 7*0 1 7*0 2 7*0 3 7*0 4 7*0 5 7*0 1 7*0 2 7*0 3
  //   7*0 4 7*0 5 7*0 11 7*0 19 7*0 21 7*0 29 7*0 1a 7*0 22 7*0 2a 7*0 23 7*0 2b 7*0 2c 7*0 11 7*0 19 7*0
  //   21 7*0 29 7*0 1a 7*0 22 7*0 2a 7*0 23 7*0 2b 7*0 2c 7*0 11 7*0 19 7*0 21 7*0 29 7*0 1a 7*0 22 7*0 2a
  //   7*0 23 7*0 2b 7*0 2c 7*0 11 7*0 19 7*0 21 7*0 29 7*0 1a 7*0 22 7*0 2a 7*0 23 7*0 2b 7*0 2c 7*0 1 7*0
  //   2 7*0 3 7*0 4 7*0 5 7*0 1 7*0 2 7*0 3 7*0 4 7*0 5 7*0 11 7*0 11 1143*0 11 7*0 19 7*0 21 7*0 29 7*0
  //   1a 7*0 22 7*0 2a 7*0 23 7*0 2b 7*0 2c 7*0 11 7*0 19 7*0 21 7*0 29 7*0 1a 7*0 22 7*0 2a 7*0 23 7*0 2b
  //   7*0 2c 7*0 11 7*0 19 7*0 21 7*0 29 7*0 a 7*0 1a 7*0 22 7*0 2a 7*0 b 7*0 13 7*0 23 7*0 2b 7*0 c 7*0
  //   14 7*0 1c 7*0 2c 7*0 d 7*0 15 7*0 1d 7*0 25 7*0 11 7*0 a 7*0 1 7*0 2 7*0 3 7*0 4 7*0 5 7*0 1 7*0 2
  //   7*0 3 7*0 4 7*0 5 7*0 1 7*0 2 7*0 3 7*0 4 7*0 5 7*0 1 7*0 2 7*0 3 7*0 4 7*0 5 7*0 11 7*0 19 7*0 21
  //   7*0 29 7*0 1a 7*0 22 7*0 2a 7*0 23 7*0 2b 7*0 2c 7*0 11 7*0 19 7*0 21 7*0 29 7*0 1a 7*0 22 7*0 2a
  //   7*0 23 7*0 2b 7*0 2c 7*0 11 7*0 19 7*0 21 7*0 29 7*0 1a 7*0 22 7*0 2a 7*0 23 7*0 2b 7*0 2c 7*0 11
  //   7*0 19 7*0 21 7*0 29 7*0 1a 7*0 22 7*0 2a 7*0 23 7*0 2b 7*0 2c 7*0 1 7*0 2 7*0 3 7*0 4 7*0 5 7*0 1
  //   7*0 2 7*0 3 7*0 4 7*0 5 7*0 11 7*0 11 1143*0 11 7*0 19 7*0 21 7*0 29 7*0 1a 7*0 22 7*0 2a 7*0 23 7*0
  //   2b 7*0 2c 7*0 11 7*0 19 7*0 21 7*0 29 7*0 1a 7*0 22 7*0 2a 7*0 23 7*0 2b 7*0 2c 7*0 11 7*0 19 7*0 21
  //   7*0 29 7*0 a 7*0 1a 7*0 22 7*0 2a 7*0 b 7*0 13 7*0 23 7*0 2b 7*0 c 7*0 14 7*0 1c 7*0 2c 7*0 d 7*0 15
  //   7*0 1d 7*0 25 7*0 11 7*0 a 7*0 1 7*0 2 7*0 3 7*0 4 7*0 5 7*0 1 7*0 2 7*0 3 7*0 4 7*0 5 7*0 1 7*0 2
  //   7*0 3 7*0 4 7*0 5 7*0 1 7*0 2 7*0 3 7*0 4 7*0 5 7*0 11 7*0 19 7*0 21 7*0 29 7*0 1a 7*0 22 7*0 2a 7*0
  //   23 7*0 2b 7*0 2c 7*0 11 7*0 19 7*0 21 7*0 29 7*0 1a 7*0 22 7*0 2a 7*0 23 7*0 2b 7*0 2c 7*0 11 7*0 19
  //   7*0 21 7*0 29 7*0 1a 7*0 22 7*0 2a 7*0 23 7*0 2b 7*0 2c 7*0 11 7*0 19 7*0 21 7*0 29 7*0 1a 7*0 22
  //   7*0 2a 7*0 23 7*0 2b 7*0 2c 7*0 1 7*0 2 7*0 3 7*0 4 7*0 5 7*0 1 7*0 2 7*0 3 7*0 4 7*0 5 7*0 11 7*0
  //   11 1143*0 11 7*0 19 7*0 21 7*0 29 7*0 1a 7*0 22 7*0 2a 7*0 23 7*0 2b 7*0 2c 7*0 11 7*0 19 7*0 21 7*0
  //   29 7*0 1a 7*0 22 7*0 2a 7*0 23 7*0 2b 7*0 2c 7*0 11 7*0 19 7*0 21 7*0 29 7*0 a 7*0 1a 7*0 22 7*0 2a
  //   7*0 b 7*0 13 7*0 23 7*0 2b 7*0 c 7*0 14 7*0 1c 7*0 2c 7*0 d 7*0 15 7*0 1d 7*0 25 7*0 11 7*0 a 7*0 1
  //   7*0 2 7*0 3 7*0 4 7*0 5 7*0 1 7*0 2 7*0 3 7*0 4 7*0 5 7*0 1 7*0 2 7*0 3 7*0 4 7*0 5 7*0 1 7*0 2 7*0
  //   3 7*0 4 7*0 5 7*0 11 7*0 19 7*0 21 7*0 29 7*0 1a 7*0 22 7*0 2a 7*0 23 7*0 2b 7*0 2c 7*0 11 7*0 19
  //   7*0 21 7*0 29 7*0 1a 7*0 22 7*0 2a 7*0 23 7*0 2b 7*0 2c 7*0 11 7*0 19 7*0 21 7*0 29 7*0 1a 7*0 22
  //   7*0 2a 7*0 23 7*0 2b 7*0 2c 7*0 11 7*0 19 7*0 21 7*0 29 7*0 1a 7*0 22 7*0 2a 7*0 23 7*0 2b 7*0 2c
  //   7*0 1 7*0 2 7*0 3 7*0 4 7*0 5 7*0 1 7*0 2 7*0 3 7*0 4 7*0 5 7*0 11 7*0 11 1143*0 11 7*0 19 7*0 21
  //   7*0 29 7*0 1a 7*0 22 7*0 2a 7*0 23 7*0 2b 7*0 2c 7*0 11 7*0 19 7*0 21 7*0 29 7*0 1a 7*0 22 7*0 2a
  //   7*0 23 7*0 2b 7*0 2c 7*0 11 7*0 19 7*0 21 7*0 29 7*0 a 7*0 1a 7*0 22 7*0 2a 7*0 b 7*0 13 7*0 23 7*0
  //   2b 7*0 c 7*0 14 7*0 1c 7*0 2c 7*0 d 7*0 15 7*0 1d 7*0 25 7*0 11 7*0 a 7*0 1 7*0 2 7*0 3 7*0 4 7*0 5
  //   7*0 1 7*0 2 7*0 3 7*0 4 7*0 5 7*0 1 7*0 2 7*0 3 7*0 4 7*0 5 7*0 1 7*0 2 7*0 3 7*0 4 7*0 5 7*0 11 7*0
  //   19 7*0 21 7*0 29 7*0 1a 7*0 22 7*0 2a 7*0 23 7*0 2b 7*0 2c 7*0 11 7*0 19 7*0 21 7*0 29 7*0 1a 7*0 22
  //   7*0 2a 7*0 23 7*0 2b 7*0 2c 7*0 11 7*0 19 7*0 21 7*0 29 7*0 1a 7*0 22 7*0 2a 7*0 23 7*0 2b 7*0 2c
  //   7*0 11 7*0 19 7*0 21 7*0 29 7*0 1a 7*0 22 7*0 2a 7*0 23 7*0 2b 7*0 2c 7*0 1 7*0 2 7*0 3 7*0 4 7*0 5
  //   7*0 1 7*0 2 7*0 3 7*0 4 7*0 5 7*0 11 7*0 11 1143*0 11 7*0 19 7*0 21 7*0 29 7*0 1a 7*0 22 7*0 2a 7*0
  //   23 7*0 2b 7*0 2c 7*0 11 7*0 19 7*0 21 7*0 29 7*0 1a 7*0 22 7*0 2a 7*0 23 7*0 2b 7*0 2c 7*0 11 7*0 19
  //   7*0 21 7*0 29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
  //   contents of rom_4 (hex, n*v repeats v):
  //   0 0 0 80 8*0 80 7*0 80 7*0 80 7*0 80 7*0 80 7*0 80 7*0 80 6*0 80 7*0 80 7*0 80 7*0 80 7*0 80 7*0 80
  //   7*0 80 7*0 80 7*0 80 7*0 80 7*0 80 7*0 80 7*0 80 7*0 80 7*0 80 7*0 80 7*0 80 7*0 80 7*0 80 7*0 80
  //   7*0 80 7*0 80 7*0 80 7*0 80 7*0 80 7*0 80 7*0 80 7*0 80 7*0 80 7*0 80 7*0 80 7*0 80 7*0 80 7*0 80
  //   7*0 80 7*0 80 7*0 80 7*0 80 7*0 80 7*0 80 7*0 80 7*0 80 7*0 80 7*0 80 7*0 80 7*0 80 7*0 80 7*0 80
  //   7*0 80 7*0 80 7*0 80 7*0 80 7*0 80 7*0 80 10*0 80 7*0 80 7*0 80 7*0 80 7*0 80 7*0 80 7*0 80 7*0 80
  //   7*0 80 7*0 80 7*0 80 7*0 80 7*0 80 4*0 80 7*0 80 7*0 80 7*0 80 7*0 80 7*0 80 7*0 80 10*0 80 4*0 80
  //   7*0 80 7*0 80 7*0 80 7*0 80 7*0 80 7*0 80 10*0 80 4*0 80 7*0 80 7*0 80 7*0 80 7*0 80 7*0 80 7*0 80
  //   10*0 80 4*0 80 7*0 80 7*0 80 11*0 80 6*0 80 7*0 80 4*0 80 7*0 80 7*0 80 7*0 80 7*0 80 7*0 80 144*0
  //   80 7*0 80 7*0 80 7*0 80 7*0 80 7*0 80 7*0 80 7*0 80 7*0 80 7*0 80 7*0 80 7*0 80 7*0 80 7*0 80 7*0 80
  //   7*0 80 7*0 80 7*0 80 7*0 80 7*0 80 7*0 80 7*0 80 7*0 80 7*0 80 5*0 1 0 80 5*0 1 0 80 5*0 1 0 80 5*0
  //   1 0 80 5*0 1 0 80 5*0 1 0 80 5*0 1 0 80 5*0 1 0 80 5*0 1 0 80 5*0 1 0 80 5*0 2 0 80 5*0 2 0 80 5*0 2
  //   0 80 5*0 2 0 80 5*0 2 0 80 5*0 2 0 80 5*0 2 0 80 5*0 2 0 80 5*0 2 0 80 5*0 2 0 80 5*0 2 0 80 5*0 2 0
  //   80 5*0 2 0 80 5*0 2 0 80 5*0 2 0 80 5*0 2 0 80 5*0 2 0 80 5*0 2 0 80 5*0 2 0 80 5*0 2 0 80 5*0 3 0
  //   80 5*0 3 0 80 5*0 4 0 80 5*0 4 0 80 5*0 4 0 80 5*0 4 0 80 5*0 4 0 80 5*0 5 0 80 5*0 5 0 80 5*0 5 0
  //   80 5*0 5 0 80 5*0 5 0 80 5*0 6 0 80 5*0 6 0 80 5*0 6 0 80 5*0 6 0 80 5*0 6 0 80 5*0 7 0 80 5*0 7 0
  //   80 5*0 7 0 80 5*0 7 0 80 5*0 7 0 80 5*0 8 0 80 5*0 8 0 80 5*0 8 0 80 5*0 8 0 80 5*0 8 0 80 5*0 8 0
  //   80 5*0 8 0 80 5*0 8 0 80 5*0 8 0 80 5*0 8 0 80 5*0 9 0 80 5*0 9 0 80 5*0 9 0 80 5*0 9 0 80 5*0 9 0
  //   80 5*0 9 0 80 5*0 9 0 80 5*0 9 0 80 5*0 9 0 80 5*0 9 0 80 5*0 a 0 80 5*0 a 0 80 5*0 a 0 80 5*0 a 0
  //   80 5*0 a 0 80 5*0 a 0 80 5*0 a 0 80 5*0 a 0 80 5*0 a 0 80 5*0 a 0 80 5*0 b 0 80 5*0 b 0 80 5*0 b 0
  //   80 5*0 b 0 80 5*0 b 0 80 5*0 b 0 80 5*0 b 0 80 5*0 b 0 80 5*0 b 0 80 5*0 b 0 80 5*0 e 0 80 5*0 e 0
  //   80 5*0 e 0 80 5*0 e 0 80 5*0 e 0 80 5*0 f 0 80 5*0 f 0 80 5*0 f 0 80 5*0 f 0 80 5*0 f 0 80 5*0 c 0
  //   80 5*0 d 0 80 6*0 80 8*0 80 7*0 80 7*0 80 7*0 80 7*0 80 7*0 80 7*0 80 6*0 80 7*0 80 7*0 80 7*0 80
  //   7*0 80 7*0 80 7*0 80 7*0 80 7*0 80 7*0 80 7*0 80 7*0 80 7*0 80 7*0 80 7*0 80 7*0 80 7*0 80 7*0 80
  //   7*0 80 7*0 80 7*0 80 7*0 80 7*0 80 7*0 80 7*0 80 7*0 80 7*0 80 7*0 80 7*0 80 7*0 80 7*0 80 7*0 80
  //   7*0 80 7*0 80 7*0 80 7*0 80 7*0 80 7*0 80 7*0 80 7*0 80 7*0 80 7*0 80 7*0 80 7*0 80 7*0 80 7*0 80
  //   7*0 80 7*0 80 7*0 80 7*0 80 7*0 80 7*0 80 7*0 80 7*0 80 10*0 80 7*0 80 7*0 80 7*0 80 7*0 80 7*0 80
  //   7*0 80 7*0 80 7*0 80 7*0 80 7*0 80 7*0 80 7*0 80 4*0 80 7*0 80 7*0 80 10*0 80 4*0 80 7*0 80 7*0 80
  //   10*0 80 4*0 80 7*0 80 7*0 80 7*0 80 7*0 80 7*0 80 7*0 80 10*0 80 4*0 80 7*0 80 7*0 80 7*0 80 7*0 80
  //   7*0 80 7*0 80 10*0 80 4*0 80 7*0 80 7*0 80 11*0 80 6*0 80 7*0 80 4*0 80 7*0 80 7*0 80 7*0 80 7*0 80
  //   7*0 80 144*0 80 7*0 80 7*0 80 7*0 80 7*0 80 7*0 80 7*0 80 7*0 80 7*0 80 7*0 80 7*0 80 7*0 80 7*0 80
  //   7*0 80 7*0 80 7*0 80 7*0 80 7*0 80 7*0 80 7*0 80 7*0 80 7*0 80 7*0 80 7*0 80 5*0 1 0 80 5*0 1 0 80
  //   5*0 1 0 80 5*0 1 0 80 5*0 1 0 80 5*0 1 0 80 5*0 1 0 80 5*0 1 0 80 5*0 1 0 80 5*0 1 0 80 5*0 2 0 80
  //   5*0 2 0 80 5*0 2 0 80 5*0 2 0 80 5*0 2 0 80 5*0 2 0 80 5*0 2 0 80 5*0 2 0 80 5*0 2 0 80 5*0 2 0 80
  //   5*0 2 0 80 5*0 2 0 80 5*0 2 0 80 5*0 2 0 80 5*0 2 0 80 5*0 2 0 80 5*0 2 0 80 5*0 2 0 80 5*0 2 0 80
  //   5*0 2 0 80 5*0 3 0 80 5*0 3 0 80 5*0 4 0 80 5*0 4 0 80 5*0 4 0 80 5*0 4 0 80 5*0 4 0 80 5*0 5 0 80
  //   5*0 5 0 80 5*0 5 0 80 5*0 5 0 80 5*0 5 0 80 5*0 6 0 80 5*0 6 0 80 5*0 6 0 80 5*0 6 0 80 5*0 6 0 80
  //   5*0 7 0 80 5*0 7 0 80 5*0 7 0 80 5*0 7 0 80 5*0 7 0 80 5*0 8 0 80 5*0 8 0 80 5*0 8 0 80 5*0 8 0 80
  //   5*0 8 0 80 5*0 8 0 80 5*0 8 0 80 5*0 8 0 80 5*0 8 0 80 5*0 8 0 80 5*0 9 0 80 5*0 9 0 80 5*0 9 0 80
  //   5*0 9 0 80 5*0 9 0 80 5*0 9 0 80 5*0 9 0 80 5*0 9 0 80 5*0 9 0 80 5*0 9 0 80 5*0 a 0 80 5*0 a 0 80
  //   5*0 a 0 80 5*0 a 0 80 5*0 a 0 80 5*0 a 0 80 5*0 a 0 80 5*0 a 0 80 5*0 a 0 80 5*0 a 0 80 5*0 b 0 80
  //   5*0 b 0 80 5*0 b 0 80 5*0 b 0 80 5*0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
  //   !WE
  //   !OE
  //   !CE
  //   0001 | 0x1 | A GPR_A MAIN_BUS
  //   0010 | 0x2 | A GPR_B MAIN_BUS
  //   0011 | 0x3 | A GPR_C MAIN_BUS
  //   0100 | 0x4| A GPR_D MAIN_BUS
  //   0101 | 0x5 | A GPR_X Main_BUS
  //   0110 | 0x6 | A PC Xfer_BUS
  //   0111 | 0x7 | A SP Xfer_BUS
  //   1000 | 0x8 | A CREG Xfer_BUS
  //   1001 | 0x9 | A ALU MAIN_BUS
  //   1010 | 0xa | A mem MAIN_BUS
  //   1100 | 0xc | A Xfer Xfer_BUS
  //   1101 | 0xd | A Xfer_R MAIN_BUS
  //   1110 | 0xe | A Xfer_L MAIN_BUS
  //   1111 | 0xf | A const_REG MAIN_BUS
  //   0001 | 0x1 | L GPR_A MAIN_BUS
  //   0010 | 0x2 | L GPR_B MAIN_BUS
  //   0011 | 0x3 | L GPR_C MAIN_BUS
  //   0100 | 0x4 | L GPR_D MAIN_BUS
  //   0101 | 0x5 | L GPR_X MAIN_BUS
  //   0110 | 0x6 | L PC Xfer_BUS
  //   0111 | 0x7 | L SP Xfer_BUS
  //   1000 | 0x8 | L CREG Xfer_BUS
  //   1001 | 0x9 | L RAM Main_BUS
  //   1011 | 0xb | L IR mem_BUS
  //   1100 | 0xc | L Xfer Xfer_BUS
  //   1101 | 0xd | L XferR Main_BUS
  //   1110 | 0xe | L XferL Main_BUS
  //   1111 |  0xf | L const_REG mem_BUS
  //   001 | 0x1 |  A PC addr_BUS
  //   010 | 0x2 |  A SP addr_BUS
  //   011 | 0x3 |  A CREG addr_BUS
  //   100 | 0x4 | A Xfer addr_BUS
  //   01 | 0x1 |  inc PC
  //   10 | 0x2 |  inc SP
  //   11 | 0x3 |  inc CREG
  //   01 | 0x1 |  dec PC
  //   10 | 0x2 |  dec SP
  //   11 | 0x3 |  dec CREG
  //   001 | 0x1 | A  GPR_A ALU_R
  //   010 | 0x2 | A  GPR_B ALU_R
  //   011 | 0x3 | A  GPR_C ALU_R
  //   100 | 0x4 | A  GPR_D ALU_R
  //   101 | 0x5 | A  GPR_X ALU_R
  //   001 | 0x1 | A  GPR_A ALU_L
  //   010 | 0x2 | A  GPR_B ALU_L
  //   011 | 0x3 | A  GPR_C ALU_L
  //   100 | 0x4 | A  GPR_D ALU_L
  //   101 | 0x5 | A  GPR_X ALU_L
  //   !WE
  //   !OE
  //   !CE
endmodule
