// Logisim project Dragon_5.circ as structural Verilog: 1 circuit, main circuit main
module main (
);

  wire clk_inv, rst;
  wire [15:0] FLAGS_q, s0_q, s1_q, s2_q, s3_q, s4_q, s5_q, s6_q, SP_q, t0_q, t1_q, t2_q, t3_q, Turing_In_q,
       Turing_Out_q, undriven, ZERO_q;

  Register #(.width(16)) ZERO (.D(undriven), .clk(clk_inv), .Q(ZERO_q), .clr(rst));  // open: en
  Register #(.width(16)) s0 (.D(undriven), .clk(clk_inv), .Q(s0_q), .clr(rst));  // open: en
  Register #(.width(16)) s1 (.D(undriven), .clk(clk_inv), .Q(s1_q), .clr(rst));  // open: en
  Register #(.width(16)) s2 (.D(undriven), .clk(clk_inv), .Q(s2_q), .clr(rst));  // open: en
  Register #(.width(16)) s3 (.D(undriven), .clk(clk_inv), .Q(s3_q), .clr(rst));  // open: en
  Register #(.width(16)) s4 (.D(undriven), .clk(clk_inv), .Q(s4_q), .clr(rst));  // open: en
  Register #(.width(16)) s5 (.D(undriven), .clk(clk_inv), .Q(s5_q), .clr(rst));  // open: en
  Register #(.width(16)) s6 (.D(undriven), .clk(clk_inv), .Q(s6_q), .clr(rst));  // open: en
  Register #(.width(16)) t0 (.D(undriven), .clk(clk_inv), .Q(t0_q), .clr(rst));  // open: en
  Register #(.width(16)) t1 (.D(undriven), .clk(clk_inv), .Q(t1_q), .clr(rst));  // open: en
  Register #(.width(16)) t2 (.D(undriven), .clk(clk_inv), .Q(t2_q), .clr(rst));  // open: en
  Register #(.width(16)) t3 (.D(undriven), .clk(clk_inv), .Q(t3_q), .clr(rst));  // open: en
  Register #(.width(16)) SP (.D(undriven), .clk(clk_inv), .Q(SP_q), .clr(rst));  // open: en
  Register #(.width(16)) Turing_In (.D(undriven), .clk(clk_inv), .Q(Turing_In_q), .clr(rst));  // open: en
  Register #(.width(16)) Turing_Out (.D(undriven), .clk(clk_inv), .Q(Turing_Out_q), .clr(rst));  // open: en
  Register #(.width(16)) FLAGS (.D(undriven), .clk(clk_inv), .Q(FLAGS_q), .clr(rst));  // open: en
  Multiplexer #(.select(4), .width(16)) multiplexer_1 (
    .in0(ZERO_q), .in1(s0_q), .in2(s1_q), .in3(s2_q), .in4(s3_q), .in5(s4_q), .in6(s5_q), .in7(s6_q),
    .in8(t0_q), .in9(t1_q), .in10(t2_q), .in11(t3_q), .in12(SP_q), .in13(Turing_In_q), .in14(Turing_Out_q),
    .in15(FLAGS_q));  // open: out, sel
  Multiplexer #(.select(4), .width(16)) multiplexer_2 (
    .in0(ZERO_q), .in1(s0_q), .in2(s1_q), .in3(s2_q), .in4(s3_q), .in5(s4_q), .in6(s5_q), .in7(s6_q),
    .in8(t0_q), .in9(t1_q), .in10(t2_q), .in11(t3_q), .in12(SP_q), .in13(Turing_In_q), .in14(Turing_Out_q),
    .in15(FLAGS_q));  // open: out, sel
endmodule
