// Logisim project Dragon_5.circ as structural Verilog: 4 circuits, main circuit main
module main (
);

  Pipeline_ID pipeline_id_1 ();  // open: Inst_Cache_1_IN, Inst_Cache_2_IN, WE, Inst_1_out, Inst_2_out
  Register_File register_file_1 ();  // open: RegF_rst, RegF_WE, RegF_A1, RegF_A2, RegF_A3, RegF_WD, RegF_D1, RegF_D2
endmodule

module ALU (
  input  [3:0] ALU_OP_IN,
  input  [15:0] ALU_A_IN,
  input  [15:0] ALU_B_IN,
  output [15:0] ALU_RES_OUT,
  output [3:0] ALU_FLAG_OUT
);

  Multiplexer #(.select(4), .width(16)) multiplexer_1 (
    .out(ALU_RES_OUT), .sel(ALU_OP_IN));  // open: in0, in1, in2, in3, in4, in5, in6, in7, in8, in9, in10, in11, in12, in13, in14, in15
endmodule

module Register_File (
  input  RegF_rst,
  input  RegF_WE,
  input  [4:0] RegF_A1,
  input  [4:0] RegF_A2,
  input  [4:0] RegF_A3,
  input  [15:0] RegF_WD,
  output [15:0] RegF_D1,
  output [15:0] RegF_D2
);

  wire clock_1_out, decoder_1_out0, decoder_1_out1, decoder_1_out2, decoder_1_out3, decoder_1_out4,
       decoder_1_out5, decoder_1_out6, decoder_1_out7, decoder_1_out8, decoder_1_out9, decoder_1_out10,
       decoder_1_out11, decoder_1_out12, decoder_1_out13, decoder_1_out14, decoder_1_out15, decoder_1_out16,
       decoder_1_out17, decoder_1_out18, decoder_1_out19, decoder_1_out20, decoder_1_out21, decoder_1_out22,
       decoder_1_out23, decoder_1_out24, decoder_1_out25, decoder_1_out26, decoder_1_out27, decoder_1_out28,
       decoder_1_out29, decoder_1_out30, decoder_1_out31;
  wire [15:0] register_1_q, register_2_q, register_3_q, register_4_q, register_5_q, register_6_q,
       register_7_q, register_8_q, register_9_q, register_10_q, register_11_q, register_12_q, register_13_q,
       register_14_q, register_15_q, register_16_q, register_17_q, register_18_q, register_19_q,
       register_20_q, register_21_q, register_22_q, register_23_q, register_24_q, register_25_q,
       register_26_q, register_27_q, register_28_q, register_29_q, register_30_q, register_31_q,
       register_32_q;

  Decoder #(.select(5)) decoder_1 (
    .out0(decoder_1_out0), .out1(decoder_1_out1), .out2(decoder_1_out2), .out3(decoder_1_out3),
    .out4(decoder_1_out4), .out5(decoder_1_out5), .out6(decoder_1_out6), .out7(decoder_1_out7),
    .out8(decoder_1_out8), .out9(decoder_1_out9), .out10(decoder_1_out10), .out11(decoder_1_out11),
    .out12(decoder_1_out12), .out13(decoder_1_out13), .out14(decoder_1_out14), .out15(decoder_1_out15),
    .out16(decoder_1_out16), .out17(decoder_1_out17), .out18(decoder_1_out18), .out19(decoder_1_out19),
    .out20(decoder_1_out20), .out21(decoder_1_out21), .out22(decoder_1_out22), .out23(decoder_1_out23),
    .out24(decoder_1_out24), .out25(decoder_1_out25), .out26(decoder_1_out26), .out27(decoder_1_out27),
    .out28(decoder_1_out28), .out29(decoder_1_out29), .out30(decoder_1_out30), .out31(decoder_1_out31),
    .sel(RegF_A3), .en(RegF_WE));
  Register #(.width(16)) register_1 (
    .D(RegF_WD), .en(decoder_1_out16), .clk(clock_1_out), .Q(register_1_q), .clr(RegF_rst));
  Register #(.width(16)) register_2 (
    .D(RegF_WD), .en(decoder_1_out17), .clk(clock_1_out), .Q(register_2_q), .clr(RegF_rst));
  Register #(.width(16)) register_3 (
    .D(RegF_WD), .en(decoder_1_out18), .clk(clock_1_out), .Q(register_3_q), .clr(RegF_rst));
  Register #(.width(16)) register_4 (
    .D(RegF_WD), .en(decoder_1_out19), .clk(clock_1_out), .Q(register_4_q), .clr(RegF_rst));
  Register #(.width(16)) register_5 (
    .D(RegF_WD), .en(decoder_1_out20), .clk(clock_1_out), .Q(register_5_q), .clr(RegF_rst));
  Register #(.width(16)) register_6 (
    .D(RegF_WD), .en(decoder_1_out21), .clk(clock_1_out), .Q(register_6_q), .clr(RegF_rst));
  Register #(.width(16)) register_7 (
    .D(RegF_WD), .en(decoder_1_out22), .clk(clock_1_out), .Q(register_7_q), .clr(RegF_rst));
  Register #(.width(16)) register_8 (
    .D(RegF_WD), .en(decoder_1_out23), .clk(clock_1_out), .Q(register_8_q), .clr(RegF_rst));
  Register #(.width(16)) register_9 (
    .D(RegF_WD), .en(decoder_1_out24), .clk(clock_1_out), .Q(register_9_q), .clr(RegF_rst));
  Register #(.width(16)) register_10 (
    .D(RegF_WD), .en(decoder_1_out25), .clk(clock_1_out), .Q(register_10_q), .clr(RegF_rst));
  Register #(.width(16)) register_11 (
    .D(RegF_WD), .en(decoder_1_out26), .clk(clock_1_out), .Q(register_11_q), .clr(RegF_rst));
  Register #(.width(16)) register_12 (
    .D(RegF_WD), .en(decoder_1_out27), .clk(clock_1_out), .Q(register_12_q), .clr(RegF_rst));
  Register #(.width(16)) register_13 (
    .D(RegF_WD), .en(decoder_1_out28), .clk(clock_1_out), .Q(register_13_q), .clr(RegF_rst));
  Register #(.width(16)) register_14 (
    .D(RegF_WD), .en(decoder_1_out29), .clk(clock_1_out), .Q(register_14_q), .clr(RegF_rst));
  Register #(.width(16)) register_15 (
    .D(RegF_WD), .en(decoder_1_out30), .clk(clock_1_out), .Q(register_15_q), .clr(RegF_rst));
  Register #(.width(16)) register_16 (
    .D(RegF_WD), .en(decoder_1_out31), .clk(clock_1_out), .Q(register_16_q), .clr(RegF_rst));
  Clock clock_1 (.out(clock_1_out));
  Register #(.width(16)) register_17 (
    .D(RegF_WD), .en(decoder_1_out0), .clk(clock_1_out), .Q(register_17_q), .clr(RegF_rst));
  Register #(.width(16)) register_18 (
    .D(RegF_WD), .en(decoder_1_out1), .clk(clock_1_out), .Q(register_18_q), .clr(RegF_rst));
  Register #(.width(16)) register_19 (
    .D(RegF_WD), .en(decoder_1_out2), .clk(clock_1_out), .Q(register_19_q), .clr(RegF_rst));
  Register #(.width(16)) register_20 (
    .D(RegF_WD), .en(decoder_1_out3), .clk(clock_1_out), .Q(register_20_q), .clr(RegF_rst));
  Register #(.width(16)) register_21 (
    .D(RegF_WD), .en(decoder_1_out4), .clk(clock_1_out), .Q(register_21_q), .clr(RegF_rst));
  Register #(.width(16)) register_22 (
    .D(RegF_WD), .en(decoder_1_out5), .clk(clock_1_out), .Q(register_22_q), .clr(RegF_rst));
  Register #(.width(16)) register_23 (
    .D(RegF_WD), .en(decoder_1_out6), .clk(clock_1_out), .Q(register_23_q), .clr(RegF_rst));
  Register #(.width(16)) register_24 (
    .D(RegF_WD), .en(decoder_1_out7), .clk(clock_1_out), .Q(register_24_q), .clr(RegF_rst));
  Register #(.width(16)) register_25 (
    .D(RegF_WD), .en(decoder_1_out8), .clk(clock_1_out), .Q(register_25_q), .clr(RegF_rst));
  Register #(.width(16)) register_26 (
    .D(RegF_WD), .en(decoder_1_out9), .clk(clock_1_out), .Q(register_26_q), .clr(RegF_rst));
  Register #(.width(16)) register_27 (
    .D(RegF_WD), .en(decoder_1_out10), .clk(clock_1_out), .Q(register_27_q), .clr(RegF_rst));
  Register #(.width(16)) register_28 (
    .D(RegF_WD), .en(decoder_1_out11), .clk(clock_1_out), .Q(register_28_q), .clr(RegF_rst));
  Register #(.width(16)) register_29 (
    .D(RegF_WD), .en(decoder_1_out12), .clk(clock_1_out), .Q(register_29_q), .clr(RegF_rst));
  Register #(.width(16)) register_30 (
    .D(RegF_WD), .en(decoder_1_out13), .clk(clock_1_out), .Q(register_30_q), .clr(RegF_rst));
  Register #(.width(16)) register_31 (
    .D(RegF_WD), .en(decoder_1_out14), .clk(clock_1_out), .Q(register_31_q), .clr(RegF_rst));
  Register #(.width(16)) register_32 (
    .D(RegF_WD), .en(decoder_1_out15), .clk(clock_1_out), .Q(register_32_q), .clr(RegF_rst));
  Multiplexer #(.select(5), .width(16)) multiplexer_1 (
    .in0(register_17_q), .in1(register_18_q), .in2(register_19_q), .in3(register_20_q), .in4(register_21_q),
    .in5(register_22_q), .in6(register_23_q), .in7(register_24_q), .in8(register_25_q), .in9(register_26_q),
    .in10(register_27_q), .in11(register_28_q), .in12(register_29_q), .in13(register_30_q),
    .in14(register_31_q), .in15(register_32_q), .in16(register_1_q), .in17(register_2_q),
    .in18(register_3_q), .in19(register_4_q), .in20(register_5_q), .in21(register_6_q), .in22(register_7_q),
    .in23(register_8_q), .in24(register_9_q), .in25(register_10_q), .in26(register_11_q),
    .in27(register_12_q), .in28(register_13_q), .in29(register_14_q), .in30(register_15_q),
    .in31(register_16_q), .out(RegF_D1), .sel(RegF_A1));
  Multiplexer #(.select(5), .width(16)) multiplexer_2 (
    .in0(register_17_q), .in1(register_18_q), .in2(register_19_q), .in3(register_20_q), .in4(register_21_q),
    .in5(register_22_q), .in6(register_23_q), .in7(register_24_q), .in8(register_25_q), .in9(register_26_q),
    .in10(register_27_q), .in11(register_28_q), .in12(register_29_q), .in13(register_30_q),
    .in14(register_31_q), .in15(register_32_q), .in16(register_1_q), .in17(register_2_q),
    .in18(register_3_q), .in19(register_4_q), .in20(register_5_q), .in21(register_6_q), .in22(register_7_q),
    .in23(register_8_q), .in24(register_9_q), .in25(register_10_q), .in26(register_11_q),
    .in27(register_12_q), .in28(register_13_q), .in29(register_14_q), .in30(register_15_q),
    .in31(register_16_q), .out(RegF_D2), .sel(RegF_A2));

  // Other names for the same wires on the sheet: RegF_bus_A[15:0] = RegF_D1; RegF_bus_B[15:0] = RegF_D2;
  //   RegF_D_in[15:0] = RegF_WD; RegF_reset = RegF_rst
endmodule

module Pipeline_ID (
  input  WE,
  input  [15:0] Inst_Cache_1_IN,
  input  [15:0] Inst_Cache_2_IN,
  output [15:0] Inst_1_out,
  output [15:0] Inst_2_out
);

  wire reset, undriven;

  Register #(.width(16)) register_1 (.D(Inst_Cache_1_IN), .en(undriven), .clk(WE), .Q(Inst_1_out), .clr(reset));
  Clock clock_1 (.out(WE));
  Register #(.width(16)) register_2 (.D(Inst_Cache_2_IN), .en(undriven), .clk(WE), .Q(Inst_2_out), .clr(reset));
endmodule
