// Logisim project Dragon_5.circ as structural Verilog: 8 circuits, main circuit main
module main (
);

  Pipeline_ID ID_Stage ();  // open: Inst_Cache_1_IN, Inst_Cache_2_IN, WE, Inst_1_out, Inst_2_out
  Register_File reg_file ();  // open: RegF_rst, RegF_WE, RegF_A1, RegF_A2, RegF_A3, RegF_WD, RegF_D1, RegF_D2
  ALU Arithmetic_logic_Unit ();  // open: ALU_OP_IN, ALU_A_IN, ALU_B_IN, ALU_FLAG_IN, ALU_RES_OUT, ALU_FLAG_OUT
endmodule

module ALU (
  input  [3:0] ALU_OP_IN,
  input  [15:0] ALU_A_IN,
  input  [15:0] ALU_B_IN,
  input  [15:0] ALU_FLAG_IN,
  output [15:0] ALU_RES_OUT,
  output [15:0] ALU_FLAG_OUT
);

  wire adder_1_cout, adder_2_cout, adder_3_cout;
  wire [15:0] adder_1_out;

  Pull_Resistor pull_resistor_1 (.node(ALU_RES_OUT));
  Adder #(.width(4)) adder_1 (
    .a(ALU_A_IN[3:0]), .b(ALU_B_IN[3:0]), .out(adder_1_out[3:0]), .cout(adder_1_cout));  // open: cin
  Adder #(.width(4)) adder_2 (
    .a(ALU_A_IN[7:4]), .b(ALU_B_IN[7:4]), .out(adder_1_out[7:4]), .cin(adder_1_cout), .cout(adder_2_cout));
  Adder #(.width(4)) adder_3 (
    .a(ALU_A_IN[11:8]), .b(ALU_B_IN[11:8]), .out(adder_1_out[11:8]), .cin(adder_2_cout), .cout(adder_3_cout));
  Adder #(.width(4)) adder_4 (
    .a(ALU_A_IN[15:12]), .b(ALU_B_IN[15:12]), .out(adder_1_out[15:12]), .cin(adder_3_cout));  // open: cout
  Controlled_Buffer #(.width(16)) controlled_buffer_1 (.in(adder_1_out));  // open: out, en

  // Other names for the same wires on the sheet: ALU_A[15:0] = ALU_A_IN; ALU_B[15:0] = ALU_B_IN;
  //   ALU_OP[3:0] = ALU_OP_IN; ALU_RES[15:0] = ALU_RES_OUT
endmodule

module Register_File (
  input  RegF_rst,
  input  RegF_WE,
  input  [4:0] RegF_A1,
  input  [4:0] RegF_A2,
  input  [4:0] RegF_A3,
  input  [15:0] RegF_WD,
  output [15:0] RegF_D1,
  output [15:0] RegF_D2
);

  wire clock_1_out;
  wire [4:0] multiplexer_1_out, multiplexer_2_out;
  wire [15:0] bit_extender_1_out, bit_extender_2_out;

  assign bit_extender_1_out = {{11{1'b0}}, multiplexer_1_out};  // Bit_Extender bit_extender_1
  Multiplexer #(.width(5)) multiplexer_1 (.in0(RegF_A1), .in1(RegF_A3), .out(multiplexer_1_out), .sel(RegF_WE));
  Clock clock_1 (.out(clock_1_out));
  assign bit_extender_2_out = {{11{1'b0}}, multiplexer_2_out};  // Bit_Extender bit_extender_2
  Multiplexer #(.width(5)) multiplexer_2 (.in0(RegF_A2), .in1(RegF_A3), .out(multiplexer_2_out), .sel(RegF_WE));
  RAM #(.addrWidth(16), .dataWidth(16)) ram_1 (
    .addr(bit_extender_1_out), .we(RegF_WE), .oe(1'b1), .clk(clock_1_out), .din(RegF_WD), .dout(RegF_D1));
  RAM #(.addrWidth(16), .dataWidth(16)) ram_2 (
    .addr(bit_extender_2_out), .we(RegF_WE), .oe(1'b1), .clk(clock_1_out), .din(RegF_WD), .dout(RegF_D2));

  // Other names for the same wires on the sheet: RegF_bus_A[15:0] = RegF_D1; RegF_bus_B[15:0] = RegF_D2;
  //   RegF_D_in[15:0] = RegF_WD; RegF_reset = RegF_rst
endmodule

module Pipeline_ID (
  input  WE,
  input  [15:0] Inst_Cache_1_IN,
  input  [15:0] Inst_Cache_2_IN,
  output [15:0] Inst_1_out,
  output [15:0] Inst_2_out
);

  wire reset, undriven;

  Register #(.width(16)) register_1 (.D(Inst_Cache_1_IN), .en(undriven), .clk(WE), .Q(Inst_1_out), .clr(reset));
  Clock clock_1 (.out(WE));
  Register #(.width(16)) register_2 (.D(Inst_Cache_2_IN), .en(undriven), .clk(WE), .Q(Inst_2_out), .clr(reset));
endmodule

module Instruction_Cache (
  input  [15:0] InstC_A,
  input  [7:0] InstC_MBR,
  input  [15:0] InstC_RAM_data,
  input  InstC_CU_Acc,
  input  InstC_reset,
  input  InstC_lookup,
  input  InstC_invalidate,
  output [15:0] InstC_RAM_A_BUS,
  output [7:0] InstC_RAM_MBR,
  output [15:0] InstC_out_port1,
  output InstC_CU_Stall_Req,
  output [15:0] InstC_out_port2
);

  wire adder_1_cout, adder_2_cout, adder_3_cout, and_1_out, and_2_out, and_4_out, clock_1_out, clock_2_out,
       clock_3_out, clock_4_out, comparator_1_eq, comparator_1_gt, comparator_1_lt, counter_1_carry,
       not_1_out, not_2_out, not_3_out, not_4_out, not_5_out, or_1_out, or_2_out, or_3_out, s_r_ff_1_qn,
       undriven, undriven_2, undriven_3, undriven_4;
  wire [3:0] counter_1_q;
  wire [7:0] adder_2_out, intr_cache_tag_sram_dout, multiplexer_2_out_2;
  wire [7:7] multiplexer_2_out;
  wire [15:0] adder_1_out, adder_3_out, bit_extender_1_out, multiplexer_1_out;

  and and_1 (and_1_out, counter_1_carry, clock_2_out);
  Counter #(.max('hf), .width(4)) counter_1 (
    .clr(or_1_out), .load(1'b0), .up(1'b1), .count(InstC_CU_Acc), .clk(clock_1_out), .D(4'b0000),
    .carry(counter_1_carry), .Q(counter_1_q));
  or or_1 (or_1_out, InstC_reset, and_1_out);
  Clock clock_1 (.out(clock_1_out));
  Clock clock_2 (.out(clock_2_out));
  assign bit_extender_1_out = {{12{1'b0}}, counter_1_q};  // Bit_Extender bit_extender_1
  S_R_Flip_Flop s_r_ff_1 (
    .S(undriven_2), .R(undriven_3), .clk(undriven_4), .Q(InstC_CU_Stall_Req), .reset(or_2_out),
    .Qn(s_r_ff_1_qn), .preset(and_2_out));
  // NoConnect on undriven_2
  // NoConnect on undriven_3
  // NoConnect on undriven_4
  or or_2 (or_2_out, counter_1_carry, InstC_reset);
  // NoConnect on undriven
  Adder #(.width(16)) adder_1 (
    .a(InstC_A), .b(bit_extender_1_out), .out(adder_1_out), .cin(undriven), .cout(adder_1_cout));
  Adder adder_2 (.a(InstC_MBR), .b({8{1'b0}}), .out(adder_2_out), .cin(adder_1_cout), .cout(adder_2_cout));
  // NoConnect on adder_2_cout
  Multiplexer #(.width(16)) multiplexer_1 (
    .in0(InstC_A), .in1(adder_1_out), .out(multiplexer_1_out), .sel(InstC_CU_Stall_Req));
  // NoConnect on s_r_ff_1_qn
  not not_1 (not_1_out, and_4_out);
  and and_2 (and_2_out, not_1_out, InstC_lookup);
  Multiplexer #(.width(8)) multiplexer_2 (
    .in0(InstC_MBR), .in1(adder_2_out), .out({multiplexer_2_out[7], multiplexer_2_out_2[6:0]}),
    .sel(InstC_CU_Stall_Req));
  // NoConnect on multiplexer_2_out[7]
  not not_2 (not_2_out, InstC_invalidate);
  and and_3 (multiplexer_2_out_2[7], not_2_out, InstC_CU_Acc);
  assign InstC_RAM_A_BUS = InstC_CU_Acc ? adder_1_out : 16'bz;  // Controlled_Buffer controlled_buffer_1
  assign InstC_RAM_MBR = InstC_CU_Acc ? adder_2_out : 8'bz;  // Controlled_Buffer controlled_buffer_2
  Clock clock_3 (.out(clock_3_out));
  or or_3 (or_3_out, counter_1_carry, and_4_out);
  not not_3 (not_3_out, clock_3_out);
  RAM #(.addrWidth(16), .asyncread("true")) intr_cache_tag_sram (
    .addr(multiplexer_1_out), .we(InstC_CU_Acc), .oe(1'b1), .clk(not_3_out), .din(multiplexer_2_out_2),
    .dout(intr_cache_tag_sram_dout));
  // NoConnect on InstC_MBR[7]
  // NoConnect on comparator_1_gt
  Comparator #(.mode("unsigned"), .width(7)) comparator_1 (
    .a(intr_cache_tag_sram_dout[6:0]), .b(InstC_MBR[6:0]), .gt(comparator_1_gt), .eq(comparator_1_eq),
    .lt(comparator_1_lt));
  // NoConnect on comparator_1_lt
  and and_4 (and_4_out, comparator_1_eq, intr_cache_tag_sram_dout[7]);
  not not_4 (not_4_out, InstC_CU_Acc);
  Adder #(.width(16)) adder_3 (
    .a(multiplexer_1_out), .b({16{1'b0}}), .out(adder_3_out), .cin(not_4_out), .cout(adder_3_cout));
  // NoConnect on adder_3_cout
  Clock clock_4 (.out(clock_4_out));
  not not_5 (not_5_out, clock_4_out);
  RAM #(.addrWidth(16), .dataWidth(16)) InstC_sram_data1 (
    .addr(multiplexer_1_out), .we(InstC_CU_Acc), .oe(or_3_out), .clk(not_5_out), .din(InstC_RAM_data),
    .dout(InstC_out_port1));
  RAM #(.addrWidth(16), .dataWidth(16)) InstC_sram_data2 (
    .addr(adder_3_out), .we(InstC_CU_Acc), .oe(or_3_out), .clk(not_5_out), .din(InstC_RAM_data),
    .dout(InstC_out_port2));

  // Notes on the sheet:
  //   to clear cache, invalidate and go thorugh every address with CU
  //   tag
  //   valid bit
  //   index + offset
  //   tag + meta data
  //   7-bit tag | 1 valid bit
  //   valid
  //   tag
  //   Cache Hit
  //   data
endmodule

module Data_Cache (
  input  [15:0] DataC_RAM_in,
  input  [15:0] DataC_A,
  input  [7:0] DataC_MBR,
  input  [15:0] DataC_data_in,
  input  DataC_CU_Acc,
  input  DataC_reset,
  input  DataC_CPU_write,
  input  DataC_lookup,
  input  DataC_invalidate,
  output [15:0] DataC_RAM_A_BUS,
  output [7:0] DataC_RAM_MBR,
  output [15:0] DataC_data_Out,
  output DataC_CU_bypass,
  output DataC_CU_Stall_Req
);

  wire adder_1_cout, adder_2_cout, and_1_out, and_2_out, and_3_out, and_5_out, and_6_out, and_7_out,
       and_8_out, clock_1_out, clock_2_out, clock_3_out, comparator_1_eq, comparator_1_gt, comparator_1_lt,
       comparator_2_eq, comparator_2_gt, comparator_2_lt, counter_1_carry, not_1_out, not_2_out, not_3_out,
       not_4_out, not_5_out, or_1_out, or_2_out, or_3_out, or_4_out, or_5_out, s_r_ff_1_qn, undriven,
       undriven_2, undriven_3, undriven_4;
  wire [3:0] counter_1_q;
  wire [7:0] adder_2_out, DataC_tag_sram_dout, multiplexer_2_out_2;
  wire [7:7] multiplexer_2_out;
  wire [15:0] adder_1_out, bit_extender_1_out, multiplexer_1_out, multiplexer_3_out;

  Clock clock_1 (.out(clock_1_out));
  and and_1 (and_1_out, counter_1_carry, clock_2_out);
  Counter #(.max('hf), .width(4)) counter_1 (
    .clr(or_1_out), .load(1'b0), .up(1'b1), .count(DataC_CU_Acc), .clk(clock_1_out), .D(4'b0000),
    .carry(counter_1_carry), .Q(counter_1_q));
  or or_1 (or_1_out, DataC_reset, and_1_out);
  Clock clock_2 (.out(clock_2_out));
  assign bit_extender_1_out = {{12{1'b0}}, counter_1_q};  // Bit_Extender bit_extender_1
  // NoConnect on undriven
  // NoConnect on adder_2_cout
  S_R_Flip_Flop s_r_ff_1 (
    .S(undriven_2), .R(undriven_3), .clk(undriven_4), .Q(DataC_CU_Stall_Req), .reset(or_2_out),
    .Qn(s_r_ff_1_qn), .preset(and_3_out));
  // NoConnect on undriven_2
  // NoConnect on undriven_3
  // NoConnect on undriven_4
  // NoConnect on s_r_ff_1_qn
  or or_2 (or_2_out, counter_1_carry, DataC_reset);
  or or_3 (or_3_out, DataC_CPU_write, DataC_CU_Acc);
  Adder #(.width(16)) adder_1 (
    .a(DataC_A), .b(bit_extender_1_out), .out(adder_1_out), .cin(undriven), .cout(adder_1_cout));
  Adder adder_2 (.a(DataC_MBR), .b({8{1'b0}}), .out(adder_2_out), .cin(adder_1_cout), .cout(adder_2_cout));
  Multiplexer #(.width(16)) multiplexer_1 (.in0(DataC_A), .in1(adder_1_out), .out(multiplexer_1_out), .sel(and_2_out));
  and and_2 (and_2_out, not_1_out, DataC_CU_Stall_Req);
  not not_1 (not_1_out, DataC_CPU_write);
  not not_2 (not_2_out, or_5_out);
  and and_3 (and_3_out, not_2_out, DataC_lookup);
  Multiplexer #(.width(8)) multiplexer_2 (
    .in0(DataC_MBR), .in1(adder_2_out), .out({multiplexer_2_out[7], multiplexer_2_out_2[6:0]}),
    .sel(DataC_CU_Stall_Req));
  // NoConnect on multiplexer_2_out[7]
  not not_3 (not_3_out, DataC_invalidate);
  and and_4 (multiplexer_2_out_2[7], not_3_out, or_3_out);
  not not_4 (not_4_out, DataC_CU_bypass);
  and and_5 (and_5_out, DataC_CU_Acc, not_4_out);
  assign DataC_RAM_A_BUS = and_5_out ? adder_1_out : 16'bz;  // Controlled_Buffer controlled_buffer_1
  assign DataC_RAM_MBR = and_5_out ? adder_2_out : 8'bz;  // Controlled_Buffer controlled_buffer_2
  Clock clock_3 (.out(clock_3_out));
  RAM #(.addrWidth(16), .dataWidth(16)) ram_1 (
    .addr(multiplexer_1_out), .we(or_3_out), .oe(or_4_out), .clk(not_5_out), .din(multiplexer_3_out),
    .dout(DataC_data_in));
  or or_4 (or_4_out, counter_1_carry, or_5_out);
  Multiplexer #(.width(16)) multiplexer_3 (
    .in0(DataC_data_in), .in1(DataC_RAM_in), .out(multiplexer_3_out), .sel(or_3_out));
  RAM #(.addrWidth(16), .asyncread("true")) DataC_tag_sram (
    .addr(multiplexer_1_out), .we(or_3_out), .oe(1'b1), .clk(not_5_out), .din(multiplexer_2_out_2),
    .dout(DataC_tag_sram_dout));
  not not_5 (not_5_out, clock_3_out);
  // NoConnect on DataC_MBR[7]
  // NoConnect on comparator_1_gt
  Comparator #(.mode("unsigned"), .width(7)) comparator_1 (
    .a(DataC_tag_sram_dout[6:0]), .b(DataC_MBR[6:0]), .gt(comparator_1_gt), .eq(comparator_1_eq),
    .lt(comparator_1_lt));
  // NoConnect on comparator_1_lt
  and and_6 (and_6_out, comparator_1_eq, DataC_tag_sram_dout[7]);
  // NoConnect on comparator_2_gt
  Comparator #(.mode("unsigned")) comparator_2 (
    .a(DataC_MBR), .b({8{1'b0}}), .gt(comparator_2_gt), .eq(comparator_2_eq), .lt(comparator_2_lt));
  // NoConnect on comparator_2_lt
  or or_5 (or_5_out, and_6_out, DataC_CU_bypass);
  or or_6 (DataC_CU_bypass, DataC_CPU_write, and_7_out);
  // NoConnect on DataC_A[0]
  // NoConnect on DataC_A[1]
  // NoConnect on DataC_A[2]
  // NoConnect on DataC_A[3]
  // NoConnect on DataC_A[4]
  // NoConnect on DataC_A[5]
  // NoConnect on DataC_A[6]
  // NoConnect on DataC_A[7]
  and and_7 (and_7_out, DataC_A[11], comparator_2_eq);
  // NoConnect on DataC_A[8]
  // NoConnect on DataC_A[9]
  // NoConnect on DataC_A[10]
  // NoConnect on DataC_A[12]
  // NoConnect on DataC_A[13]
  // NoConnect on DataC_A[14]
  // NoConnect on DataC_A[15]
  and and_8 (and_8_out, DataC_CU_bypass, DataC_CU_Acc);
  assign DataC_RAM_A_BUS = and_8_out ? DataC_A : 16'bz;  // Controlled_Buffer controlled_buffer_3
  assign DataC_RAM_MBR = and_8_out ? DataC_MBR : 8'bz;  // Controlled_Buffer controlled_buffer_4

  assign DataC_data_Out = DataC_data_in;

  // Other names for the same wires on the sheet: DataC_data[15:0] = DataC_data_in

  // Notes on the sheet:
  //   to clear cache, invalidate and go thorugh every address with CU
  //   tag
  //   index + offset
  //   valid bit
  //   data
  //   tag + meta data
  //   7-bit tag | 1 valid bit
  //   valid
  //   tag
  //   Cache Hit
  //   bypass cache
  //   if address is or above 0xF800
  //   0xF800 = 0b1111 1000 0000 0000
  //   CU is responsible to connect Data lines to CPU and address lines from cache to ram
endmodule

module memory_card (
  input  [15:0] mem_card_data_bus_in,
  input  [15:0] mem_card_addr_bus_in,
  input  [1:0] mem_card_bank_select,
  input  mem_card_write,
  input  mem_card_load,
  input  mem_card_enable,
  output [15:0] mem_card_data_bus_out,
  output [15:0] mem_card_addr_bus_out,
  output mem_card_present
);

  wire and_1_out, and_2_out, and_3_out, and_4_out, and_5_out, and_6_out, and_7_out, and_8_out, clock_1_out,
       clock_2_out, decoder_1_out0, decoder_1_out1, decoder_1_out2, decoder_1_out3;
  wire [15:0] ram_1_dout, ram_2_dout, ram_3_dout, ram_4_dout;

  Decoder #(.select(2)) decoder_1 (
    .out0(decoder_1_out0), .out1(decoder_1_out1), .out2(decoder_1_out2), .out3(decoder_1_out3),
    .sel(mem_card_bank_select), .en(mem_card_enable));
  and and_1 (and_1_out, mem_card_write, decoder_1_out0);
  and and_2 (and_2_out, mem_card_write, decoder_1_out1);
  and and_3 (and_3_out, mem_card_write, decoder_1_out2);
  and and_4 (and_4_out, mem_card_write, decoder_1_out3);
  and and_5 (and_5_out, mem_card_load, decoder_1_out0);
  and and_6 (and_6_out, mem_card_load, decoder_1_out1);
  and and_7 (and_7_out, mem_card_load, decoder_1_out2);
  and and_8 (and_8_out, mem_card_load, decoder_1_out3);
  Clock clock_1 (.out(clock_1_out));
  RAM #(.addrWidth(16), .dataWidth(16)) ram_1 (
    .addr(mem_card_addr_bus_in), .we(and_1_out), .oe(1'b1), .clk(clock_1_out), .din(mem_card_data_bus_in),
    .dout(ram_1_dout));
  RAM #(.addrWidth(16), .dataWidth(16)) ram_2 (
    .addr(mem_card_addr_bus_in), .we(and_2_out), .oe(1'b1), .clk(clock_1_out), .din(mem_card_data_bus_in),
    .dout(ram_2_dout));
  assign mem_card_data_bus_in = and_5_out ? ram_1_dout : 16'bz;  // Controlled_Buffer controlled_buffer_1
  assign mem_card_data_bus_in = and_6_out ? ram_2_dout : 16'bz;  // Controlled_Buffer controlled_buffer_2
  Clock clock_2 (.out(clock_2_out));
  RAM #(.addrWidth(16), .dataWidth(16)) ram_3 (
    .addr(mem_card_addr_bus_in), .we(and_3_out), .oe(1'b1), .clk(clock_2_out), .din(mem_card_data_bus_in),
    .dout(ram_3_dout));
  RAM #(.addrWidth(16), .dataWidth(16)) ram_4 (
    .addr(mem_card_addr_bus_in), .we(and_4_out), .oe(1'b1), .clk(clock_2_out), .din(mem_card_data_bus_in),
    .dout(ram_4_dout));
  assign mem_card_data_bus_in = and_7_out ? ram_3_dout : 16'bz;  // Controlled_Buffer controlled_buffer_3
  assign mem_card_data_bus_in = and_8_out ? ram_4_dout : 16'bz;  // Controlled_Buffer controlled_buffer_4

  assign mem_card_addr_bus_out = mem_card_addr_bus_in;
  assign mem_card_data_bus_out = mem_card_data_bus_in;
  assign mem_card_present = 1'b1;

  // Other names for the same wires on the sheet: mem_card_addr_bus[15:0] = mem_card_addr_bus_in;
  //   mem_card_data_bus[15:0] = mem_card_data_bus_in
endmodule

module mem_controller (
  input  memCtr_present1,
  input  memCtr_present2,
  input  [15:0] memCtr_addr,
  input  memCtr_present3,
  input  memCtr_present4,
  input  memCtr_present5,
  input  [7:0] memCtr_MBR,
  input  memCtr_present6,
  input  memCtr_present7,
  input  memCtr_present8,
  input  [15:0] memCtr_data_bus_in,
  input  memCtr_write_bus,
  input  memCtr_read_bus,
  input  memCtr_CU_bus_permission,
  input  memCtr_IO_READY,
  input  memCtr_CU_write,
  input  memCtr_CU_load,
  output [15:0] memCtr_data_bus_out,
  output [1:0] memCtr_select1,
  output [1:0] memCtr_select2,
  output [1:0] memCtr_select3,
  output [1:0] memCtr_select4,
  output [1:0] memCtr_select5,
  output [1:0] memCtr_select6,
  output [1:0] memCtr_select7,
  output [1:0] memCtr_select8,
  output memCtr_CU_pipeline_stall_req,
  output memCtr_enable1,
  output memCtr_enable2,
  output memCtr_enable3,
  output memCtr_enable4,
  output memCtr_enable5,
  output memCtr_enable6,
  output memCtr_enable7,
  output memCtr_enable8
);

  wire and_1_out, comparator_1_eq, comparator_1_gt, comparator_1_lt, not_1_out, not_2_out;

  Decoder #(.select(3)) decoder_1 (
    .out0(memCtr_enable1), .out1(memCtr_enable2), .out2(memCtr_enable3), .out3(memCtr_enable4),
    .out4(memCtr_enable5), .out5(memCtr_enable6), .out6(memCtr_enable7), .out7(memCtr_enable8),
    .sel(memCtr_MBR[4:2]), .en(not_1_out));
  // NoConnect on comparator_1_gt
  Comparator #(.mode("unsigned")) comparator_1 (
    .a(memCtr_MBR), .b({8{1'b0}}), .gt(comparator_1_gt), .eq(comparator_1_eq), .lt(comparator_1_lt));
  // NoConnect on comparator_1_lt
  not not_1 (not_1_out, and_1_out);
  and and_1 (and_1_out, memCtr_addr[11], comparator_1_eq);
  and and_2 (memCtr_CU_pipeline_stall_req, and_1_out, not_2_out);
  not not_2 (not_2_out, memCtr_IO_READY);

  assign memCtr_data_bus_out = memCtr_data_bus_in;
  assign memCtr_read_bus = memCtr_CU_load;
  assign memCtr_select1 = memCtr_MBR[1:0];
  assign memCtr_select2 = memCtr_MBR[1:0];
  assign memCtr_select3 = memCtr_MBR[1:0];
  assign memCtr_select4 = memCtr_MBR[1:0];
  assign memCtr_select5 = memCtr_MBR[1:0];
  assign memCtr_select6 = memCtr_MBR[1:0];
  assign memCtr_select7 = memCtr_MBR[1:0];
  assign memCtr_select8 = memCtr_MBR[1:0];
  assign memCtr_write_bus = memCtr_CU_write;

  // Other names for the same wires on the sheet: memCtr_addr_bus_slot1[15:0] = memCtr_addr;
  //   memCtr_addr_bus_slot2[15:0] = memCtr_addr; memCtr_addr_bus_slot3[15:0] = memCtr_addr;
  //   memCtr_addr_bus_slot4[15:0] = memCtr_addr; memCtr_addr_bus_slot5[15:0] = memCtr_addr;
  //   memCtr_addr_bus_slot6[15:0] = memCtr_addr; memCtr_addr_bus_slot7[15:0] = memCtr_addr;
  //   memCtr_addr_bus_slot8[15:0] = memCtr_addr; memCtr_IO_addr[15:0] = memCtr_addr;
  //   memCtr_bus_perm = memCtr_CU_bus_permission; memCtr_data[15:0] = memCtr_data_bus_in;
  //   memCtr_data_bus_slot1[15:0] = memCtr_data_bus_in; memCtr_data_bus_slot2[15:0] = memCtr_data_bus_in;
  //   memCtr_data_bus_slot3[15:0] = memCtr_data_bus_in; memCtr_data_bus_slot4[15:0] = memCtr_data_bus_in;
  //   memCtr_data_bus_slot5[15:0] = memCtr_data_bus_in; memCtr_data_bus_slot6[15:0] = memCtr_data_bus_in;
  //   memCtr_data_bus_slot7[15:0] = memCtr_data_bus_in; memCtr_data_bus_slot8[15:0] = memCtr_data_bus_in;
  //   memCtr_IO_data[15:0] = memCtr_data_bus_in; memCtr_pipe_stall_req = memCtr_CU_pipeline_stall_req
endmodule
