// Logisim project 8bit computer.circ as structural Verilog: 3 circuits, main circuit main
module main (
  input  AI,
  input  BI,
  input  CLRA,
  input  CLRB,
  input  AO,
  input  BO,
  input  in_7,
  input  in_8,
  input  in_9,
  input  in_10,
  input  in_11,
  input  in_12,
  input  in_13,
  input  in_14,
  input  in_15,
  input  SUB,
  input  EO,
  input  MAI,
  input  in_19,
  input  OE,
  input  CLR,
  input  WE,
  input  in_23,
  input  [3:0] in_24,
  input  [7:0] in_25
);

  wire adder_1_cout, adder_1_out, adder_2_cout, adder_2_out, adder_3_cout, adder_3_out, adder_4_cout,
       adder_4_out, adder_5_cout, adder_5_out, adder_6_cout, adder_6_out, adder_7_cout, adder_7_out,
       adder_8_out, and_1_out, and_2_out, and_3_out, and_4_out, and_5_out, and_6_out, and_7_out, and_8_out,
       and_9_out, and_10_out, and_11_out, and_12_out, and_13_out, and_14_out, and_15_out, and_16_out,
       and_17_out, and_18_out, and_19_out, and_20_out, and_21_out, and_22_out, and_23_out, and_24_out,
       and_25_out, and_26_out, and_27_out, and_28_out, and_29_out, and_30_out, and_31_out, and_32_out,
       and_33_out, and_34_out, and_35_out, and_36_out, and_37_out, and_38_out, and_39_out, and_40_out,
       and_41_out, and_42_out, and_43_out, and_44_out, and_45_out, and_46_out, and_47_out, and_48_out,
       and_49_out, and_50_out, and_51_out, and_52_out, and_53_out, and_54_out, and_55_out, and_56_out,
       and_57_out, and_58_out, and_59_out, and_60_out, and_61_out, and_62_out, and_63_out, and_64_out,
       and_65_out, and_66_out, and_67_out, and_68_out, and_69_out, button_1_out, clock_1_out, d_ff_1_q,
       d_ff_2_q, d_ff_3_q, d_ff_4_q, d_ff_5_q, d_ff_6_q, d_ff_7_q, d_ff_8_q, d_ff_9_q, d_ff_10_q, d_ff_11_q,
       d_ff_12_q, d_ff_13_q, d_ff_14_q, d_ff_15_q, d_ff_16_q, d_ff_17_q, d_ff_18_q, d_ff_19_q, d_ff_20_q,
       j_k_ff_1_q, j_k_ff_1_qn, not_1_out, not_2_out, not_3_out, not_4_out, not_5_out, not_6_out, or_1_out,
       or_2_out, or_3_out, or_4_out, or_5_out, or_6_out, or_7_out, or_8_out, or_9_out, or_10_out, or_11_out,
       or_12_out, or_13_out, or_14_out, or_15_out, or_16_out, or_17_out, or_18_out, or_19_out, or_20_out,
       or_33_out, or_34_out, or_35_out, or_36_out, undriven, undriven_2, undriven_3, undriven_4, undriven_5,
       xor_1_out, xor_2_out, xor_3_out, xor_4_out, xor_5_out, xor_6_out, xor_7_out, xor_8_out;
  wire [3:0] or_21_out;
  wire [7:0] controlled_buffer_1_out, or_25_out;

  not not_1 (not_1_out, AI);
  not not_2 (not_2_out, BI);
  not not_3 (not_3_out, MAI);
  LED led_1 (.in(in_23));
  and and_1 (and_1_out, d_ff_1_q, not_1_out);
  and and_2 (and_2_out, AI, controlled_buffer_1_out[0]);
  and and_3 (and_3_out, d_ff_2_q, not_1_out);
  and and_4 (and_4_out, AI, controlled_buffer_1_out[1]);
  and and_5 (and_5_out, d_ff_3_q, not_1_out);
  and and_6 (and_6_out, AI, controlled_buffer_1_out[2]);
  and and_7 (and_7_out, d_ff_4_q, not_1_out);
  and and_8 (and_8_out, AI, controlled_buffer_1_out[3]);
  and and_9 (and_9_out, d_ff_5_q, not_1_out);
  and and_10 (and_10_out, AI, controlled_buffer_1_out[4]);
  and and_11 (and_11_out, d_ff_6_q, not_1_out);
  and and_12 (and_12_out, AI, controlled_buffer_1_out[5]);
  and and_13 (and_13_out, d_ff_7_q, not_1_out);
  and and_14 (and_14_out, AI, controlled_buffer_1_out[6]);
  and and_15 (and_15_out, d_ff_8_q, not_1_out);
  and and_16 (and_16_out, AI, controlled_buffer_1_out[7]);
  and and_17 (and_17_out, d_ff_9_q, not_2_out);
  and and_18 (and_18_out, BI, controlled_buffer_1_out[0]);
  and and_19 (and_19_out, d_ff_10_q, not_2_out);
  and and_20 (and_20_out, BI, controlled_buffer_1_out[1]);
  and and_21 (and_21_out, d_ff_11_q, not_2_out);
  and and_22 (and_22_out, BI, controlled_buffer_1_out[2]);
  and and_23 (and_23_out, d_ff_12_q, not_2_out);
  and and_24 (and_24_out, BI, controlled_buffer_1_out[3]);
  and and_25 (and_25_out, d_ff_13_q, not_2_out);
  and and_26 (and_26_out, BI, controlled_buffer_1_out[4]);
  and and_27 (and_27_out, d_ff_14_q, not_2_out);
  and and_28 (and_28_out, BI, controlled_buffer_1_out[5]);
  and and_29 (and_29_out, d_ff_15_q, not_2_out);
  and and_30 (and_30_out, BI, controlled_buffer_1_out[6]);
  and and_31 (and_31_out, d_ff_16_q, not_2_out);
  and and_32 (and_32_out, BI, controlled_buffer_1_out[7]);
  and and_33 (and_33_out, d_ff_17_q, not_3_out);
  and and_34 (and_34_out, MAI, controlled_buffer_1_out[0]);
  and and_35 (and_35_out, d_ff_18_q, not_3_out);
  and and_36 (and_36_out, MAI, controlled_buffer_1_out[1]);
  and and_37 (and_37_out, d_ff_19_q, not_3_out);
  and and_38 (and_38_out, MAI, controlled_buffer_1_out[2]);
  and and_39 (and_39_out, d_ff_20_q, not_3_out);
  and and_40 (and_40_out, MAI, controlled_buffer_1_out[3]);
  Clock clock_1 (.out(clock_1_out));
  D_Flip_Flop d_ff_1 (.clk(clock_1_out), .D(or_1_out), .Q(d_ff_1_q), .reset(CLRA));  // open: Qn, preset, en
  or or_1 (or_1_out, and_1_out, and_2_out);
  D_Flip_Flop d_ff_2 (.clk(clock_1_out), .D(or_2_out), .Q(d_ff_2_q), .reset(CLRA));  // open: Qn, preset, en
  or or_2 (or_2_out, and_3_out, and_4_out);
  D_Flip_Flop d_ff_3 (.clk(clock_1_out), .D(or_3_out), .Q(d_ff_3_q), .reset(CLRA));  // open: Qn, preset, en
  or or_3 (or_3_out, and_5_out, and_6_out);
  D_Flip_Flop d_ff_4 (.clk(clock_1_out), .D(or_4_out), .Q(d_ff_4_q), .reset(CLRA));  // open: Qn, preset, en
  or or_4 (or_4_out, and_7_out, and_8_out);
  D_Flip_Flop d_ff_5 (.clk(clock_1_out), .D(or_5_out), .Q(d_ff_5_q), .reset(CLRA));  // open: Qn, preset, en
  or or_5 (or_5_out, and_9_out, and_10_out);
  D_Flip_Flop d_ff_6 (.clk(clock_1_out), .D(or_6_out), .Q(d_ff_6_q), .reset(CLRA));  // open: Qn, preset, en
  or or_6 (or_6_out, and_11_out, and_12_out);
  D_Flip_Flop d_ff_7 (.clk(clock_1_out), .D(or_7_out), .Q(d_ff_7_q), .reset(CLRA));  // open: Qn, preset, en
  or or_7 (or_7_out, and_13_out, and_14_out);
  D_Flip_Flop d_ff_8 (.clk(clock_1_out), .D(or_8_out), .Q(d_ff_8_q), .reset(CLRA));  // open: Qn, preset, en
  or or_8 (or_8_out, and_15_out, and_16_out);
  D_Flip_Flop d_ff_9 (.clk(clock_1_out), .D(or_9_out), .Q(d_ff_9_q), .reset(CLRB));  // open: Qn, preset, en
  or or_9 (or_9_out, and_17_out, and_18_out);
  D_Flip_Flop d_ff_10 (.clk(clock_1_out), .D(or_10_out), .Q(d_ff_10_q), .reset(CLRB));  // open: Qn, preset, en
  or or_10 (or_10_out, and_19_out, and_20_out);
  D_Flip_Flop d_ff_11 (.clk(clock_1_out), .D(or_11_out), .Q(d_ff_11_q), .reset(CLRB));  // open: Qn, preset, en
  or or_11 (or_11_out, and_21_out, and_22_out);
  D_Flip_Flop d_ff_12 (.clk(clock_1_out), .D(or_12_out), .Q(d_ff_12_q), .reset(CLRB));  // open: Qn, preset, en
  or or_12 (or_12_out, and_23_out, and_24_out);
  D_Flip_Flop d_ff_13 (.clk(clock_1_out), .D(or_13_out), .Q(d_ff_13_q), .reset(CLRB));  // open: Qn, preset, en
  or or_13 (or_13_out, and_25_out, and_26_out);
  D_Flip_Flop d_ff_14 (.clk(clock_1_out), .D(or_14_out), .Q(d_ff_14_q), .reset(CLRB));  // open: Qn, preset, en
  or or_14 (or_14_out, and_27_out, and_28_out);
  D_Flip_Flop d_ff_15 (.clk(clock_1_out), .D(or_15_out), .Q(d_ff_15_q), .reset(CLRB));  // open: Qn, preset, en
  or or_15 (or_15_out, and_29_out, and_30_out);
  D_Flip_Flop d_ff_16 (.clk(clock_1_out), .D(or_16_out), .Q(d_ff_16_q), .reset(CLRB));  // open: Qn, preset, en
  or or_16 (or_16_out, and_31_out, and_32_out);
  D_Flip_Flop d_ff_17 (.clk(clock_1_out), .D(or_17_out), .Q(d_ff_17_q), .reset(in_19));  // open: Qn, preset, en
  or or_17 (or_17_out, and_33_out, and_34_out);
  D_Flip_Flop d_ff_18 (.clk(clock_1_out), .D(or_18_out), .Q(d_ff_18_q), .reset(in_19));  // open: Qn, preset, en
  or or_18 (or_18_out, and_35_out, and_36_out);
  D_Flip_Flop d_ff_19 (.clk(clock_1_out), .D(or_19_out), .Q(d_ff_19_q), .reset(in_19));  // open: Qn, preset, en
  or or_19 (or_19_out, and_37_out, and_38_out);
  D_Flip_Flop d_ff_20 (.clk(clock_1_out), .D(or_20_out), .Q(d_ff_20_q), .reset(in_19));  // open: Qn, preset, en
  or or_20 (or_20_out, and_39_out, and_40_out);
  and and_41 (and_41_out, in_23, button_1_out);
  Button button_1 (.out(button_1_out));
  not not_4 (not_4_out, in_23);
  not not_5 (not_5_out, not_4_out);
  not not_6 (not_6_out, in_23);
  LED led_2 (.in(controlled_buffer_1_out[7]));
  and and_42 (and_42_out, not_5_out, in_24[0]);
  or or_21 (or_21_out[0], and_42_out, and_43_out);
  and and_43 (and_43_out, not_4_out, d_ff_17_q);
  and and_44 (and_44_out, not_5_out, in_24[1]);
  or or_22 (or_21_out[1], and_44_out, and_45_out);
  and and_45 (and_45_out, not_4_out, d_ff_18_q);
  and and_46 (and_46_out, not_5_out, in_24[2]);
  or or_23 (or_21_out[2], and_46_out, and_47_out);
  and and_47 (and_47_out, not_4_out, d_ff_19_q);
  and and_48 (and_48_out, not_5_out, in_24[3]);
  or or_24 (or_21_out[3], and_48_out, and_49_out);
  and and_49 (and_49_out, not_4_out, d_ff_20_q);
  and and_50 (and_50_out, not_6_out, controlled_buffer_1_out[0]);
  and and_51 (and_51_out, in_23, in_25[0]);
  and and_52 (and_52_out, not_6_out, controlled_buffer_1_out[1]);
  and and_53 (and_53_out, in_23, in_25[1]);
  and and_54 (and_54_out, not_6_out, controlled_buffer_1_out[2]);
  and and_55 (and_55_out, in_23, in_25[2]);
  and and_56 (and_56_out, not_6_out, controlled_buffer_1_out[3]);
  and and_57 (and_57_out, in_23, in_25[3]);
  and and_58 (and_58_out, not_6_out, controlled_buffer_1_out[4]);
  and and_59 (and_59_out, in_23, in_25[4]);
  and and_60 (and_60_out, not_6_out, controlled_buffer_1_out[5]);
  and and_61 (and_61_out, in_23, in_25[5]);
  and and_62 (and_62_out, not_6_out, controlled_buffer_1_out[6]);
  and and_63 (and_63_out, in_23, in_25[6]);
  and and_64 (and_64_out, not_6_out, controlled_buffer_1_out[7]);
  and and_65 (and_65_out, in_23, in_25[7]);
  LED led_3 (.in(controlled_buffer_1_out[4]));
  LED led_4 (.in(controlled_buffer_1_out[5]));
  LED led_5 (.in(controlled_buffer_1_out[6]));
  LED led_6 (.in(controlled_buffer_1_out[3]));
  Adder #(.width(1)) adder_1 (.a(d_ff_1_q), .b(xor_1_out), .out(adder_1_out), .cin(SUB), .cout(adder_1_cout));
  xor xor_1 (xor_1_out, SUB, d_ff_9_q);
  Adder #(.width(1)) adder_2 (.a(d_ff_2_q), .b(xor_2_out), .out(adder_2_out), .cin(adder_1_cout), .cout(adder_2_cout));
  xor xor_2 (xor_2_out, SUB, d_ff_10_q);
  Adder #(.width(1)) adder_3 (.a(d_ff_3_q), .b(xor_3_out), .out(adder_3_out), .cin(adder_2_cout), .cout(adder_3_cout));
  xor xor_3 (xor_3_out, SUB, d_ff_11_q);
  Adder #(.width(1)) adder_4 (.a(d_ff_4_q), .b(xor_4_out), .out(adder_4_out), .cin(adder_3_cout), .cout(adder_4_cout));
  xor xor_4 (xor_4_out, SUB, d_ff_12_q);
  Adder #(.width(1)) adder_5 (.a(d_ff_5_q), .b(xor_5_out), .out(adder_5_out), .cin(adder_4_cout), .cout(adder_5_cout));
  xor xor_5 (xor_5_out, SUB, d_ff_13_q);
  Adder #(.width(1)) adder_6 (.a(d_ff_6_q), .b(xor_6_out), .out(adder_6_out), .cin(adder_5_cout), .cout(adder_6_cout));
  xor xor_6 (xor_6_out, SUB, d_ff_14_q);
  Adder #(.width(1)) adder_7 (.a(d_ff_7_q), .b(xor_7_out), .out(adder_7_out), .cin(adder_6_cout), .cout(adder_7_cout));
  xor xor_7 (xor_7_out, SUB, d_ff_15_q);
  Adder #(.width(1)) adder_8 (.a(d_ff_8_q), .b(xor_8_out), .out(adder_8_out), .cin(adder_7_cout));  // open: cout
  xor xor_8 (xor_8_out, SUB, d_ff_16_q);
  assign controlled_buffer_1_out[0] = AO ? d_ff_1_q : 1'bz;  // Controlled_Buffer controlled_buffer_1
  assign controlled_buffer_1_out[1] = AO ? d_ff_2_q : 1'bz;  // Controlled_Buffer controlled_buffer_2
  assign controlled_buffer_1_out[2] = AO ? d_ff_3_q : 1'bz;  // Controlled_Buffer controlled_buffer_3
  assign controlled_buffer_1_out[3] = AO ? d_ff_4_q : 1'bz;  // Controlled_Buffer controlled_buffer_4
  assign controlled_buffer_1_out[4] = AO ? d_ff_5_q : 1'bz;  // Controlled_Buffer controlled_buffer_5
  assign controlled_buffer_1_out[5] = AO ? d_ff_6_q : 1'bz;  // Controlled_Buffer controlled_buffer_6
  assign controlled_buffer_1_out[6] = AO ? d_ff_7_q : 1'bz;  // Controlled_Buffer controlled_buffer_7
  assign controlled_buffer_1_out[7] = AO ? d_ff_8_q : 1'bz;  // Controlled_Buffer controlled_buffer_8
  assign controlled_buffer_1_out[0] = BO ? d_ff_9_q : 1'bz;  // Controlled_Buffer controlled_buffer_9
  assign controlled_buffer_1_out[1] = BO ? d_ff_10_q : 1'bz;  // Controlled_Buffer controlled_buffer_10
  assign controlled_buffer_1_out[2] = BO ? d_ff_11_q : 1'bz;  // Controlled_Buffer controlled_buffer_11
  assign controlled_buffer_1_out[3] = BO ? d_ff_12_q : 1'bz;  // Controlled_Buffer controlled_buffer_12
  assign controlled_buffer_1_out[4] = BO ? d_ff_13_q : 1'bz;  // Controlled_Buffer controlled_buffer_13
  assign controlled_buffer_1_out[5] = BO ? d_ff_14_q : 1'bz;  // Controlled_Buffer controlled_buffer_14
  assign controlled_buffer_1_out[6] = BO ? d_ff_15_q : 1'bz;  // Controlled_Buffer controlled_buffer_15
  assign controlled_buffer_1_out[7] = BO ? d_ff_16_q : 1'bz;  // Controlled_Buffer controlled_buffer_16
  or or_25 (or_25_out[0], and_50_out, and_51_out);
  or or_26 (or_25_out[1], and_52_out, and_53_out);
  or or_27 (or_25_out[2], and_54_out, and_55_out);
  or or_28 (or_25_out[3], and_56_out, and_57_out);
  or or_29 (or_25_out[4], and_58_out, and_59_out);
  or or_30 (or_25_out[5], and_60_out, and_61_out);
  or or_31 (or_25_out[6], and_62_out, and_63_out);
  or or_32 (or_25_out[7], and_64_out, and_65_out);
  Hex_Digit_Display hex_digit_display_1 ();  // open: value, dp
  Hex_Digit_Display hex_digit_display_2 ();  // open: value, dp
  LED led_7 (.in(controlled_buffer_1_out[2]));
  LED led_8 (.in(controlled_buffer_1_out[1]));
  LED led_9 (.in(controlled_buffer_1_out[0]));
  or or_33 (or_33_out, and_41_out, WE);
  assign controlled_buffer_1_out[5] = in_7 ? in_10 : 1'bz;  // Controlled_Buffer controlled_buffer_17
  assign controlled_buffer_1_out[7] = in_7 ? in_8 : 1'bz;  // Controlled_Buffer controlled_buffer_18
  assign controlled_buffer_1_out[6] = in_7 ? in_9 : 1'bz;  // Controlled_Buffer controlled_buffer_19
  assign controlled_buffer_1_out[0] = EO ? adder_1_out : 1'bz;  // Controlled_Buffer controlled_buffer_20
  assign controlled_buffer_1_out[1] = EO ? adder_2_out : 1'bz;  // Controlled_Buffer controlled_buffer_21
  assign controlled_buffer_1_out[2] = EO ? adder_3_out : 1'bz;  // Controlled_Buffer controlled_buffer_22
  assign controlled_buffer_1_out[3] = EO ? adder_4_out : 1'bz;  // Controlled_Buffer controlled_buffer_23
  assign controlled_buffer_1_out[4] = EO ? adder_5_out : 1'bz;  // Controlled_Buffer controlled_buffer_24
  assign controlled_buffer_1_out[5] = EO ? adder_6_out : 1'bz;  // Controlled_Buffer controlled_buffer_25
  assign controlled_buffer_1_out[6] = EO ? adder_7_out : 1'bz;  // Controlled_Buffer controlled_buffer_26
  assign controlled_buffer_1_out[7] = EO ? adder_8_out : 1'bz;  // Controlled_Buffer controlled_buffer_27
  or or_34 (or_34_out, and_41_out, clock_1_out);
  _7_Segment_Display u_7_segment_display_1 ();  // open: g, f, a, b, e, d, c, dp
  _7_Segment_Display u_7_segment_display_2 ();  // open: g, f, a, b, e, d, c, dp
  assign controlled_buffer_1_out[4] = in_7 ? in_11 : 1'bz;  // Controlled_Buffer controlled_buffer_28
  assign controlled_buffer_1_out[2] = in_7 ? in_13 : 1'bz;  // Controlled_Buffer controlled_buffer_29
  assign controlled_buffer_1_out[3] = in_7 ? in_12 : 1'bz;  // Controlled_Buffer controlled_buffer_30
  assign controlled_buffer_1_out[1] = in_7 ? in_14 : 1'bz;  // Controlled_Buffer controlled_buffer_31
  RAM #(.addrWidth(4), .bus("separate")) ram_1 (
    .addr(or_21_out), .din(or_25_out), .data(controlled_buffer_1_out), .str(or_33_out), .clk(or_34_out),
    .ld(OE), .clr(CLR));  // open: sel
  _7_Segment_Display u_7_segment_display_3 ();  // open: g, f, a, b, e, d, c, dp
  _7_Segment_Display u_7_segment_display_4 ();  // open: g, f, a, b, e, d, c, dp
  assign controlled_buffer_1_out[0] = in_7 ? in_15 : 1'bz;  // Controlled_Buffer controlled_buffer_32
  Pull_Resistor pull_resistor_1 (.node(controlled_buffer_1_out[0]));
  Pull_Resistor pull_resistor_2 (.node(controlled_buffer_1_out[1]));
  Pull_Resistor pull_resistor_3 (.node(controlled_buffer_1_out[2]));
  Pull_Resistor pull_resistor_4 (.node(controlled_buffer_1_out[3]));
  Pull_Resistor pull_resistor_5 (.node(controlled_buffer_1_out[4]));
  Pull_Resistor pull_resistor_6 (.node(controlled_buffer_1_out[5]));
  Pull_Resistor pull_resistor_7 (.node(controlled_buffer_1_out[6]));
  Pull_Resistor pull_resistor_8 (.node(controlled_buffer_1_out[7]));
  and and_66 (and_66_out, j_k_ff_1_q, undriven_4);
  and and_67 (and_67_out, undriven_3, or_36_out);
  and and_68 (and_68_out, undriven, undriven_2, undriven_3);
  and and_69 (and_69_out, undriven_4, j_k_ff_1_qn);
  or or_35 (or_35_out, and_66_out, and_67_out);
  J_K_Flip_Flop j_k_ff_1 (
    .J(or_35_out), .clk(undriven_5), .K(or_36_out), .Q(j_k_ff_1_q), .Qn(j_k_ff_1_qn));  // open: preset, en, reset
  or or_36 (or_36_out, and_68_out, and_69_out);
endmodule

module Bin____7segment_dec_decoder (
  input  [7:0] in_1,
  input  in_2,
  input  in_3
);

  wire and_1_out, and_2_out, and_3_out, and_4_out, not_1_out, not_2_out, not_3_out, not_4_out, not_5_out,
       not_6_out, not_7_out, not_8_out;
  wire [7:0] undriven;

  assign undriven[6] = and_4_out ? and_4_out : 1'bz;  // Controlled_Buffer controlled_buffer_1
  assign undriven[7] = and_4_out ? and_4_out : 1'bz;  // Controlled_Buffer controlled_buffer_2
  assign undriven[4] = and_4_out ? and_4_out : 1'bz;  // Controlled_Buffer controlled_buffer_3
  assign undriven[2] = and_4_out ? and_4_out : 1'bz;  // Controlled_Buffer controlled_buffer_4
  assign undriven[1] = and_4_out ? and_4_out : 1'bz;  // Controlled_Buffer controlled_buffer_5
  assign undriven[6] = and_3_out ? and_3_out : 1'bz;  // Controlled_Buffer controlled_buffer_6
  assign undriven[7] = and_3_out ? and_3_out : 1'bz;  // Controlled_Buffer controlled_buffer_7
  assign undriven[4] = and_3_out ? and_3_out : 1'bz;  // Controlled_Buffer controlled_buffer_8
  assign undriven[3] = and_3_out ? and_3_out : 1'bz;  // Controlled_Buffer controlled_buffer_9
  assign undriven[2] = and_3_out ? and_3_out : 1'bz;  // Controlled_Buffer controlled_buffer_10
  assign undriven[7] = and_2_out ? and_2_out : 1'bz;  // Controlled_Buffer controlled_buffer_11
  assign undriven[1] = and_2_out ? and_2_out : 1'bz;  // Controlled_Buffer controlled_buffer_12
  assign undriven[7] = and_1_out ? and_1_out : 1'bz;  // Controlled_Buffer controlled_buffer_13
  assign undriven[6] = and_1_out ? and_1_out : 1'bz;  // Controlled_Buffer controlled_buffer_14
  assign undriven[5] = and_1_out ? and_1_out : 1'bz;  // Controlled_Buffer controlled_buffer_15
  assign undriven[3] = and_1_out ? and_1_out : 1'bz;  // Controlled_Buffer controlled_buffer_16
  assign undriven[2] = and_1_out ? and_1_out : 1'bz;  // Controlled_Buffer controlled_buffer_17
  assign undriven[1] = and_1_out ? and_1_out : 1'bz;  // Controlled_Buffer controlled_buffer_18
  not not_1 (not_1_out, in_1[0]);
  not not_2 (not_2_out, in_1[1]);
  not not_3 (not_3_out, in_1[2]);
  not not_4 (not_4_out, in_1[3]);
  not not_5 (not_5_out, in_1[4]);
  not not_6 (not_6_out, in_1[5]);
  not not_7 (not_7_out, in_1[6]);
  not not_8 (not_8_out, in_1[7]);
  _7_Segment_Display u_7_segment_display_1 (
    .g(undriven[4]), .f(undriven[5]), .a(undriven[6]), .b(undriven[7]), .e(undriven[3]), .d(undriven[2]),
    .c(undriven[1]), .dp(undriven[0]));
  and and_1 (and_1_out, not_8_out, not_7_out, not_6_out, not_5_out, not_4_out, not_3_out, not_2_out, not_1_out);
  and and_2 (and_2_out, in_1[0], not_2_out, not_3_out, not_4_out, not_5_out, not_6_out, not_7_out, not_8_out);
  and and_3 (and_3_out, in_1[1], not_1_out, not_3_out, not_4_out, not_5_out, not_6_out, not_7_out, not_8_out);
  and and_4 (and_4_out, in_1[0], in_1[1], not_3_out, not_4_out, not_5_out, not_6_out, not_7_out, not_8_out);
  // AND_Gate and_5 has open pins: in0=in_1[2], in1=not_1_out, in2=not_2_out, in3=not_4_out, in4=not_5_out, in5=not_6_out, in6=not_7_out, in7=not_8_out, out=open
  // AND_Gate and_6 has open pins: in0=in_1[2], in1=in_1[0], in2=not_2_out, in3=not_4_out, in4=not_5_out, in5=not_6_out, in6=not_7_out, in7=not_8_out, out=open
  // AND_Gate and_7 has open pins: in0=in_1[2], in1=in_1[1], in2=not_1_out, in3=not_4_out, in4=not_5_out, in5=not_6_out, in6=not_7_out, in7=not_8_out, out=open
  // AND_Gate and_8 has open pins: in0=in_1[2], in1=in_1[1], in2=in_1[0], in3=not_4_out, in4=not_5_out, in5=not_6_out, in6=not_7_out, in7=not_8_out, out=open
  // AND_Gate and_9 has open pins: in0=in_1[3], in1=not_1_out, in2=not_2_out, in3=not_3_out, in4=not_5_out, in5=not_6_out, in6=not_7_out, in7=not_8_out, out=open
  // AND_Gate and_10 has open pins: in0=in_1[3], in1=in_1[0], in2=not_2_out, in3=not_3_out, in4=not_5_out, in5=not_6_out, in6=not_7_out, in7=not_8_out, out=open
  // AND_Gate and_11 has open pins: in0=in_1[3], in1=in_1[1], in2=not_1_out, in3=not_3_out, in4=not_5_out, in5=not_6_out, in6=not_7_out, in7=not_8_out, out=open
  // AND_Gate and_12 has open pins: in0=in_1[3], in1=in_1[1], in2=in_1[0], in3=not_3_out, in4=not_5_out, in5=not_6_out, in6=not_7_out, in7=not_8_out, out=open
  // AND_Gate and_13 has open pins: in0=in_1[3], in1=in_1[2], in2=not_1_out, in3=not_2_out, in4=not_5_out, in5=not_6_out, in6=not_7_out, in7=not_8_out, out=open
  // AND_Gate and_14 has open pins: in0=in_1[3], in1=in_1[2], in2=in_1[0], in3=not_2_out, in4=not_5_out, in5=not_6_out, in6=not_7_out, in7=not_8_out, out=open
  // AND_Gate and_15 has open pins: in0=in_1[3], in1=in_1[2], in2=in_1[1], in3=not_1_out, in4=not_5_out, in5=not_6_out, in6=not_7_out, in7=not_8_out, out=open
  // AND_Gate and_16 has open pins: in0=in_1[3], in1=in_1[2], in2=in_1[1], in3=in_1[0], in4=not_5_out, in5=not_6_out, in6=not_7_out, in7=not_8_out, out=open
  // AND_Gate and_17 has open pins: in0=in_1[4], in1=not_1_out, in2=not_2_out, in3=not_3_out, in4=not_4_out, in5=not_6_out, in6=not_7_out, in7=not_8_out, out=open
  // AND_Gate and_18 has open pins: in0=in_1[4], in1=in_1[0], in2=not_2_out, in3=not_3_out, in4=not_4_out, in5=not_6_out, in6=not_7_out, in7=not_8_out, out=open
  // AND_Gate and_19 has open pins: in0=in_1[4], in1=in_1[1], in2=not_1_out, in3=not_3_out, in4=not_4_out, in5=not_6_out, in6=not_7_out, in7=not_8_out, out=open
  // AND_Gate and_20 has open pins: in0=in_1[4], in1=in_1[1], in2=in_1[0], in3=not_3_out, in4=not_4_out, in5=not_6_out, in6=not_7_out, in7=not_8_out, out=open
  // AND_Gate and_21 has open pins: in0=in_1[4], in1=in_1[2], in2=not_1_out, in3=not_2_out, in4=not_4_out, in5=not_6_out, in6=not_7_out, in7=not_8_out, out=open
  // AND_Gate and_22 has open pins: in0=in_1[4], in1=in_1[2], in2=in_1[0], in3=not_2_out, in4=not_4_out, in5=not_6_out, in6=not_7_out, in7=not_8_out, out=open
  // AND_Gate and_23 has open pins: in0=in_1[4], in1=in_1[2], in2=in_1[1], in3=not_1_out, in4=not_4_out, in5=not_6_out, in6=not_7_out, in7=not_8_out, out=open
  // AND_Gate and_24 has open pins: in0=in_1[4], in1=in_1[2], in2=in_1[1], in3=in_1[0], in4=not_4_out, in5=not_6_out, in6=not_7_out, in7=not_8_out, out=open
  // AND_Gate and_25 has open pins: in0=in_1[4], in1=in_1[3], in2=not_1_out, in3=not_2_out, in4=not_3_out, in5=not_6_out, in6=not_7_out, in7=not_8_out, out=open
  // AND_Gate and_26 has open pins: in0=in_1[4], in1=in_1[3], in2=in_1[0], in3=not_2_out, in4=not_3_out, in5=not_6_out, in6=not_7_out, in7=not_8_out, out=open
  // AND_Gate and_27 has open pins: in0=in_1[4], in1=in_1[3], in2=in_1[1], in3=not_1_out, in4=not_3_out, in5=not_6_out, in6=not_7_out, in7=not_8_out, out=open
  // AND_Gate and_28 has open pins: in0=in_1[4], in1=in_1[3], in2=in_1[1], in3=in_1[0], in4=not_3_out, in5=not_6_out, in6=not_7_out, in7=not_8_out, out=open
  // AND_Gate and_29 has open pins: in0=in_1[4], in1=in_1[3], in2=in_1[2], in3=not_1_out, in4=not_2_out, in5=not_6_out, in6=not_7_out, in7=not_8_out, out=open
  // AND_Gate and_30 has open pins: in0=in_1[4], in1=in_1[3], in2=in_1[2], in3=in_1[0], in4=not_2_out, in5=not_6_out, in6=not_7_out, in7=not_8_out, out=open
  // AND_Gate and_31 has open pins: in0=in_1[4], in1=in_1[3], in2=in_1[2], in3=in_1[1], in4=not_1_out, in5=not_6_out, in6=not_7_out, in7=not_8_out, out=open
  // AND_Gate and_32 has open pins: in0=in_1[4], in1=in_1[3], in2=in_1[2], in3=in_1[1], in4=in_1[0], in5=not_6_out, in6=not_7_out, in7=not_8_out, out=open
  // AND_Gate and_33 has open pins: in0=in_1[5], in1=not_2_out, in2=not_3_out, in3=not_4_out, in4=not_5_out, in5=not_6_out, in6=not_7_out, in7=not_8_out, out=open
  // AND_Gate and_34 is placed but not wired
  // AND_Gate and_35 is placed but not wired
  // AND_Gate and_36 is placed but not wired
  // AND_Gate and_37 is placed but not wired
  // AND_Gate and_38 is placed but not wired
  // AND_Gate and_39 is placed but not wired
  // AND_Gate and_40 is placed but not wired
  // AND_Gate and_41 is placed but not wired
  // AND_Gate and_42 is placed but not wired
  // AND_Gate and_43 is placed but not wired
  // AND_Gate and_44 is placed but not wired
  // AND_Gate and_45 is placed but not wired
  // AND_Gate and_46 is placed but not wired
  // AND_Gate and_47 is placed but not wired
  // AND_Gate and_48 is placed but not wired
  // AND_Gate and_49 is placed but not wired
  // AND_Gate and_50 is placed but not wired
  // AND_Gate and_51 is placed but not wired
  // AND_Gate and_52 is placed but not wired
  // AND_Gate and_53 is placed but not wired
  // AND_Gate and_54 is placed but not wired
  // AND_Gate and_55 is placed but not wired
  // AND_Gate and_56 is placed but not wired
  // AND_Gate and_57 is placed but not wired
  // AND_Gate and_58 is placed but not wired
  // AND_Gate and_59 is placed but not wired
  // AND_Gate and_60 is placed but not wired
  // AND_Gate and_61 is placed but not wired
  // AND_Gate and_62 is placed but not wired
  // AND_Gate and_63 is placed but not wired
  // AND_Gate and_64 is placed but not wired
  // AND_Gate and_65 is placed but not wired
  // AND_Gate and_66 is placed but not wired
  // AND_Gate and_67 is placed but not wired
  // AND_Gate and_68 is placed but not wired
  // AND_Gate and_69 is placed but not wired
  // AND_Gate and_70 is placed but not wired
  // AND_Gate and_71 is placed but not wired
  // AND_Gate and_72 is placed but not wired
  // AND_Gate and_73 is placed but not wired
  // AND_Gate and_74 is placed but not wired
  // AND_Gate and_75 is placed but not wired
  // AND_Gate and_76 is placed but not wired
  // AND_Gate and_77 is placed but not wired
  // AND_Gate and_78 is placed but not wired
  // AND_Gate and_79 is placed but not wired
  // AND_Gate and_80 is placed but not wired
  // AND_Gate and_81 is placed but not wired
  // AND_Gate and_82 is placed but not wired
  // AND_Gate and_83 is placed but not wired
  // AND_Gate and_84 is placed but not wired
  // AND_Gate and_85 is placed but not wired
  // AND_Gate and_86 is placed but not wired
  // AND_Gate and_87 is placed but not wired
  // AND_Gate and_88 is placed but not wired
  // AND_Gate and_89 is placed but not wired
  // AND_Gate and_90 is placed but not wired
  // AND_Gate and_91 is placed but not wired
  // AND_Gate and_92 is placed but not wired
  // AND_Gate and_93 is placed but not wired
  // AND_Gate and_94 is placed but not wired
  // AND_Gate and_95 is placed but not wired
  // AND_Gate and_96 is placed but not wired
  // AND_Gate and_97 is placed but not wired
  // AND_Gate and_98 is placed but not wired
  // AND_Gate and_99 is placed but not wired
  // AND_Gate and_100: pin names not known; wires that end beside it: not_1_out, not_2_out
endmodule

module Counter (
  input  OE,
  input  LE,
  input  CE,
  input  in_4,
  input  in_5
);

  wire and_1_out, and_2_out, clock_1_out, or_1_out, or_2_out, t_ff_1_q, t_ff_2_q, xor_1_out, xor_2_out;

  Clock clock_1 (.out(clock_1_out));
  and and_1 (and_1_out, xor_1_out, LE);
  or or_1 (or_1_out, CE, and_1_out);
  xor xor_1 (xor_1_out, t_ff_1_q, in_4);
  T_Flip_Flop t_ff_1 (.clk(clock_1_out), .T(or_1_out), .Q(t_ff_1_q));  // open: Qn, preset, reset, en
  and and_2 (and_2_out, xor_2_out, LE);
  T_Flip_Flop t_ff_2 (.clk(clock_1_out), .T(or_2_out), .Q(t_ff_2_q));  // open: Qn, preset, reset, en
  or or_2 (or_2_out, t_ff_1_q, and_2_out);
  xor xor_2 (xor_2_out, t_ff_2_q, in_5);

  // Notes on the sheet:
  //   CLK
endmodule
